// Logisim project cpu24.circ as structural Verilog: 21 circuits, main circuit ◇单周期MIPS
module \单周期MIPS  (
  output RegWrite,
  output MemWrite,
  output [31:0] PC,
  output [31:0] IR,
  output [31:0] RDin,
  output [31:0] MDin,
  output [31:0] LedData
);

  wire AluSrcB, and_1_out, and_2_out, and_3_out, and_4_out, Beq, BLTZ, Bne, CLK, comparator_1_eq,
       comparator_2_eq, Equal, Go, halt, IR1, IR2, IR3, JAL, JMP, JR, LB, Less, MemToReg, mips_probe_1_p2,
       or_1_out, RegDst, SignedExt, Syscall, W1, W2, W3;
  wire [1:0] Addr1___0;
  wire [3:0] AluOP;
  wire [4:0] multiplexer_4_out, multiplexer_5_out, multiplexer_6_out, multiplexer_7_out;
  wire [7:0] multiplexer_11_out;
  wire [15:0] incrementer_1_p3, \总周期数 ;
  wire [27:0] PC_plus_4;
  wire [31:0] bit_extender_1_out, bit_extender_2_out, bit_extender_3_out, multiplexer_1_out,
       multiplexer_2_out, multiplexer_3_out, multiplexer_8_out, multiplexer_9_out, multiplexer_10_out,
       multiplexer_12_out, multiplexer_13_out, PCBranch, R1, ram_1_data, shifter_1_out;
  wire [31:2] mips_alu_1_result;
  wire [31:28] JumpAddr;

  Clock #(.highDuration(1), .lowDuration(1)) clock_1 (.out(CLK));
  Button _1 (.out(IR1));
  Button _2 (.out(IR2));
  Button _3 (.out(IR3));
  Button \u_继续运行  (.out(Go));
  LED #(.active("true")) led_1 (.in(W1));
  LED #(.active("true")) led_2 (.in(W2));
  LED #(.active("true")) led_3 (.in(W3));
  Hex_Digit_Display hex_digit_display_1 (.value(LedData[31:28]));  // open: dp
  Hex_Digit_Display hex_digit_display_2 (.value(LedData[23:20]));  // open: dp
  Hex_Digit_Display hex_digit_display_3 (.value(LedData[27:24]));  // open: dp
  Comparator #(.width(32), .mode("twosComplement")) comparator_1 (
    .a(R1), .b(32'h22), .eq(comparator_1_eq));  // open: gt, lt
  nand nand_1 (halt, ~comparator_1_eq, Syscall);  // NAND_Gate
  Multiplexer #(.select(1), .width(32), .disabled("Z"), .enable("false")) multiplexer_1 (
    .in0({JumpAddr, PC_plus_4}), .in1({JumpAddr, IR[25:0], 2'b00}), .out(multiplexer_1_out), .sel(JMP));
  and and_1 (and_1_out, Beq, Equal);
  and and_2 (and_2_out, BLTZ, Less);
  and and_3 (and_3_out, Bne, ~Equal);  // AND_Gate
  Hex_Digit_Display hex_digit_display_4 (.value(LedData[15:12]));  // open: dp
  Hex_Digit_Display hex_digit_display_5 (.value(LedData[19:16]));  // open: dp
  // Probe on halt
  Multiplexer #(.select(1), .width(32), .disabled("Z"), .enable("false")) multiplexer_2 (
    .in0(multiplexer_1_out), .in1(R1), .out(multiplexer_2_out), .sel(JR));
  Multiplexer #(.select(1), .width(32), .disabled("Z"), .enable("false")) multiplexer_3 (
    .in0(multiplexer_2_out), .in1(PCBranch), .out(multiplexer_3_out), .sel(or_1_out));
  or or_1 (or_1_out, and_1_out, and_2_out, and_3_out);
  Hex_Digit_Display hex_digit_display_6 (.value(LedData[7:4]));  // open: dp
  Hex_Digit_Display hex_digit_display_7 (.value(LedData[11:8]));  // open: dp
  // Probe on \总周期数 
  // Probe on multiplexer_3_out
  Register #(.width(32), .trigger("rising"), .Select("low")) u_PC (
    .D(multiplexer_3_out), .en(halt), .Q(PC), .clk(CLK));  // open: clr
  Hex_Digit_Display hex_digit_display_8 (.value(LedData[3:0]));  // open: dp
  ROM #(.addrWidth(10), .dataWidth(32), .Select("high")) rom_1 (.addr(PC[11:2]), .data(IR));
  Adder #(.width(32)) adder_1 (.a(PC), .b(32'h4), .out({JumpAddr, PC_plus_4}));  // open: cin, cout
  // Mips_Probe mips_probe_1: pin names not known; wires that end beside it: IR, mips_probe_1_p2, mips_probe_1_p2
  \单周期硬布线控制器  \u_单周期硬布线控制器_1  (
    .Func(IR[5:0]), .OP(IR[31:26]), .ALU_OP(AluOP), .MemToReg(MemToReg), .MemWrite(MemWrite),
    .ALU_SRC(AluSrcB), .RegWrite(RegWrite), .SysCALL(Syscall), .SignedExt(SignedExt), .RegDst(RegDst),
    .JR(JR), .JMP(JMP), .Beq(Beq), .JAL(JAL), .Bne(Bne), .LB(LB), .BLTZ(BLTZ));  // open: eret
  Multiplexer #(.select(1), .width(5), .disabled("Z"), .enable("false")) multiplexer_4 (
    .in0(IR[20:16]), .in1(IR[15:11]), .out(multiplexer_4_out), .sel(RegDst));
  Multiplexer #(.select(1), .width(5), .disabled("Z"), .enable("false")) multiplexer_5 (
    .in0(multiplexer_4_out), .in1({5{1'b1}}), .out(multiplexer_5_out), .sel(JAL));
  Multiplexer #(.select(1), .width(5), .disabled("Z"), .enable("false")) multiplexer_6 (
    .in0(IR[25:21]), .in1(5'b00010), .out(multiplexer_6_out), .sel(Syscall));
  Multiplexer #(.select(1), .width(5), .disabled("Z"), .enable("false")) multiplexer_7 (
    .in0(IR[20:16]), .in1(5'b00100), .out(multiplexer_7_out), .sel(Syscall));
  assign bit_extender_1_out = {{16{1'b0}}, IR[15:0]};  // Bit_Extender bit_extender_1
  assign bit_extender_2_out = {{16{IR[15]}}, IR[15:0]};  // Bit_Extender bit_extender_2
  Multiplexer #(.select(1), .width(32), .disabled("Z"), .enable("false")) multiplexer_8 (
    .in0(bit_extender_1_out), .in1(bit_extender_2_out), .out(multiplexer_8_out), .sel(SignedExt));
  MIPS_Regifile mips_regifile_1 (
    .Din(RDin), .Clk(CLK), .R1(R1), .R2(MDin), .WE(RegWrite), .W_num(multiplexer_5_out),
    .R1_num(multiplexer_6_out), .R2_num(multiplexer_7_out));
  // Probe on multiplexer_8_out
  Comparator #(.width(32), .mode("twosComplement")) comparator_2 (
    .a(R1), .b(32'h22), .eq(comparator_2_eq));  // open: gt, lt
  Multiplexer #(.select(1), .width(32), .disabled("Z"), .enable("false")) multiplexer_9 (
    .in0(MDin), .in1(multiplexer_8_out), .out(multiplexer_9_out), .sel(AluSrcB));
  Shifter #(.width(32), .shift("ll")) shifter_1 (.in(multiplexer_8_out), .\dist (5'b00010), .out(shifter_1_out));
  Multiplexer #(.select(1), .width(32), .disabled("Z"), .enable("false")) multiplexer_10 (
    .in0(LedData), .in1(MDin), .out(multiplexer_10_out), .sel(and_4_out));
  and and_4 (and_4_out, comparator_2_eq, Syscall);
  MIPS_ALU mips_alu_1 (
    .X(R1), .Y(multiplexer_9_out), .AluOP(AluOP), .Equal(Equal), .Result({mips_alu_1_result, Addr1___0}),
    .shamt(IR[10:6]), .Less(Less));  // open: Result_2
  Register #(.width(32), .trigger("rising"), .Select("low")) register_1 (
    .D(multiplexer_10_out), .Q(LedData), .clk(CLK));  // open: en, clr
  Adder #(.width(32)) adder_2 (.a(shifter_1_out), .b({JumpAddr, PC_plus_4}), .out(PCBranch));  // open: cin, cout
  RAM #(.addrWidth(10), .dataWidth(32), .bus("separate"), .Select("high")) ram_1 (
    .addr(mips_alu_1_result[11:2]), .din(MDin), .data(ram_1_data), .str(MemWrite), .clk(CLK), .ld(1'b1));  // open: sel, clr
  Multiplexer #(.select(2), .width(8), .disabled("Z"), .enable("false")) multiplexer_11 (
    .in0(ram_1_data[7:0]), .in1(ram_1_data[15:8]), .in2(ram_1_data[23:16]), .in3(ram_1_data[31:24]),
    .out(multiplexer_11_out), .sel(Addr1___0));
  assign bit_extender_3_out = {{24{multiplexer_11_out[7]}}, multiplexer_11_out};  // Bit_Extender bit_extender_3
  Multiplexer #(.select(1), .width(32), .disabled("Z"), .enable("false")) multiplexer_12 (
    .in0(ram_1_data), .in1(bit_extender_3_out), .out(multiplexer_12_out), .sel(LB));
  // Probe on R1
  // Probe on IR[10:6]
  // Probe on MDin
  Register #(.width(16), .trigger("rising"), .Select("low")) register_2 (
    .D(incrementer_1_p3), .en(halt), .Q(\总周期数 ), .clk(CLK));  // open: clr
  Multiplexer #(.select(1), .width(32), .disabled("Z"), .enable("false")) multiplexer_13 (
    .in0({mips_alu_1_result, Addr1___0}), .in1(multiplexer_12_out), .out(multiplexer_13_out), .sel(MemToReg));
  // Incrementer incrementer_1: pin names not known; wires that end beside it: multiplexer_12_out, \总周期数 , incrementer_1_p3
  Multiplexer #(.select(1), .width(32), .disabled("Z"), .enable("false")) multiplexer_14 (
    .in0(multiplexer_13_out), .in1({JumpAddr, PC_plus_4}), .out(RDin), .sel(JAL));

  // Other names for the same wires on the sheet: OP[5:0] = IR[31:26]; Func[5:0] = IR[5:0]; JumpAddr[27:2] = IR[25:0];
  //   shamt[4:0] = IR[10:6]; PC_plus_4[31:28] = JumpAddr

  // Notes on the sheet:
  //   中断源
  //   中断等待指示
  //   总复位信号应将除ROM以外所有存储组件全部清零
  //   控制停机
  //   数码管输出
  //   数码管输出应该用寄存器锁存，否则显示数据只能一闪而过
  //   指令存储器
  //   contents of rom_1 (hex, n*v repeats v):
  //   20090000 200b0010 34118483 20120404 118c00 129400 36318281 22520404 ad310000 2328820 21290004
  //   216bffff 1560fffb 200b0020 20090000 81310000 112020 20020022 c 21290001 216bffff 1560fff9 2002000a c
  //   JMP
  //   JR
  //   OP
  //   Func
  //   Syscall
  //   指令字
  //   Beq
  //   Bne
  //   MemToReg
  //   MemWrite
  //   AluOP
  //   AluSrcB
  //   RegWrite
  //   JAL
  //   RegDst
  //   LB
  //   BLTZ
  //   硬布线控制器
  //   Func
  //   rs
  //   rt
  //   rd
  //   为方便自动评测，需要输出PC，IR，寄存器文件写入端口RDin，内存写入端口MDin等信号
  //   OP
  //   数据通路
  //   数码管显示电路
  //   监视
endmodule

// 单周期硬布线控制器
module \单周期硬布线控制器  (
  input  [5:0] OP,
  input  [5:0] Func,
  output [3:0] ALU_OP,
  output MemToReg,
  output MemWrite,
  output ALU_SRC,
  output RegWrite,
  output SysCALL,
  output SignedExt,
  output RegDst,
  output Beq,
  output Bne,
  output JR,
  output JMP,
  output JAL,
  output LB,
  output BLTZ,
  output eret
);

  \运算控制器自动生成  \u_运算控制器自动生成_1  (
    .OP0(OP[0]), .OP1(OP[1]), .OP2(OP[2]), .OP3(OP[3]), .OP4(OP[4]), .OP5(OP[5]), .F0(Func[0]), .F1(Func[1]),
    .F2(Func[2]), .F3(Func[3]), .F4(Func[4]), .F5(Func[5]), .S0(ALU_OP[0]), .S1(ALU_OP[1]), .S2(ALU_OP[2]),
    .S3(ALU_OP[3]));
  \控制信号自动生成  \u_控制信号自动生成_1  (
    .OP0(OP[0]), .OP1(OP[1]), .OP2(OP[2]), .MemToReg(MemToReg), .OP3(OP[3]), .OP4(OP[4]), .OP5(OP[5]),
    .F0(Func[0]), .MemWrite(MemWrite), .F1(Func[1]), .F2(Func[2]), .F3(Func[3]), .eret(eret), .F4(Func[4]),
    .F5(Func[5]), .ALU_SRC(ALU_SRC), .RegWrite(RegWrite), .SysCALL(SysCALL), .SignedExt(SignedExt),
    .RegDst(RegDst), .BEQ(Beq), .BNE(Bne), .JR(JR), .JUMP(JMP), .JAL(JAL), .LB(LB), .BLTZ(BLTZ));

  // Other names for the same wires on the sheet: OP_CODE[5:0] = OP

  // Notes on the sheet:
  //   运算器控制器，根据指令生成运算器功能选择信号
  //   控制信号生成，产生数据通路需要的其他控制信号
endmodule

// 运算器控制器
module \运算控制器自动生成  (
  input  OP0,
  input  OP1,
  input  OP2,
  input  OP3,
  input  OP4,
  input  OP5,
  input  F0,
  input  F1,
  input  F2,
  input  F3,
  input  F4,
  input  F5,
  output S0,
  output S1,
  output S2,
  output S3
);

  wire and_1_out, and_2_out, and_3_out, and_4_out, and_5_out, and_6_out, and_7_out, and_8_out, and_9_out,
       and_10_out, and_11_out, and_12_out, and_13_out, and_14_out, and_15_out, and_16_out, and_17_out,
       and_18_out, and_19_out, and_20_out, and_21_out, and_22_out, and_23_out, and_24_out, and_25_out,
       and_26_out, and_27_out, and_28_out, and_29_out, and_30_out, and_31_out, and_32_out, and_33_out,
       and_34_out, and_35_out, and_36_out, and_37_out, and_38_out, and_39_out, and_40_out, and_41_out,
       and_42_out, and_43_out, and_44_out, not_1_out, not_2_out, not_3_out, not_4_out, not_5_out, not_6_out,
       not_7_out, not_8_out, not_9_out, not_10_out, not_11_out, not_12_out, not_13_out, not_14_out,
       not_15_out, not_16_out, not_17_out, not_18_out, not_19_out, not_20_out, not_21_out, not_22_out,
       not_23_out, not_24_out, not_25_out, not_26_out, not_27_out, not_28_out, not_29_out, not_30_out,
       not_31_out, not_32_out, not_33_out, not_34_out, not_35_out, not_36_out, not_37_out, not_38_out,
       not_39_out, not_40_out, not_41_out, not_42_out, not_43_out, not_44_out, not_45_out, not_46_out,
       not_47_out, not_48_out, not_49_out, not_50_out, not_51_out, not_52_out, not_53_out, not_54_out,
       not_55_out, not_56_out, not_57_out, not_58_out, not_59_out, not_60_out, not_61_out, not_62_out,
       not_63_out, not_64_out, not_65_out, not_66_out, not_67_out, not_68_out, not_69_out, not_70_out,
       not_71_out, not_72_out, not_73_out, not_74_out, not_75_out, not_76_out, not_77_out, not_78_out,
       not_79_out, not_80_out, not_81_out, not_82_out, not_83_out, not_84_out, not_85_out, not_86_out,
       not_87_out, not_88_out, not_89_out, not_90_out, not_91_out, not_92_out, not_93_out, not_94_out,
       not_95_out, not_96_out, not_97_out, not_98_out, not_99_out, not_100_out, not_101_out, not_102_out,
       not_103_out, not_104_out, not_105_out, not_106_out, not_107_out, not_108_out, not_109_out,
       not_110_out, not_111_out, not_112_out, not_113_out, not_114_out, not_115_out, not_116_out,
       not_117_out, not_118_out, not_119_out, not_120_out, not_121_out, not_122_out, not_123_out,
       not_124_out, not_125_out, not_126_out, not_127_out, not_128_out, not_129_out, not_130_out,
       not_131_out, not_132_out, not_133_out, not_134_out, not_135_out, not_136_out, not_137_out,
       not_138_out, not_139_out, not_140_out, not_141_out, not_142_out, not_143_out, not_144_out,
       not_145_out, not_146_out, not_147_out, not_148_out, not_149_out, not_150_out, not_151_out,
       not_152_out, not_153_out, not_154_out, not_155_out, not_156_out, not_157_out, not_158_out,
       not_159_out, not_160_out, not_161_out, not_162_out, not_163_out, not_164_out, not_165_out,
       not_166_out, not_167_out, not_168_out, not_169_out, not_170_out, not_171_out, not_172_out,
       not_173_out, not_174_out, not_175_out, not_176_out, not_177_out, not_178_out, not_179_out,
       not_180_out, not_181_out, not_182_out, not_183_out, not_184_out, not_185_out, not_186_out,
       not_187_out, not_188_out, not_189_out, not_190_out, not_191_out, not_192_out, not_193_out,
       not_194_out, not_195_out, not_196_out, not_197_out, not_198_out, not_199_out, not_200_out,
       not_201_out, not_202_out, not_203_out, not_204_out, not_205_out, not_206_out, not_207_out,
       not_208_out, not_209_out, not_210_out, not_211_out, not_212_out, not_213_out, not_214_out,
       not_215_out, not_216_out, not_217_out, not_218_out, not_219_out, not_220_out, not_221_out,
       not_222_out, not_223_out, not_224_out, not_225_out, not_226_out, not_227_out, not_228_out,
       not_229_out, not_230_out, not_231_out, not_232_out, not_233_out, not_234_out, not_235_out,
       not_236_out, not_237_out, not_238_out, not_239_out, not_240_out, not_241_out, not_242_out,
       not_243_out, not_244_out, not_245_out, not_246_out, not_247_out, not_248_out, not_249_out,
       not_250_out, not_251_out, not_252_out, not_253_out, not_254_out, not_255_out, not_256_out,
       not_257_out, not_258_out, not_259_out, not_260_out, not_261_out, not_262_out, not_263_out,
       not_264_out, not_265_out, not_266_out, not_267_out, not_268_out, not_269_out, not_270_out,
       not_271_out, not_272_out, not_273_out, not_274_out, not_275_out, not_276_out, not_277_out,
       not_278_out, not_279_out, not_280_out, not_281_out, not_282_out, not_283_out, not_284_out,
       not_285_out, not_286_out, not_287_out, not_288_out, not_289_out, not_290_out, not_291_out,
       not_292_out, not_293_out, not_294_out, not_295_out, not_296_out, not_297_out, not_298_out,
       not_299_out, not_300_out, not_301_out, not_302_out, not_303_out, not_304_out, not_305_out,
       not_306_out, not_307_out, not_308_out, not_309_out, not_310_out, not_311_out, not_312_out,
       not_313_out, not_314_out, not_315_out, not_316_out, not_317_out, not_318_out, not_319_out,
       not_320_out, not_321_out;

  not not_1 (not_1_out, OP5);
  not not_2 (not_2_out, OP4);
  not not_3 (not_3_out, OP3);
  not not_4 (not_4_out, OP2);
  not not_5 (not_5_out, OP1);
  not not_6 (not_6_out, OP0);
  not not_7 (not_7_out, F5);
  not not_8 (not_8_out, F4);
  not not_9 (not_9_out, F3);
  not not_10 (not_10_out, F2);
  not not_11 (not_11_out, OP5);
  not not_12 (not_12_out, OP4);
  not not_13 (not_13_out, OP3);
  not not_14 (not_14_out, OP2);
  not not_15 (not_15_out, OP1);
  not not_16 (not_16_out, OP0);
  not not_17 (not_17_out, F4);
  not not_18 (not_18_out, F3);
  not not_19 (not_19_out, F2);
  not not_20 (not_20_out, F1);
  not not_21 (not_21_out, F0);
  not not_22 (not_22_out, OP5);
  not not_23 (not_23_out, OP4);
  not not_24 (not_24_out, OP3);
  not not_25 (not_25_out, OP2);
  not not_26 (not_26_out, OP1);
  not not_27 (not_27_out, OP0);
  not not_28 (not_28_out, F4);
  not not_29 (not_29_out, F3);
  not not_30 (not_30_out, F2);
  not not_31 (not_31_out, F1);
  not not_32 (not_32_out, OP5);
  not not_33 (not_33_out, OP4);
  not not_34 (not_34_out, OP3);
  not not_35 (not_35_out, OP2);
  not not_36 (not_36_out, OP1);
  not not_37 (not_37_out, OP0);
  not not_38 (not_38_out, F4);
  not not_39 (not_39_out, F3);
  not not_40 (not_40_out, F1);
  not not_41 (not_41_out, F0);
  not not_42 (not_42_out, OP5);
  not not_43 (not_43_out, OP4);
  not not_44 (not_44_out, OP3);
  not not_45 (not_45_out, OP2);
  not not_46 (not_46_out, OP1);
  not not_47 (not_47_out, OP0);
  not not_48 (not_48_out, F4);
  not not_49 (not_49_out, F2);
  not not_50 (not_50_out, F0);
  not not_51 (not_51_out, OP5);
  not not_52 (not_52_out, OP4);
  not not_53 (not_53_out, OP2);
  not not_54 (not_54_out, OP1);
  not not_55 (not_55_out, OP0);
  not not_56 (not_56_out, OP5);
  not not_57 (not_57_out, OP4);
  not not_58 (not_58_out, OP1);
  not not_59 (not_59_out, OP0);
  not not_60 (not_60_out, OP5);
  not not_61 (not_61_out, OP4);
  not not_62 (not_62_out, OP2);
  not not_63 (not_63_out, OP1);
  not not_64 (not_64_out, OP5);
  not not_65 (not_65_out, OP4);
  not not_66 (not_66_out, OP2);
  not not_67 (not_67_out, OP0);
  not not_68 (not_68_out, OP4);
  not not_69 (not_69_out, OP3);
  not not_70 (not_70_out, OP2);
  not not_71 (not_71_out, OP4);
  not not_72 (not_72_out, OP2);
  not not_73 (not_73_out, OP5);
  not not_74 (not_74_out, OP4);
  not not_75 (not_75_out, OP3);
  not not_76 (not_76_out, OP2);
  not not_77 (not_77_out, OP1);
  not not_78 (not_78_out, OP0);
  not not_79 (not_79_out, F5);
  not not_80 (not_80_out, F4);
  not not_81 (not_81_out, F3);
  not not_82 (not_82_out, OP5);
  not not_83 (not_83_out, OP4);
  not not_84 (not_84_out, OP3);
  not not_85 (not_85_out, OP2);
  not not_86 (not_86_out, OP1);
  not not_87 (not_87_out, OP0);
  not not_88 (not_88_out, F4);
  not not_89 (not_89_out, F3);
  not not_90 (not_90_out, F0);
  not not_91 (not_91_out, OP4);
  not not_92 (not_92_out, OP3);
  not not_93 (not_93_out, OP2);
  not not_94 (not_94_out, OP1);
  not not_95 (not_95_out, OP0);
  not not_96 (not_96_out, OP5);
  not not_97 (not_97_out, OP4);
  not not_98 (not_98_out, OP3);
  not not_99 (not_99_out, OP2);
  not not_100 (not_100_out, OP1);
  not not_101 (not_101_out, OP0);
  not not_102 (not_102_out, F5);
  not not_103 (not_103_out, F4);
  not not_104 (not_104_out, F3);
  not not_105 (not_105_out, F2);
  not not_106 (not_106_out, F0);
  not not_107 (not_107_out, OP5);
  not not_108 (not_108_out, OP4);
  not not_109 (not_109_out, OP3);
  not not_110 (not_110_out, OP2);
  not not_111 (not_111_out, OP1);
  not not_112 (not_112_out, OP0);
  not not_113 (not_113_out, F4);
  not not_114 (not_114_out, F3);
  not not_115 (not_115_out, F2);
  not not_116 (not_116_out, F0);
  not not_117 (not_117_out, OP5);
  not not_118 (not_118_out, OP4);
  not not_119 (not_119_out, OP3);
  not not_120 (not_120_out, OP2);
  not not_121 (not_121_out, OP1);
  not not_122 (not_122_out, OP0);
  not not_123 (not_123_out, F4);
  not not_124 (not_124_out, F3);
  not not_125 (not_125_out, F1);
  not not_126 (not_126_out, F0);
  not not_127 (not_127_out, OP5);
  not not_128 (not_128_out, OP4);
  not not_129 (not_129_out, OP3);
  not not_130 (not_130_out, OP2);
  not not_131 (not_131_out, OP1);
  not not_132 (not_132_out, OP0);
  not not_133 (not_133_out, F4);
  not not_134 (not_134_out, F3);
  not not_135 (not_135_out, OP5);
  not not_136 (not_136_out, OP4);
  not not_137 (not_137_out, OP3);
  not not_138 (not_138_out, OP2);
  not not_139 (not_139_out, OP1);
  not not_140 (not_140_out, OP0);
  not not_141 (not_141_out, F4);
  not not_142 (not_142_out, F2);
  not not_143 (not_143_out, F0);
  not not_144 (not_144_out, OP5);
  not not_145 (not_145_out, OP4);
  not not_146 (not_146_out, OP3);
  not not_147 (not_147_out, OP2);
  not not_148 (not_148_out, OP1);
  not not_149 (not_149_out, OP0);
  not not_150 (not_150_out, F5);
  not not_151 (not_151_out, F4);
  not not_152 (not_152_out, F1);
  not not_153 (not_153_out, F0);
  not not_154 (not_154_out, OP5);
  not not_155 (not_155_out, OP4);
  not not_156 (not_156_out, OP1);
  not not_157 (not_157_out, OP0);
  not not_158 (not_158_out, OP5);
  not not_159 (not_159_out, OP4);
  not not_160 (not_160_out, OP2);
  not not_161 (not_161_out, OP0);
  not not_162 (not_162_out, OP5);
  not not_163 (not_163_out, OP4);
  not not_164 (not_164_out, OP3);
  not not_165 (not_165_out, OP2);
  not not_166 (not_166_out, OP1);
  not not_167 (not_167_out, OP0);
  not not_168 (not_168_out, F4);
  not not_169 (not_169_out, F3);
  not not_170 (not_170_out, F2);
  not not_171 (not_171_out, F1);
  not not_172 (not_172_out, F0);
  not not_173 (not_173_out, OP5);
  not not_174 (not_174_out, OP4);
  not not_175 (not_175_out, OP3);
  not not_176 (not_176_out, OP2);
  not not_177 (not_177_out, OP1);
  not not_178 (not_178_out, OP0);
  not not_179 (not_179_out, F4);
  not not_180 (not_180_out, F3);
  not not_181 (not_181_out, F2);
  not not_182 (not_182_out, F1);
  not not_183 (not_183_out, OP5);
  not not_184 (not_184_out, OP4);
  not not_185 (not_185_out, OP3);
  not not_186 (not_186_out, OP2);
  not not_187 (not_187_out, OP1);
  not not_188 (not_188_out, OP0);
  not not_189 (not_189_out, F4);
  not not_190 (not_190_out, F3);
  not not_191 (not_191_out, F2);
  not not_192 (not_192_out, F0);
  not not_193 (not_193_out, OP5);
  not not_194 (not_194_out, OP4);
  not not_195 (not_195_out, OP3);
  not not_196 (not_196_out, OP2);
  not not_197 (not_197_out, OP1);
  not not_198 (not_198_out, OP0);
  not not_199 (not_199_out, F4);
  not not_200 (not_200_out, F3);
  not not_201 (not_201_out, F1);
  not not_202 (not_202_out, F0);
  not not_203 (not_203_out, OP5);
  not not_204 (not_204_out, OP4);
  not not_205 (not_205_out, OP3);
  not not_206 (not_206_out, OP2);
  not not_207 (not_207_out, OP1);
  not not_208 (not_208_out, OP0);
  not not_209 (not_209_out, F4);
  not not_210 (not_210_out, F2);
  not not_211 (not_211_out, OP5);
  not not_212 (not_212_out, OP4);
  not not_213 (not_213_out, OP3);
  not not_214 (not_214_out, OP2);
  not not_215 (not_215_out, OP1);
  not not_216 (not_216_out, OP0);
  not not_217 (not_217_out, F5);
  not not_218 (not_218_out, F4);
  not not_219 (not_219_out, F1);
  not not_220 (not_220_out, F0);
  not not_221 (not_221_out, OP5);
  not not_222 (not_222_out, OP4);
  not not_223 (not_223_out, OP2);
  not not_224 (not_224_out, OP1);
  not not_225 (not_225_out, OP0);
  not not_226 (not_226_out, OP5);
  not not_227 (not_227_out, OP4);
  not not_228 (not_228_out, OP1);
  not not_229 (not_229_out, OP0);
  not not_230 (not_230_out, OP5);
  not not_231 (not_231_out, OP4);
  not not_232 (not_232_out, OP2);
  not not_233 (not_233_out, OP1);
  not not_234 (not_234_out, OP4);
  not not_235 (not_235_out, OP3);
  not not_236 (not_236_out, OP2);
  not not_237 (not_237_out, OP4);
  not not_238 (not_238_out, OP2);
  not not_239 (not_239_out, OP5);
  not not_240 (not_240_out, OP4);
  not not_241 (not_241_out, OP3);
  not not_242 (not_242_out, OP2);
  not not_243 (not_243_out, OP1);
  not not_244 (not_244_out, OP0);
  not not_245 (not_245_out, F5);
  not not_246 (not_246_out, F4);
  not not_247 (not_247_out, F3);
  not not_248 (not_248_out, OP4);
  not not_249 (not_249_out, OP3);
  not not_250 (not_250_out, OP2);
  not not_251 (not_251_out, OP1);
  not not_252 (not_252_out, OP0);
  not not_253 (not_253_out, OP5);
  not not_254 (not_254_out, OP4);
  not not_255 (not_255_out, OP3);
  not not_256 (not_256_out, OP2);
  not not_257 (not_257_out, OP1);
  not not_258 (not_258_out, OP0);
  not not_259 (not_259_out, F4);
  not not_260 (not_260_out, F3);
  not not_261 (not_261_out, F1);
  not not_262 (not_262_out, OP5);
  not not_263 (not_263_out, OP4);
  not not_264 (not_264_out, OP3);
  not not_265 (not_265_out, OP2);
  not not_266 (not_266_out, OP1);
  not not_267 (not_267_out, OP0);
  not not_268 (not_268_out, F4);
  not not_269 (not_269_out, F3);
  not not_270 (not_270_out, OP5);
  not not_271 (not_271_out, OP4);
  not not_272 (not_272_out, OP3);
  not not_273 (not_273_out, OP2);
  not not_274 (not_274_out, OP1);
  not not_275 (not_275_out, OP0);
  not not_276 (not_276_out, F4);
  not not_277 (not_277_out, F2);
  not not_278 (not_278_out, F0);
  not not_279 (not_279_out, OP5);
  not not_280 (not_280_out, OP4);
  not not_281 (not_281_out, OP3);
  not not_282 (not_282_out, OP2);
  not not_283 (not_283_out, OP1);
  not not_284 (not_284_out, OP0);
  not not_285 (not_285_out, F4);
  not not_286 (not_286_out, F2);
  not not_287 (not_287_out, OP5);
  not not_288 (not_288_out, OP4);
  not not_289 (not_289_out, OP3);
  not not_290 (not_290_out, OP2);
  not not_291 (not_291_out, OP1);
  not not_292 (not_292_out, OP0);
  not not_293 (not_293_out, F5);
  not not_294 (not_294_out, F4);
  not not_295 (not_295_out, F1);
  not not_296 (not_296_out, F0);
  not not_297 (not_297_out, OP5);
  not not_298 (not_298_out, OP4);
  not not_299 (not_299_out, OP2);
  not not_300 (not_300_out, OP0);
  not not_301 (not_301_out, OP5);
  not not_302 (not_302_out, OP4);
  not not_303 (not_303_out, OP1);
  not not_304 (not_304_out, OP5);
  not not_305 (not_305_out, OP4);
  not not_306 (not_306_out, OP3);
  not not_307 (not_307_out, OP2);
  not not_308 (not_308_out, OP1);
  not not_309 (not_309_out, OP0);
  not not_310 (not_310_out, F5);
  not not_311 (not_311_out, F4);
  not not_312 (not_312_out, F3);
  not not_313 (not_313_out, OP5);
  not not_314 (not_314_out, OP4);
  not not_315 (not_315_out, OP3);
  not not_316 (not_316_out, OP2);
  not not_317 (not_317_out, OP1);
  not not_318 (not_318_out, OP0);
  not not_319 (not_319_out, F4);
  not not_320 (not_320_out, F3);
  not not_321 (not_321_out, F0);
  and and_1 (and_1_out, not_1_out, not_2_out, not_3_out, not_4_out, not_5_out, not_6_out, not_7_out, not_8_out, not_9_out, not_10_out, F1, F0);
  and and_2 (and_2_out, not_11_out, not_12_out, not_13_out, not_14_out, not_15_out, not_16_out, F5, not_17_out, not_18_out, not_19_out, not_20_out, not_21_out);
  and and_3 (and_3_out, not_22_out, not_23_out, not_24_out, not_25_out, not_26_out, not_27_out, F5, not_28_out, not_29_out, not_30_out, not_31_out, F0);
  and and_4 (and_4_out, not_32_out, not_33_out, not_34_out, not_35_out, not_36_out, not_37_out, F5, not_38_out, not_39_out, F2, not_40_out, not_41_out);
  and and_5 (and_5_out, not_42_out, not_43_out, not_44_out, not_45_out, not_46_out, not_47_out, F5, not_48_out, F3, not_49_out, F1, not_50_out);
  and and_6 (and_6_out, not_51_out, not_52_out, OP3, not_53_out, not_54_out, not_55_out);
  and and_7 (and_7_out, not_56_out, not_57_out, OP3, OP2, not_58_out, not_59_out);
  and and_8 (and_8_out, not_60_out, not_61_out, OP3, not_62_out, not_63_out, OP0);
  and and_9 (and_9_out, not_64_out, not_65_out, OP3, not_66_out, OP1, not_67_out);
  and and_10 (and_10_out, OP5, not_68_out, not_69_out, not_70_out, OP1, OP0);
  and and_11 (and_11_out, OP5, not_71_out, OP3, not_72_out, OP1, OP0);
  and and_12 (and_12_out, not_73_out, not_74_out, not_75_out, not_76_out, not_77_out, not_78_out, not_79_out, not_80_out, not_81_out, F2, F1, F0);
  and and_13 (and_13_out, not_82_out, not_83_out, not_84_out, not_85_out, not_86_out, not_87_out, F5, not_88_out, not_89_out, F2, F1, not_90_out);
  and and_14 (and_14_out, OP5, not_91_out, not_92_out, not_93_out, not_94_out, not_95_out);
  and and_15 (and_15_out, not_96_out, not_97_out, not_98_out, not_99_out, not_100_out, not_101_out, not_102_out, not_103_out, not_104_out, not_105_out, F1, not_106_out);
  and and_16 (and_16_out, not_107_out, not_108_out, not_109_out, not_110_out, not_111_out, not_112_out, F5, not_113_out, not_114_out, not_115_out, F1, not_116_out);
  and and_17 (and_17_out, not_117_out, not_118_out, not_119_out, not_120_out, not_121_out, not_122_out, F5, not_123_out, not_124_out, F2, not_125_out, not_126_out);
  and and_18 (and_18_out, not_127_out, not_128_out, not_129_out, not_130_out, not_131_out, not_132_out, F5, not_133_out, not_134_out, F2, F1, F0);
  and and_19 (and_19_out, not_135_out, not_136_out, not_137_out, not_138_out, not_139_out, not_140_out, F5, not_141_out, F3, not_142_out, F1, not_143_out);
  and and_20 (and_20_out, not_144_out, not_145_out, not_146_out, not_147_out, not_148_out, not_149_out, not_150_out, not_151_out, F3, F2, not_152_out, not_153_out);
  and and_21 (and_21_out, not_154_out, not_155_out, OP3, OP2, not_156_out, not_157_out);
  and and_22 (and_22_out, not_158_out, not_159_out, OP3, not_160_out, OP1, not_161_out);
  and and_23 (and_23_out, not_162_out, not_163_out, not_164_out, not_165_out, not_166_out, not_167_out, F5, not_168_out, not_169_out, not_170_out, not_171_out, not_172_out);
  and and_24 (and_24_out, not_173_out, not_174_out, not_175_out, not_176_out, not_177_out, not_178_out, F5, not_179_out, not_180_out, not_181_out, not_182_out, F0);
  and and_25 (and_25_out, not_183_out, not_184_out, not_185_out, not_186_out, not_187_out, not_188_out, F5, not_189_out, not_190_out, not_191_out, F1, not_192_out);
  and and_26 (and_26_out, not_193_out, not_194_out, not_195_out, not_196_out, not_197_out, not_198_out, F5, not_199_out, not_200_out, F2, not_201_out, not_202_out);
  and and_27 (and_27_out, not_203_out, not_204_out, not_205_out, not_206_out, not_207_out, not_208_out, F5, not_209_out, F3, not_210_out, F1, F0);
  and and_28 (and_28_out, not_211_out, not_212_out, not_213_out, not_214_out, not_215_out, not_216_out, not_217_out, not_218_out, F3, F2, not_219_out, not_220_out);
  and and_29 (and_29_out, not_221_out, not_222_out, OP3, not_223_out, not_224_out, not_225_out);
  and and_30 (and_30_out, not_226_out, not_227_out, OP3, OP2, not_228_out, not_229_out);
  and and_31 (and_31_out, not_230_out, not_231_out, OP3, not_232_out, not_233_out, OP0);
  and and_32 (and_32_out, OP5, not_234_out, not_235_out, not_236_out, OP1, OP0);
  and and_33 (and_33_out, OP5, not_237_out, OP3, not_238_out, OP1, OP0);
  and and_34 (and_34_out, not_239_out, not_240_out, not_241_out, not_242_out, not_243_out, not_244_out, not_245_out, not_246_out, not_247_out, F2, F1, F0);
  and and_35 (and_35_out, OP5, not_248_out, not_249_out, not_250_out, not_251_out, not_252_out);
  and and_36 (and_36_out, not_253_out, not_254_out, not_255_out, not_256_out, not_257_out, not_258_out, F5, not_259_out, not_260_out, F2, not_261_out, F0);
  and and_37 (and_37_out, not_262_out, not_263_out, not_264_out, not_265_out, not_266_out, not_267_out, F5, not_268_out, not_269_out, F2, F1, F0);
  and and_38 (and_38_out, not_270_out, not_271_out, not_272_out, not_273_out, not_274_out, not_275_out, F5, not_276_out, F3, not_277_out, F1, not_278_out);
  and and_39 (and_39_out, not_279_out, not_280_out, not_281_out, not_282_out, not_283_out, not_284_out, F5, not_285_out, F3, not_286_out, F1, F0);
  and and_40 (and_40_out, not_287_out, not_288_out, not_289_out, not_290_out, not_291_out, not_292_out, not_293_out, not_294_out, F3, F2, not_295_out, not_296_out);
  and and_41 (and_41_out, not_297_out, not_298_out, OP3, not_299_out, OP1, not_300_out);
  and and_42 (and_42_out, not_301_out, not_302_out, OP3, OP2, not_303_out, OP0);
  and and_43 (and_43_out, not_304_out, not_305_out, not_306_out, not_307_out, not_308_out, not_309_out, not_310_out, not_311_out, not_312_out, F2, F1, F0);
  and and_44 (and_44_out, not_313_out, not_314_out, not_315_out, not_316_out, not_317_out, not_318_out, F5, not_319_out, not_320_out, F2, F1, not_321_out);
  or or_1 (S1, and_15_out, and_16_out, and_17_out, and_18_out, and_19_out, and_20_out, and_21_out, and_22_out);
  or or_2 (S3, and_36_out, and_37_out, and_38_out, and_39_out, and_40_out, and_41_out, and_42_out, and_43_out, and_44_out);
  or or_3 (S0, and_1_out, and_2_out, and_3_out, and_4_out, and_5_out, and_6_out, and_7_out, and_8_out, and_9_out, and_10_out, and_11_out, and_12_out, and_13_out, and_14_out);
  or or_4 (S2, and_23_out, and_24_out, and_25_out, and_26_out, and_27_out, and_28_out, and_29_out, and_30_out, and_31_out, and_32_out, and_33_out, and_34_out, and_35_out);
endmodule

// 控制信号生成
module \控制信号自动生成  (
  input  OP0,
  input  OP1,
  input  OP2,
  input  OP3,
  input  OP4,
  input  OP5,
  input  F0,
  input  F1,
  input  F2,
  input  F3,
  input  F4,
  input  F5,
  output MemToReg,
  output MemWrite,
  output eret,
  output ALU_SRC,
  output RegWrite,
  output SysCALL,
  output SignedExt,
  output RegDst,
  output BEQ,
  output BNE,
  output JR,
  output JUMP,
  output JAL,
  output LB,
  output BLTZ
);

  wire and_1_out, and_2_out, and_5_out, and_6_out, and_7_out, and_8_out, and_9_out, and_10_out, and_11_out,
       and_12_out, and_13_out, and_14_out, and_15_out, and_16_out, and_17_out, and_18_out, and_19_out,
       and_20_out, and_21_out, and_22_out, and_23_out, and_24_out, and_25_out, and_26_out, and_27_out,
       and_28_out, and_29_out, and_30_out, and_31_out, and_32_out, and_33_out, and_35_out, and_36_out,
       and_37_out, and_38_out, and_39_out, and_40_out, and_41_out, and_42_out, and_43_out, and_44_out,
       and_45_out, and_46_out, and_47_out, and_48_out, and_49_out, and_50_out, and_51_out, and_52_out,
       and_53_out, and_54_out, and_55_out, and_56_out, and_60_out, and_61_out, not_1_out, not_2_out,
       not_3_out, not_4_out, not_5_out, not_6_out, not_7_out, not_8_out, not_9_out, not_10_out, not_11_out,
       not_12_out, not_13_out, not_14_out, not_15_out, not_16_out, not_17_out, not_18_out, not_19_out,
       not_20_out, not_21_out, not_22_out, not_23_out, not_24_out, not_25_out, not_26_out, not_27_out,
       not_28_out, not_29_out, not_30_out, not_31_out, not_32_out, not_33_out, not_34_out, not_35_out,
       not_36_out, not_37_out, not_38_out, not_39_out, not_40_out, not_41_out, not_42_out, not_43_out,
       not_44_out, not_45_out, not_46_out, not_47_out, not_48_out, not_49_out, not_50_out, not_51_out,
       not_52_out, not_53_out, not_54_out, not_55_out, not_56_out, not_57_out, not_58_out, not_59_out,
       not_60_out, not_61_out, not_62_out, not_63_out, not_64_out, not_65_out, not_66_out, not_67_out,
       not_68_out, not_69_out, not_70_out, not_71_out, not_72_out, not_73_out, not_74_out, not_75_out,
       not_76_out, not_77_out, not_78_out, not_79_out, not_80_out, not_81_out, not_82_out, not_83_out,
       not_84_out, not_85_out, not_86_out, not_87_out, not_88_out, not_89_out, not_90_out, not_91_out,
       not_92_out, not_93_out, not_94_out, not_95_out, not_96_out, not_97_out, not_98_out, not_99_out,
       not_100_out, not_101_out, not_102_out, not_103_out, not_104_out, not_105_out, not_106_out,
       not_107_out, not_108_out, not_109_out, not_110_out, not_111_out, not_112_out, not_113_out,
       not_114_out, not_115_out, not_116_out, not_117_out, not_118_out, not_119_out, not_120_out,
       not_121_out, not_122_out, not_123_out, not_124_out, not_125_out, not_126_out, not_127_out,
       not_128_out, not_129_out, not_130_out, not_131_out, not_132_out, not_133_out, not_134_out,
       not_135_out, not_136_out, not_137_out, not_138_out, not_139_out, not_140_out, not_141_out,
       not_142_out, not_143_out, not_144_out, not_145_out, not_146_out, not_147_out, not_148_out,
       not_149_out, not_150_out, not_151_out, not_152_out, not_153_out, not_154_out, not_155_out,
       not_156_out, not_157_out, not_158_out, not_159_out, not_160_out, not_161_out, not_162_out,
       not_163_out, not_164_out, not_165_out, not_166_out, not_167_out, not_168_out, not_169_out,
       not_170_out, not_171_out, not_172_out, not_173_out, not_174_out, not_175_out, not_176_out,
       not_177_out, not_178_out, not_179_out, not_180_out, not_181_out, not_182_out, not_183_out,
       not_184_out, not_185_out, not_186_out, not_187_out, not_188_out, not_189_out, not_190_out,
       not_191_out, not_192_out, not_193_out, not_194_out, not_195_out, not_196_out, not_197_out,
       not_198_out, not_199_out, not_200_out, not_201_out, not_202_out, not_203_out, not_204_out,
       not_205_out, not_206_out, not_207_out, not_208_out, not_209_out, not_210_out, not_211_out,
       not_212_out, not_213_out, not_214_out, not_215_out, not_216_out, not_217_out, not_218_out,
       not_219_out, not_220_out, not_221_out, not_222_out, not_223_out, not_224_out, not_225_out,
       not_226_out, not_227_out, not_228_out, not_229_out, not_230_out, not_231_out, not_232_out,
       not_233_out, not_234_out, not_235_out, not_236_out, not_237_out, not_238_out, not_239_out,
       not_240_out, not_241_out, not_242_out, not_243_out, not_244_out, not_245_out, not_246_out,
       not_247_out, not_248_out, not_249_out, not_250_out, not_251_out, not_252_out, not_253_out,
       not_254_out, not_255_out, not_256_out, not_257_out, not_258_out, not_259_out, not_260_out,
       not_261_out, not_262_out, not_263_out, not_264_out, not_265_out, not_266_out, not_267_out,
       not_268_out, not_269_out, not_270_out, not_271_out, not_272_out, not_273_out, not_274_out,
       not_275_out, not_276_out, not_277_out, not_278_out, not_279_out, not_280_out, not_281_out,
       not_282_out, not_283_out, not_284_out, not_285_out, not_286_out, not_287_out, not_288_out,
       not_289_out, not_290_out, not_291_out, not_292_out, not_293_out, not_294_out, not_295_out,
       not_296_out, not_297_out, not_298_out, not_299_out, not_300_out, not_301_out, not_302_out,
       not_303_out, not_304_out, not_305_out, not_306_out, not_307_out, not_308_out, not_309_out,
       not_310_out, not_311_out, not_312_out, not_313_out, not_314_out, not_315_out, not_316_out,
       not_317_out, not_318_out, not_319_out, not_320_out, not_321_out, not_322_out, not_323_out,
       not_324_out, not_325_out, not_326_out, not_327_out, not_328_out, not_329_out, not_330_out,
       not_331_out, not_332_out, not_333_out, not_334_out, not_335_out, not_336_out, not_337_out,
       not_338_out, not_339_out, not_340_out, not_341_out, not_342_out, not_343_out, not_344_out,
       not_345_out, not_346_out, not_347_out, not_348_out, not_349_out, not_350_out, not_351_out,
       not_352_out, not_353_out, not_354_out, not_355_out, not_356_out, not_357_out, not_358_out,
       not_359_out, not_360_out, not_361_out, not_362_out, not_363_out, not_364_out, not_365_out,
       not_366_out, not_367_out, not_368_out, not_369_out, not_370_out, not_371_out, not_372_out,
       not_373_out, not_374_out, not_375_out, not_376_out, not_377_out, not_378_out, not_379_out,
       not_380_out, not_381_out, not_382_out, not_383_out, not_384_out, not_385_out, not_386_out,
       not_387_out, not_388_out, not_389_out, not_390_out, not_391_out, not_392_out, not_393_out,
       not_394_out, not_395_out, not_396_out, not_397_out, not_398_out, not_399_out, not_400_out,
       not_401_out, not_402_out, not_403_out, not_404_out, not_405_out, not_406_out, not_407_out,
       not_408_out, not_409_out, not_410_out, not_411_out, not_412_out, not_413_out, not_414_out,
       not_415_out, not_416_out, not_417_out, not_418_out, not_419_out, not_420_out, not_421_out,
       not_422_out, not_423_out;

  not not_1 (not_1_out, OP4);
  not not_2 (not_2_out, OP3);
  not not_3 (not_3_out, OP2);
  not not_4 (not_4_out, OP4);
  not not_5 (not_5_out, OP3);
  not not_6 (not_6_out, OP2);
  not not_7 (not_7_out, OP1);
  not not_8 (not_8_out, OP0);
  not not_9 (not_9_out, OP4);
  not not_10 (not_10_out, OP2);
  not not_11 (not_11_out, OP5);
  not not_12 (not_12_out, OP3);
  not not_13 (not_13_out, OP2);
  not not_14 (not_14_out, OP1);
  not not_15 (not_15_out, OP0);
  not not_16 (not_16_out, F5);
  not not_17 (not_17_out, F2);
  not not_18 (not_18_out, F1);
  not not_19 (not_19_out, F0);
  not not_20 (not_20_out, OP5);
  not not_21 (not_21_out, OP4);
  not not_22 (not_22_out, OP2);
  not not_23 (not_23_out, OP1);
  not not_24 (not_24_out, OP0);
  not not_25 (not_25_out, OP5);
  not not_26 (not_26_out, OP4);
  not not_27 (not_27_out, OP1);
  not not_28 (not_28_out, OP0);
  not not_29 (not_29_out, OP5);
  not not_30 (not_30_out, OP4);
  not not_31 (not_31_out, OP2);
  not not_32 (not_32_out, OP1);
  not not_33 (not_33_out, OP5);
  not not_34 (not_34_out, OP4);
  not not_35 (not_35_out, OP2);
  not not_36 (not_36_out, OP0);
  not not_37 (not_37_out, OP5);
  not not_38 (not_38_out, OP4);
  not not_39 (not_39_out, OP1);
  not not_40 (not_40_out, OP4);
  not not_41 (not_41_out, OP3);
  not not_42 (not_42_out, OP2);
  not not_43 (not_43_out, OP4);
  not not_44 (not_44_out, OP2);
  not not_45 (not_45_out, OP4);
  not not_46 (not_46_out, OP3);
  not not_47 (not_47_out, OP2);
  not not_48 (not_48_out, OP1);
  not not_49 (not_49_out, OP0);
  not not_50 (not_50_out, OP5);
  not not_51 (not_51_out, OP4);
  not not_52 (not_52_out, OP3);
  not not_53 (not_53_out, OP2);
  not not_54 (not_54_out, OP1);
  not not_55 (not_55_out, OP0);
  not not_56 (not_56_out, F5);
  not not_57 (not_57_out, F4);
  not not_58 (not_58_out, F3);
  not not_59 (not_59_out, F2);
  not not_60 (not_60_out, F1);
  not not_61 (not_61_out, F0);
  not not_62 (not_62_out, OP5);
  not not_63 (not_63_out, OP4);
  not not_64 (not_64_out, OP3);
  not not_65 (not_65_out, OP2);
  not not_66 (not_66_out, OP1);
  not not_67 (not_67_out, OP0);
  not not_68 (not_68_out, F5);
  not not_69 (not_69_out, F4);
  not not_70 (not_70_out, F3);
  not not_71 (not_71_out, F2);
  not not_72 (not_72_out, OP5);
  not not_73 (not_73_out, OP4);
  not not_74 (not_74_out, OP3);
  not not_75 (not_75_out, OP2);
  not not_76 (not_76_out, OP1);
  not not_77 (not_77_out, OP0);
  not not_78 (not_78_out, F5);
  not not_79 (not_79_out, F4);
  not not_80 (not_80_out, F3);
  not not_81 (not_81_out, F2);
  not not_82 (not_82_out, F0);
  not not_83 (not_83_out, OP5);
  not not_84 (not_84_out, OP4);
  not not_85 (not_85_out, OP3);
  not not_86 (not_86_out, OP2);
  not not_87 (not_87_out, OP1);
  not not_88 (not_88_out, OP0);
  not not_89 (not_89_out, F4);
  not not_90 (not_90_out, F3);
  not not_91 (not_91_out, F2);
  not not_92 (not_92_out, F1);
  not not_93 (not_93_out, F0);
  not not_94 (not_94_out, OP5);
  not not_95 (not_95_out, OP4);
  not not_96 (not_96_out, OP3);
  not not_97 (not_97_out, OP2);
  not not_98 (not_98_out, OP1);
  not not_99 (not_99_out, OP0);
  not not_100 (not_100_out, F4);
  not not_101 (not_101_out, F3);
  not not_102 (not_102_out, F2);
  not not_103 (not_103_out, F1);
  not not_104 (not_104_out, OP5);
  not not_105 (not_105_out, OP4);
  not not_106 (not_106_out, OP3);
  not not_107 (not_107_out, OP2);
  not not_108 (not_108_out, OP1);
  not not_109 (not_109_out, OP0);
  not not_110 (not_110_out, F4);
  not not_111 (not_111_out, F3);
  not not_112 (not_112_out, F2);
  not not_113 (not_113_out, F0);
  not not_114 (not_114_out, OP5);
  not not_115 (not_115_out, OP4);
  not not_116 (not_116_out, OP3);
  not not_117 (not_117_out, OP2);
  not not_118 (not_118_out, OP1);
  not not_119 (not_119_out, OP0);
  not not_120 (not_120_out, F4);
  not not_121 (not_121_out, F3);
  not not_122 (not_122_out, F1);
  not not_123 (not_123_out, F0);
  not not_124 (not_124_out, OP5);
  not not_125 (not_125_out, OP4);
  not not_126 (not_126_out, OP3);
  not not_127 (not_127_out, OP2);
  not not_128 (not_128_out, OP1);
  not not_129 (not_129_out, OP0);
  not not_130 (not_130_out, F4);
  not not_131 (not_131_out, F3);
  not not_132 (not_132_out, F1);
  not not_133 (not_133_out, OP5);
  not not_134 (not_134_out, OP4);
  not not_135 (not_135_out, OP3);
  not not_136 (not_136_out, OP2);
  not not_137 (not_137_out, OP1);
  not not_138 (not_138_out, OP0);
  not not_139 (not_139_out, F4);
  not not_140 (not_140_out, F3);
  not not_141 (not_141_out, OP5);
  not not_142 (not_142_out, OP4);
  not not_143 (not_143_out, OP3);
  not not_144 (not_144_out, OP2);
  not not_145 (not_145_out, OP1);
  not not_146 (not_146_out, OP0);
  not not_147 (not_147_out, F4);
  not not_148 (not_148_out, F2);
  not not_149 (not_149_out, F0);
  not not_150 (not_150_out, OP5);
  not not_151 (not_151_out, OP4);
  not not_152 (not_152_out, OP3);
  not not_153 (not_153_out, OP2);
  not not_154 (not_154_out, OP1);
  not not_155 (not_155_out, OP0);
  not not_156 (not_156_out, F4);
  not not_157 (not_157_out, F2);
  not not_158 (not_158_out, OP5);
  not not_159 (not_159_out, OP4);
  not not_160 (not_160_out, OP3);
  not not_161 (not_161_out, OP2);
  not not_162 (not_162_out, OP5);
  not not_163 (not_163_out, OP4);
  not not_164 (not_164_out, OP2);
  not not_165 (not_165_out, OP1);
  not not_166 (not_166_out, OP0);
  not not_167 (not_167_out, OP5);
  not not_168 (not_168_out, OP4);
  not not_169 (not_169_out, OP1);
  not not_170 (not_170_out, OP0);
  not not_171 (not_171_out, OP5);
  not not_172 (not_172_out, OP4);
  not not_173 (not_173_out, OP2);
  not not_174 (not_174_out, OP1);
  not not_175 (not_175_out, OP5);
  not not_176 (not_176_out, OP4);
  not not_177 (not_177_out, OP2);
  not not_178 (not_178_out, OP0);
  not not_179 (not_179_out, OP5);
  not not_180 (not_180_out, OP4);
  not not_181 (not_181_out, OP1);
  not not_182 (not_182_out, OP4);
  not not_183 (not_183_out, OP3);
  not not_184 (not_184_out, OP2);
  not not_185 (not_185_out, OP5);
  not not_186 (not_186_out, OP4);
  not not_187 (not_187_out, OP3);
  not not_188 (not_188_out, OP2);
  not not_189 (not_189_out, OP1);
  not not_190 (not_190_out, OP0);
  not not_191 (not_191_out, F5);
  not not_192 (not_192_out, F4);
  not not_193 (not_193_out, F3);
  not not_194 (not_194_out, OP5);
  not not_195 (not_195_out, OP4);
  not not_196 (not_196_out, OP3);
  not not_197 (not_197_out, OP2);
  not not_198 (not_198_out, OP1);
  not not_199 (not_199_out, OP0);
  not not_200 (not_200_out, F4);
  not not_201 (not_201_out, F3);
  not not_202 (not_202_out, F0);
  not not_203 (not_203_out, OP4);
  not not_204 (not_204_out, OP3);
  not not_205 (not_205_out, OP2);
  not not_206 (not_206_out, OP1);
  not not_207 (not_207_out, OP0);
  not not_208 (not_208_out, OP5);
  not not_209 (not_209_out, OP4);
  not not_210 (not_210_out, OP3);
  not not_211 (not_211_out, OP2);
  not not_212 (not_212_out, OP1);
  not not_213 (not_213_out, OP0);
  not not_214 (not_214_out, F5);
  not not_215 (not_215_out, F4);
  not not_216 (not_216_out, F1);
  not not_217 (not_217_out, F0);
  not not_218 (not_218_out, OP5);
  not not_219 (not_219_out, OP4);
  not not_220 (not_220_out, OP3);
  not not_221 (not_221_out, OP1);
  not not_222 (not_222_out, OP0);
  not not_223 (not_223_out, OP5);
  not not_224 (not_224_out, OP4);
  not not_225 (not_225_out, OP3);
  not not_226 (not_226_out, OP1);
  not not_227 (not_227_out, OP5);
  not not_228 (not_228_out, OP4);
  not not_229 (not_229_out, OP2);
  not not_230 (not_230_out, OP1);
  not not_231 (not_231_out, OP0);
  not not_232 (not_232_out, OP5);
  not not_233 (not_233_out, OP4);
  not not_234 (not_234_out, OP2);
  not not_235 (not_235_out, OP1);
  not not_236 (not_236_out, OP5);
  not not_237 (not_237_out, OP4);
  not not_238 (not_238_out, OP2);
  not not_239 (not_239_out, OP0);
  not not_240 (not_240_out, OP4);
  not not_241 (not_241_out, OP3);
  not not_242 (not_242_out, OP2);
  not not_243 (not_243_out, OP4);
  not not_244 (not_244_out, OP2);
  not not_245 (not_245_out, OP4);
  not not_246 (not_246_out, OP3);
  not not_247 (not_247_out, OP2);
  not not_248 (not_248_out, OP1);
  not not_249 (not_249_out, OP0);
  not not_250 (not_250_out, OP5);
  not not_251 (not_251_out, OP4);
  not not_252 (not_252_out, OP3);
  not not_253 (not_253_out, OP2);
  not not_254 (not_254_out, OP1);
  not not_255 (not_255_out, OP5);
  not not_256 (not_256_out, OP4);
  not not_257 (not_257_out, OP3);
  not not_258 (not_258_out, OP2);
  not not_259 (not_259_out, OP1);
  not not_260 (not_260_out, OP0);
  not not_261 (not_261_out, F5);
  not not_262 (not_262_out, F4);
  not not_263 (not_263_out, F3);
  not not_264 (not_264_out, F2);
  not not_265 (not_265_out, F1);
  not not_266 (not_266_out, F0);
  not not_267 (not_267_out, OP5);
  not not_268 (not_268_out, OP4);
  not not_269 (not_269_out, OP3);
  not not_270 (not_270_out, OP2);
  not not_271 (not_271_out, OP1);
  not not_272 (not_272_out, OP0);
  not not_273 (not_273_out, F5);
  not not_274 (not_274_out, F4);
  not not_275 (not_275_out, F3);
  not not_276 (not_276_out, F2);
  not not_277 (not_277_out, OP5);
  not not_278 (not_278_out, OP4);
  not not_279 (not_279_out, OP3);
  not not_280 (not_280_out, OP2);
  not not_281 (not_281_out, OP1);
  not not_282 (not_282_out, OP0);
  not not_283 (not_283_out, F5);
  not not_284 (not_284_out, F4);
  not not_285 (not_285_out, F3);
  not not_286 (not_286_out, F2);
  not not_287 (not_287_out, F0);
  not not_288 (not_288_out, OP5);
  not not_289 (not_289_out, OP4);
  not not_290 (not_290_out, OP3);
  not not_291 (not_291_out, OP2);
  not not_292 (not_292_out, OP1);
  not not_293 (not_293_out, OP0);
  not not_294 (not_294_out, F4);
  not not_295 (not_295_out, F3);
  not not_296 (not_296_out, F2);
  not not_297 (not_297_out, F1);
  not not_298 (not_298_out, F0);
  not not_299 (not_299_out, OP5);
  not not_300 (not_300_out, OP4);
  not not_301 (not_301_out, OP3);
  not not_302 (not_302_out, OP2);
  not not_303 (not_303_out, OP1);
  not not_304 (not_304_out, OP0);
  not not_305 (not_305_out, F4);
  not not_306 (not_306_out, F3);
  not not_307 (not_307_out, F2);
  not not_308 (not_308_out, F1);
  not not_309 (not_309_out, OP5);
  not not_310 (not_310_out, OP4);
  not not_311 (not_311_out, OP3);
  not not_312 (not_312_out, OP2);
  not not_313 (not_313_out, OP1);
  not not_314 (not_314_out, OP0);
  not not_315 (not_315_out, F4);
  not not_316 (not_316_out, F3);
  not not_317 (not_317_out, F2);
  not not_318 (not_318_out, F0);
  not not_319 (not_319_out, OP5);
  not not_320 (not_320_out, OP4);
  not not_321 (not_321_out, OP3);
  not not_322 (not_322_out, OP2);
  not not_323 (not_323_out, OP1);
  not not_324 (not_324_out, OP0);
  not not_325 (not_325_out, F4);
  not not_326 (not_326_out, F3);
  not not_327 (not_327_out, F1);
  not not_328 (not_328_out, F0);
  not not_329 (not_329_out, OP5);
  not not_330 (not_330_out, OP4);
  not not_331 (not_331_out, OP3);
  not not_332 (not_332_out, OP2);
  not not_333 (not_333_out, OP1);
  not not_334 (not_334_out, OP0);
  not not_335 (not_335_out, F4);
  not not_336 (not_336_out, F3);
  not not_337 (not_337_out, F1);
  not not_338 (not_338_out, OP5);
  not not_339 (not_339_out, OP4);
  not not_340 (not_340_out, OP3);
  not not_341 (not_341_out, OP2);
  not not_342 (not_342_out, OP1);
  not not_343 (not_343_out, OP0);
  not not_344 (not_344_out, F4);
  not not_345 (not_345_out, F3);
  not not_346 (not_346_out, OP5);
  not not_347 (not_347_out, OP4);
  not not_348 (not_348_out, OP3);
  not not_349 (not_349_out, OP2);
  not not_350 (not_350_out, OP1);
  not not_351 (not_351_out, OP0);
  not not_352 (not_352_out, F4);
  not not_353 (not_353_out, F2);
  not not_354 (not_354_out, F0);
  not not_355 (not_355_out, OP5);
  not not_356 (not_356_out, OP4);
  not not_357 (not_357_out, OP3);
  not not_358 (not_358_out, OP2);
  not not_359 (not_359_out, OP1);
  not not_360 (not_360_out, OP0);
  not not_361 (not_361_out, F4);
  not not_362 (not_362_out, F2);
  not not_363 (not_363_out, OP5);
  not not_364 (not_364_out, OP4);
  not not_365 (not_365_out, OP3);
  not not_366 (not_366_out, OP2);
  not not_367 (not_367_out, OP1);
  not not_368 (not_368_out, OP0);
  not not_369 (not_369_out, F5);
  not not_370 (not_370_out, F4);
  not not_371 (not_371_out, F3);
  not not_372 (not_372_out, OP5);
  not not_373 (not_373_out, OP4);
  not not_374 (not_374_out, OP3);
  not not_375 (not_375_out, OP2);
  not not_376 (not_376_out, OP1);
  not not_377 (not_377_out, OP0);
  not not_378 (not_378_out, F4);
  not not_379 (not_379_out, F3);
  not not_380 (not_380_out, F0);
  not not_381 (not_381_out, OP5);
  not not_382 (not_382_out, OP4);
  not not_383 (not_383_out, OP3);
  not not_384 (not_384_out, OP1);
  not not_385 (not_385_out, OP0);
  not not_386 (not_386_out, OP5);
  not not_387 (not_387_out, OP4);
  not not_388 (not_388_out, OP3);
  not not_389 (not_389_out, OP1);
  not not_390 (not_390_out, OP5);
  not not_391 (not_391_out, OP4);
  not not_392 (not_392_out, OP3);
  not not_393 (not_393_out, OP2);
  not not_394 (not_394_out, OP1);
  not not_395 (not_395_out, OP0);
  not not_396 (not_396_out, F5);
  not not_397 (not_397_out, F4);
  not not_398 (not_398_out, F2);
  not not_399 (not_399_out, F1);
  not not_400 (not_400_out, F0);
  not not_401 (not_401_out, OP5);
  not not_402 (not_402_out, OP4);
  not not_403 (not_403_out, OP3);
  not not_404 (not_404_out, OP2);
  not not_405 (not_405_out, OP0);
  not not_406 (not_406_out, OP5);
  not not_407 (not_407_out, OP4);
  not not_408 (not_408_out, OP3);
  not not_409 (not_409_out, OP2);
  not not_410 (not_410_out, OP5);
  not not_411 (not_411_out, OP4);
  not not_412 (not_412_out, OP3);
  not not_413 (not_413_out, OP2);
  not not_414 (not_414_out, OP4);
  not not_415 (not_415_out, OP3);
  not not_416 (not_416_out, OP2);
  not not_417 (not_417_out, OP1);
  not not_418 (not_418_out, OP0);
  not not_419 (not_419_out, OP5);
  not not_420 (not_420_out, OP4);
  not not_421 (not_421_out, OP3);
  not not_422 (not_422_out, OP2);
  not not_423 (not_423_out, OP1);
  and and_1 (and_1_out, OP5, not_1_out, not_2_out, not_3_out, OP1, OP0);
  and and_2 (and_2_out, OP5, not_4_out, not_5_out, not_6_out, not_7_out, not_8_out);
  and and_3 (MemWrite, OP5, not_9_out, OP3, not_10_out, OP1, OP0);
  and and_4 (eret, not_11_out, OP4, not_12_out, not_13_out, not_14_out, not_15_out, not_16_out, F4, F3, not_17_out, not_18_out, not_19_out);
  and and_5 (and_5_out, not_20_out, not_21_out, OP3, not_22_out, not_23_out, not_24_out);
  and and_6 (and_6_out, not_25_out, not_26_out, OP3, OP2, not_27_out, not_28_out);
  and and_7 (and_7_out, not_29_out, not_30_out, OP3, not_31_out, not_32_out, OP0);
  and and_8 (and_8_out, not_33_out, not_34_out, OP3, not_35_out, OP1, not_36_out);
  and and_9 (and_9_out, not_37_out, not_38_out, OP3, OP2, not_39_out, OP0);
  and and_10 (and_10_out, OP5, not_40_out, not_41_out, not_42_out, OP1, OP0);
  and and_11 (and_11_out, OP5, not_43_out, OP3, not_44_out, OP1, OP0);
  and and_12 (and_12_out, OP5, not_45_out, not_46_out, not_47_out, not_48_out, not_49_out);
  and and_13 (and_13_out, not_50_out, not_51_out, not_52_out, not_53_out, not_54_out, not_55_out, not_56_out, not_57_out, not_58_out, not_59_out, not_60_out, not_61_out);
  and and_14 (and_14_out, not_62_out, not_63_out, not_64_out, not_65_out, not_66_out, not_67_out, not_68_out, not_69_out, not_70_out, not_71_out, F1, F0);
  and and_15 (and_15_out, not_72_out, not_73_out, not_74_out, not_75_out, not_76_out, not_77_out, not_78_out, not_79_out, not_80_out, not_81_out, F1, not_82_out);
  and and_16 (and_16_out, not_83_out, not_84_out, not_85_out, not_86_out, not_87_out, not_88_out, F5, not_89_out, not_90_out, not_91_out, not_92_out, not_93_out);
  and and_17 (and_17_out, not_94_out, not_95_out, not_96_out, not_97_out, not_98_out, not_99_out, F5, not_100_out, not_101_out, not_102_out, not_103_out, F0);
  and and_18 (and_18_out, not_104_out, not_105_out, not_106_out, not_107_out, not_108_out, not_109_out, F5, not_110_out, not_111_out, not_112_out, F1, not_113_out);
  and and_19 (and_19_out, not_114_out, not_115_out, not_116_out, not_117_out, not_118_out, not_119_out, F5, not_120_out, not_121_out, F2, not_122_out, not_123_out);
  and and_20 (and_20_out, not_124_out, not_125_out, not_126_out, not_127_out, not_128_out, not_129_out, F5, not_130_out, not_131_out, F2, not_132_out, F0);
  and and_21 (and_21_out, not_133_out, not_134_out, not_135_out, not_136_out, not_137_out, not_138_out, F5, not_139_out, not_140_out, F2, F1, F0);
  and and_22 (and_22_out, not_141_out, not_142_out, not_143_out, not_144_out, not_145_out, not_146_out, F5, not_147_out, F3, not_148_out, F1, not_149_out);
  and and_23 (and_23_out, not_150_out, not_151_out, not_152_out, not_153_out, not_154_out, not_155_out, F5, not_156_out, F3, not_157_out, F1, F0);
  and and_24 (and_24_out, not_158_out, not_159_out, not_160_out, not_161_out, OP1, OP0);
  and and_25 (and_25_out, not_162_out, not_163_out, OP3, not_164_out, not_165_out, not_166_out);
  and and_26 (and_26_out, not_167_out, not_168_out, OP3, OP2, not_169_out, not_170_out);
  and and_27 (and_27_out, not_171_out, not_172_out, OP3, not_173_out, not_174_out, OP0);
  and and_28 (and_28_out, not_175_out, not_176_out, OP3, not_177_out, OP1, not_178_out);
  and and_29 (and_29_out, not_179_out, not_180_out, OP3, OP2, not_181_out, OP0);
  and and_30 (and_30_out, OP5, not_182_out, not_183_out, not_184_out, OP1, OP0);
  and and_31 (and_31_out, not_185_out, not_186_out, not_187_out, not_188_out, not_189_out, not_190_out, not_191_out, not_192_out, not_193_out, F2, F1, F0);
  and and_32 (and_32_out, not_194_out, not_195_out, not_196_out, not_197_out, not_198_out, not_199_out, F5, not_200_out, not_201_out, F2, F1, not_202_out);
  and and_33 (and_33_out, OP5, not_203_out, not_204_out, not_205_out, not_206_out, not_207_out);
  and and_34 (SysCALL, not_208_out, not_209_out, not_210_out, not_211_out, not_212_out, not_213_out, not_214_out, not_215_out, F3, F2, not_216_out, not_217_out);
  and and_35 (and_35_out, not_218_out, not_219_out, not_220_out, OP2, not_221_out, not_222_out);
  and and_36 (and_36_out, not_223_out, not_224_out, not_225_out, OP2, not_226_out, OP0);
  and and_37 (and_37_out, not_227_out, not_228_out, OP3, not_229_out, not_230_out, not_231_out);
  and and_38 (and_38_out, not_232_out, not_233_out, OP3, not_234_out, not_235_out, OP0);
  and and_39 (and_39_out, not_236_out, not_237_out, OP3, not_238_out, OP1, not_239_out);
  and and_40 (and_40_out, OP5, not_240_out, not_241_out, not_242_out, OP1, OP0);
  and and_41 (and_41_out, OP5, not_243_out, OP3, not_244_out, OP1, OP0);
  and and_42 (and_42_out, OP5, not_245_out, not_246_out, not_247_out, not_248_out, not_249_out);
  and and_43 (and_43_out, not_250_out, not_251_out, not_252_out, not_253_out, not_254_out, OP0);
  and and_44 (and_44_out, not_255_out, not_256_out, not_257_out, not_258_out, not_259_out, not_260_out, not_261_out, not_262_out, not_263_out, not_264_out, not_265_out, not_266_out);
  and and_45 (and_45_out, not_267_out, not_268_out, not_269_out, not_270_out, not_271_out, not_272_out, not_273_out, not_274_out, not_275_out, not_276_out, F1, F0);
  and and_46 (and_46_out, not_277_out, not_278_out, not_279_out, not_280_out, not_281_out, not_282_out, not_283_out, not_284_out, not_285_out, not_286_out, F1, not_287_out);
  and and_47 (and_47_out, not_288_out, not_289_out, not_290_out, not_291_out, not_292_out, not_293_out, F5, not_294_out, not_295_out, not_296_out, not_297_out, not_298_out);
  and and_48 (and_48_out, not_299_out, not_300_out, not_301_out, not_302_out, not_303_out, not_304_out, F5, not_305_out, not_306_out, not_307_out, not_308_out, F0);
  and and_49 (and_49_out, not_309_out, not_310_out, not_311_out, not_312_out, not_313_out, not_314_out, F5, not_315_out, not_316_out, not_317_out, F1, not_318_out);
  and and_50 (and_50_out, not_319_out, not_320_out, not_321_out, not_322_out, not_323_out, not_324_out, F5, not_325_out, not_326_out, F2, not_327_out, not_328_out);
  and and_51 (and_51_out, not_329_out, not_330_out, not_331_out, not_332_out, not_333_out, not_334_out, F5, not_335_out, not_336_out, F2, not_337_out, F0);
  and and_52 (and_52_out, not_338_out, not_339_out, not_340_out, not_341_out, not_342_out, not_343_out, F5, not_344_out, not_345_out, F2, F1, F0);
  and and_53 (and_53_out, not_346_out, not_347_out, not_348_out, not_349_out, not_350_out, not_351_out, F5, not_352_out, F3, not_353_out, F1, not_354_out);
  and and_54 (and_54_out, not_355_out, not_356_out, not_357_out, not_358_out, not_359_out, not_360_out, F5, not_361_out, F3, not_362_out, F1, F0);
  and and_55 (and_55_out, not_363_out, not_364_out, not_365_out, not_366_out, not_367_out, not_368_out, not_369_out, not_370_out, not_371_out, F2, F1, F0);
  and and_56 (and_56_out, not_372_out, not_373_out, not_374_out, not_375_out, not_376_out, not_377_out, F5, not_378_out, not_379_out, F2, F1, not_380_out);
  and and_57 (BEQ, not_381_out, not_382_out, not_383_out, OP2, not_384_out, not_385_out);
  and and_58 (BNE, not_386_out, not_387_out, not_388_out, OP2, not_389_out, OP0);
  and and_59 (JR, not_390_out, not_391_out, not_392_out, not_393_out, not_394_out, not_395_out, not_396_out, not_397_out, F3, not_398_out, not_399_out, not_400_out);
  and and_60 (and_60_out, not_401_out, not_402_out, not_403_out, not_404_out, OP1, not_405_out);
  and and_61 (and_61_out, not_406_out, not_407_out, not_408_out, not_409_out, OP1, OP0);
  and and_62 (JAL, not_410_out, not_411_out, not_412_out, not_413_out, OP1, OP0);
  and and_63 (LB, OP5, not_414_out, not_415_out, not_416_out, not_417_out, not_418_out);
  and and_64 (BLTZ, not_419_out, not_420_out, not_421_out, not_422_out, not_423_out, OP0);
  or or_1 (MemToReg, and_1_out, and_2_out);
  or or_2 (ALU_SRC, and_5_out, and_6_out, and_7_out, and_8_out, and_9_out, and_10_out, and_11_out, and_12_out);
  or or_3 (SignedExt, and_35_out, and_36_out, and_37_out, and_38_out, and_39_out, and_40_out, and_41_out, and_42_out, and_43_out);
  or or_4 (JUMP, and_60_out, and_61_out);
  or or_5 (RegWrite, and_13_out, and_14_out, and_15_out, and_16_out, and_17_out, and_18_out, and_19_out, and_20_out, and_21_out, and_22_out, and_23_out, and_24_out, and_25_out, and_26_out, and_27_out, and_28_out, and_29_out, and_30_out, and_31_out, and_32_out, and_33_out);
  or or_6 (RegDst, and_44_out, and_45_out, and_46_out, and_47_out, and_48_out, and_49_out, and_50_out, and_51_out, and_52_out, and_53_out, and_54_out, and_55_out, and_56_out);
endmodule

// ALU
module MIPS_ALU (
  input  [4:0] shamt,
  input  [31:0] X,
  input  [31:0] Y,
  input  [3:0] AluOP,
  output Less,
  output Equal,
  output [31:0] Result,
  output [31:0] Result_2
);

  wire comparator_4_eq;
  wire [0:0] comparator_1_lt, comparator_2_lt;
  wire [31:0] adder_1_out, AND_out, bit_extender_1_out, divider_1_out, divider_1_rem, multiplier_1_cout,
       multiplier_1_out, NOR_out, OR_out, shifter_1_out, shifter_2_out, shifter_3_out, shifter_4_out,
       subtractor_1_out, XOR_out;

  assign AND_out = X & Y;  // AND_Gate AND, 32 bits wide
  assign OR_out = X | Y;  // OR_Gate OR, 32 bits wide
  Shifter #(.width(32), .shift("ll")) shifter_1 (.in(Y), .\dist (shamt), .out(shifter_1_out));
  Shifter #(.width(32), .shift("ar")) shifter_2 (.in(Y), .\dist (shamt), .out(shifter_2_out));
  Shifter #(.width(32), .shift("lr")) shifter_3 (.in(Y), .\dist (shamt), .out(shifter_3_out));
  Multiplier #(.width(32)) multiplier_1 (.a(X), .b(Y), .out(multiplier_1_out), .cout(multiplier_1_cout));  // open: cin
  Divider #(.width(32)) divider_1 (.a(X), .b(Y), .out(divider_1_out), .rem(divider_1_rem));  // open: upper
  Adder #(.width(32)) adder_1 (.a(X), .b(Y), .out(adder_1_out));  // open: cin, cout
  Subtractor #(.width(32)) subtractor_1 (.a(X), .b(Y), .out(subtractor_1_out));  // open: bin, bout
  assign XOR_out = X ^ Y;  // XOR_Gate XOR, 32 bits wide
  assign NOR_out = ~(X | Y);  // NOR_Gate NOR, 32 bits wide
  Comparator #(.width(32), .mode("twosComplement")) comparator_1 (
    .a(X), .b(Y), .eq(Equal), .lt(comparator_1_lt[0]));  // open: gt
  Comparator #(.width(32), .mode("unsigned")) comparator_2 (.a(X), .b(Y), .lt(comparator_2_lt[0]));  // open: gt, eq
  Shifter #(.width(32), .shift("ar")) shifter_4 (.in(Y), .\dist (X[4:0]), .out(shifter_4_out));
  Comparator #(.width(32), .mode("twosComplement")) comparator_3 (.a(X), .b({32{1'b0}}), .lt(Less));  // open: gt, eq
  Comparator #(.width(32), .mode("twosComplement")) comparator_4 (
    .a(X), .b(32'h22), .eq(comparator_4_eq));  // open: gt, lt
  assign bit_extender_1_out = {{31{comparator_4_eq}}, comparator_4_eq};  // Bit_Extender bit_extender_1
  Multiplexer #(.select(4), .width(32), .disabled("Z"), .enable("false")) multiplexer_1 (
    .in0(shifter_1_out), .in1(shifter_2_out), .in2(shifter_3_out), .in3(multiplier_1_out),
    .in4(divider_1_out), .in5(adder_1_out), .in6(subtractor_1_out), .in7(AND_out), .in8(OR_out),
    .in9(XOR_out), .in10(NOR_out), .in11({{31{1'b0}}, comparator_1_lt[0]}),
    .in12({{31{1'b0}}, comparator_2_lt[0]}), .in13(shifter_4_out), .in14(bit_extender_1_out),
    .in15({32{1'b0}}), .out(Result), .sel(AluOP));
  Multiplexer #(.select(4), .width(32), .disabled("Z"), .enable("false")) multiplexer_2 (
    .in0({32{1'b0}}), .in1({32{1'b0}}), .in2({32{1'b0}}), .in3(multiplier_1_cout), .in4(divider_1_rem),
    .in5({32{1'b0}}), .in6({32{1'b0}}), .in7({32{1'b0}}), .in8({32{1'b0}}), .in9({32{1'b0}}),
    .in10({32{1'b0}}), .in11({32{1'b0}}), .in12({32{1'b0}}), .in13({32{1'b0}}), .in14({32{1'b0}}),
    .in15({32{1'b0}}), .out(Result_2), .sel(AluOP));

  // Other names for the same wires on the sheet: Result2[31:0] = Result_2; S[3:0] = AluOP

  // Notes on the sheet:
  //   不要改变此引脚区域内容，也不要改变ALU封装形式
  //   输入引脚
  //   输出引脚
endmodule

module MIPS_Regifile (
  input  [31:0] Din,
  input  Clk,
  input  WE,
  input  [4:0] R1_num,
  input  [4:0] W_num,
  input  [4:0] R2_num,
  output [31:0] R1,
  output [31:0] R2
);

  // RegisterFile registerfile_1: pin names not known; wires that end beside it: Din, Clk, WE, W_num, R1_num, R2_num, R1, R2
endmodule

module \理想流水线  (
  output RegWrite,
  output MemWrite,
  output [31:0] IF_PC,
  output [31:0] ID_PC,
  output [31:0] EX_PC,
  output [31:0] M_PC,
  output [31:0] WB_PC,
  output [31:0] RDin,
  output [31:0] MDin,
  output [31:0] LedData
);

  wire AluSrcB, AluSrcB_p2, and_1_out, and_2_out, and_3_out, and_4_out, Beq, BLTZ, Bne, CLK, comparator_1_eq,
       comparator_2_eq, d_ff_1_q, d_ff_2_q, d_ff_3_q, d_ff_4_q, d_ff_5_q, d_ff_7_q, d_ff_8_q, d_ff_8_qn,
       d_ff_9_q, d_ff_9_qn, d_ff_10_q, d_ff_10_qn, d_ff_11_q, d_ff_11_qn, d_ff_13_q, d_ff_13_qn, d_ff_14_qn,
       d_ff_15_qn, d_ff_16_qn, d_ff_17_qn, d_ff_18_qn, Equal, Go, halt, ID_MemWrite, ID_RegWrite, ID_Syscall,
       incrementer_1_p1, IR1, IR2, IR3, JAL, JAL_p4, JMP, JR, LB, LB_p4, Less, MemToReg, MemToReg_p4,
       or_1_out, RegDst, RST, SignedExt, Syscall, W1, W2, W3;
  wire [1:0] Addr1___0;
  wire [3:0] AluOP, AluOP_p2;
  wire [4:0] multiplexer_4_out, multiplexer_5_out, multiplexer_6_out, register_7_q, register_14_q, shamt_p2,
       W, W_p4;
  wire [5:0] Func, OP;
  wire [7:0] multiplexer_11_out;
  wire [15:0] incrementer_1_p3, \LoadUse次数 , \总周期数 , \插入气泡数 , \无条件分支数 , \条件分支成功数 ;
  wire [27:8] JumpAddr;
  wire [31:0] adder_2_out, adder_4_out, AluB, bit_extender_1_out, bit_extender_2_out, bit_extender_3_out,
       incrementer_1_p4, mips_alu_1_result, multiplexer_1_out, multiplexer_2_out, multiplexer_3_out,
       multiplexer_8_out, multiplexer_9_out, multiplexer_10_out, multiplexer_13_out, PC_plus_4, PCBranch, R1,
       R2, ram_1_data, register_3_q, register_5_q, register_15_q, register_16_q, rom_1_data, shifter_1_out;
  wire [31:2] register_11_q;

  Button \u_总复位  (.out(RST));
  Button _1 (.out(IR1));
  Button _2 (.out(IR2));
  Button _3 (.out(IR3));
  Button \u_继续运行  (.out(Go));
  LED #(.active("true")) led_1 (.in(W1));
  LED #(.active("true")) led_2 (.in(W2));
  LED #(.active("true")) led_3 (.in(W3));
  Multiplexer #(.select(1), .width(32), .disabled("Z"), .enable("false")) multiplexer_1 (
    .in0(PC_plus_4), .in1({ID_PC[31:28], JumpAddr, Func, 2'b00}), .out(multiplexer_1_out), .sel(JMP));
  Hex_Digit_Display hex_digit_display_1 (.value(LedData[31:28]));  // open: dp
  Multiplexer #(.select(1), .width(32), .disabled("Z"), .enable("false")) multiplexer_2 (
    .in0(multiplexer_1_out), .in1(R1), .out(multiplexer_2_out), .sel(JR));
  and and_1 (and_1_out, Beq, Equal);
  and and_2 (and_2_out, BLTZ, Less);
  and and_3 (and_3_out, Bne, ~Equal);  // AND_Gate
  Hex_Digit_Display hex_digit_display_2 (.value(LedData[27:24]));  // open: dp
  Hex_Digit_Display hex_digit_display_3 (.value(LedData[23:20]));  // open: dp
  Comparator #(.width(32), .mode("twosComplement")) comparator_1 (
    .a(R1), .b(32'h22), .eq(comparator_1_eq));  // open: gt, lt
  nand nand_1 (halt, ~comparator_1_eq, Syscall);  // NAND_Gate
  // Probe on multiplexer_3_out
  Multiplexer #(.select(1), .width(32), .disabled("Z"), .enable("false")) multiplexer_3 (
    .in0(multiplexer_2_out), .in1(PCBranch), .out(multiplexer_3_out), .sel(or_1_out));
  or or_1 (or_1_out, and_1_out, and_2_out, and_3_out);
  Hex_Digit_Display hex_digit_display_4 (.value(LedData[19:16]));  // open: dp
  Hex_Digit_Display hex_digit_display_5 (.value(LedData[15:12]));  // open: dp
  // Probe on halt
  Register #(.width(32), .trigger("rising"), .Select("low")) PC (
    .D(multiplexer_3_out), .en(halt), .Q(IF_PC), .clk(CLK));  // open: clr
  Hex_Digit_Display hex_digit_display_6 (.value(LedData[7:4]));  // open: dp
  Hex_Digit_Display hex_digit_display_7 (.value(LedData[11:8]));  // open: dp
  Clock #(.highDuration(1), .lowDuration(1)) clock_1 (.out(CLK));
  Adder #(.width(32)) adder_1 (.a(IF_PC), .b(32'h4), .out(PC_plus_4));  // open: cin, cout
  Hex_Digit_Display hex_digit_display_8 (.value(LedData[3:0]));  // open: dp
  ROM #(.addrWidth(10), .dataWidth(32), .Select("high")) rom_1 (.addr(IF_PC[11:2]), .data(rom_1_data));
  Register #(.width(32), .trigger("rising"), .Select("low")) register_1 (
    .D(rom_1_data), .Q({OP, JumpAddr, Func}), .clk(CLK));  // open: en, clr
  Register #(.width(32), .trigger("rising"), .Select("low")) register_2 (
    .D(IF_PC), .Q(ID_PC), .clk(CLK));  // open: en, clr
  // Probe on \总周期数 
  // Probe on \无条件分支数 
  // Probe on \条件分支成功数 
  // Probe on \插入气泡数 
  // Probe on \LoadUse次数 
  // Probe on IF_PC[11:0]
  \单周期硬布线控制器  \u_单周期硬布线控制器_1  (
    .Func(Func), .OP(OP), .ALU_OP(AluOP), .MemToReg(MemToReg), .MemWrite(ID_MemWrite), .ALU_SRC(AluSrcB),
    .RegWrite(ID_RegWrite), .SysCALL(ID_Syscall), .SignedExt(SignedExt), .RegDst(RegDst), .JR(JR), .JMP(JMP),
    .Beq(Beq), .JAL(JAL), .Bne(Bne), .LB(LB), .BLTZ(BLTZ));  // open: eret
  Multiplexer #(.select(1), .width(5), .disabled("Z"), .enable("false")) multiplexer_4 (
    .in0(JumpAddr[22:18]), .in1(JumpAddr[17:13]), .out(multiplexer_4_out), .sel(RegDst));
  // Probe on EX_PC[11:0]
  // Probe on ID_PC[11:0]
  Multiplexer #(.select(1), .width(5), .disabled("Z"), .enable("false")) multiplexer_5 (
    .in0(JumpAddr[27:23]), .in1(5'b00010), .out(multiplexer_5_out), .sel(Syscall));
  Multiplexer #(.select(1), .width(5), .disabled("Z"), .enable("false")) multiplexer_6 (
    .in0(JumpAddr[22:18]), .in1(5'b00100), .out(multiplexer_6_out), .sel(Syscall));
  Multiplexer #(.select(1), .width(5), .disabled("Z"), .enable("false")) multiplexer_7 (
    .in0(multiplexer_4_out), .in1({5{1'b1}}), .out(W), .sel(JAL));
  // Probe on M_PC[11:0]
  assign bit_extender_1_out = {{16{1'b0}}, {JumpAddr[17:8], Func}};  // Bit_Extender bit_extender_1
  assign bit_extender_2_out = {{16{JumpAddr[17]}}, {JumpAddr[17:8], Func}};  // Bit_Extender bit_extender_2
  // Probe on WB_PC[11:0]
  MIPS_Regifile mips_regifile_1 (
    .Din(RDin), .Clk(CLK), .R1(R1), .R2(R2), .WE(RegWrite), .W_num(W_p4), .R1_num(multiplexer_5_out),
    .R2_num(multiplexer_6_out));
  Multiplexer #(.select(1), .width(32), .disabled("Z"), .enable("false")) multiplexer_8 (
    .in0(bit_extender_1_out), .in1(bit_extender_2_out), .out(multiplexer_8_out), .sel(SignedExt));
  // Probe on multiplexer_8_out
  Register #(.width(32), .trigger("rising"), .Select("low")) register_3 (
    .D(R1), .Q(register_3_q), .clk(CLK));  // open: en, clr
  Register #(.width(32), .trigger("rising"), .Select("low")) register_4 (.D(R2), .Q(AluB), .clk(CLK));  // open: en, clr
  Register #(.width(32), .trigger("rising"), .Select("low")) register_5 (
    .D(multiplexer_8_out), .Q(register_5_q), .clk(CLK));  // open: en, clr
  Register #(.width(32), .trigger("rising"), .Select("low")) register_6 (
    .D(ID_PC), .Q(EX_PC), .clk(CLK));  // open: en, clr
  Register #(.width(5), .trigger("rising"), .Select("low")) register_7 (
    .D(W), .Q(register_7_q), .clk(CLK));  // open: en, clr
  D_Flip_Flop #(.trigger("rising"), .Pre_Clr_Positions("LEGACY"), .NegatePresetClear("false"), .enable("true"), .NewFFLayout("false")) d_ff_1 (
    .clk(CLK), .D(MemToReg), .Q(d_ff_1_q));  // open: Qn, preset, en, reset
  D_Flip_Flop #(.trigger("rising"), .Pre_Clr_Positions("LEGACY"), .NegatePresetClear("false"), .enable("true"), .NewFFLayout("false")) d_ff_2 (
    .clk(CLK), .D(JAL), .Q(d_ff_2_q));  // open: Qn, preset, en, reset
  D_Flip_Flop #(.trigger("rising"), .Pre_Clr_Positions("LEGACY"), .NegatePresetClear("false"), .enable("true"), .NewFFLayout("false")) d_ff_3 (
    .clk(CLK), .D(ID_RegWrite), .Q(d_ff_3_q));  // open: Qn, preset, en, reset
  D_Flip_Flop #(.trigger("rising"), .Pre_Clr_Positions("LEGACY"), .NegatePresetClear("false"), .enable("true"), .NewFFLayout("false")) d_ff_4 (
    .clk(CLK), .D(LB), .Q(d_ff_4_q));  // open: Qn, preset, en, reset
  D_Flip_Flop #(.trigger("rising"), .Pre_Clr_Positions("LEGACY"), .NegatePresetClear("false"), .enable("true"), .NewFFLayout("false")) d_ff_5 (
    .clk(CLK), .D(ID_MemWrite), .Q(d_ff_5_q));  // open: Qn, preset, en, reset
  Register #(.width(4), .trigger("rising"), .Select("low")) register_8 (
    .D(AluOP), .Q(AluOP_p2), .clk(CLK));  // open: en, clr
  D_Flip_Flop #(.trigger("rising"), .Pre_Clr_Positions("LEGACY"), .NegatePresetClear("false"), .enable("true"), .NewFFLayout("false")) d_ff_6 (
    .clk(CLK), .D(AluSrcB), .Q(AluSrcB_p2));  // open: Qn, preset, en, reset
  Register #(.width(5), .trigger("rising"), .Select("low")) register_9 (
    .D(JumpAddr[12:8]), .Q(shamt_p2), .clk(CLK));  // open: en, clr
  D_Flip_Flop #(.trigger("rising"), .Pre_Clr_Positions("LEGACY"), .NegatePresetClear("false"), .enable("true"), .NewFFLayout("false")) d_ff_7 (
    .clk(CLK), .D(ID_Syscall), .Q(d_ff_7_q));  // open: Qn, preset, en, reset
  Comparator #(.width(32), .mode("twosComplement")) comparator_2 (
    .a(R1), .b(32'h22), .eq(comparator_2_eq));  // open: gt, lt
  Multiplexer #(.select(1), .width(32), .disabled("Z"), .enable("false")) multiplexer_9 (
    .in0(AluB), .in1(register_5_q), .out(multiplexer_9_out), .sel(AluSrcB_p2));
  Shifter #(.width(32), .shift("ll")) shifter_1 (.in(register_5_q), .\dist (5'b00010), .out(shifter_1_out));
  Adder #(.width(32)) adder_2 (.a(32'h4), .b(EX_PC), .out(adder_2_out));  // open: cin, cout
  Multiplexer #(.select(1), .width(32), .disabled("Z"), .enable("false")) multiplexer_10 (
    .in0(LedData), .in1(R2), .out(multiplexer_10_out), .sel(and_4_out));
  and and_4 (and_4_out, comparator_2_eq, Syscall);
  MIPS_ALU mips_alu_1 (
    .X(register_3_q), .Y(multiplexer_9_out), .AluOP(AluOP_p2), .Equal(Equal), .Result(mips_alu_1_result),
    .shamt(shamt_p2), .Less(Less));  // open: Result_2
  Adder #(.width(32)) adder_3 (.a(shifter_1_out), .b(adder_2_out), .out(PCBranch));  // open: cin, cout
  Register #(.width(32), .trigger("rising"), .Select("low")) register_10 (
    .D(multiplexer_10_out), .Q(LedData), .clk(CLK));  // open: en, clr
  Register #(.width(32), .trigger("rising"), .Select("low")) register_11 (
    .D(mips_alu_1_result), .Q({register_11_q, Addr1___0}), .clk(CLK));  // open: en, clr
  Register #(.width(32), .trigger("rising"), .Select("low")) register_12 (
    .D(AluB), .Q(MDin), .clk(CLK));  // open: en, clr
  Register #(.width(32), .trigger("rising"), .Select("low")) register_13 (
    .D(EX_PC), .Q(M_PC), .clk(CLK));  // open: en, clr
  Register #(.width(5), .trigger("rising"), .Select("low")) register_14 (
    .D(register_7_q), .Q(register_14_q), .clk(CLK));  // open: en, clr
  D_Flip_Flop #(.trigger("rising"), .Pre_Clr_Positions("LEGACY"), .NegatePresetClear("false"), .enable("true"), .NewFFLayout("false")) d_ff_8 (
    .clk(CLK), .D(d_ff_1_q), .Q(d_ff_8_q), .Qn(d_ff_8_qn));  // open: preset, en, reset
  D_Flip_Flop #(.trigger("rising"), .Pre_Clr_Positions("LEGACY"), .NegatePresetClear("false"), .enable("true"), .NewFFLayout("false")) d_ff_9 (
    .clk(CLK), .D(d_ff_2_q), .Q(d_ff_9_q), .Qn(d_ff_9_qn));  // open: preset, en, reset
  D_Flip_Flop #(.trigger("rising"), .Pre_Clr_Positions("LEGACY"), .NegatePresetClear("false"), .enable("true"), .NewFFLayout("false")) d_ff_10 (
    .clk(CLK), .D(d_ff_3_q), .Q(d_ff_10_q), .Qn(d_ff_10_qn));  // open: preset, en, reset
  D_Flip_Flop #(.trigger("rising"), .Pre_Clr_Positions("LEGACY"), .NegatePresetClear("false"), .enable("true"), .NewFFLayout("false")) d_ff_11 (
    .clk(CLK), .D(d_ff_4_q), .Q(d_ff_11_q), .Qn(d_ff_11_qn));  // open: preset, en, reset
  D_Flip_Flop #(.trigger("rising"), .Pre_Clr_Positions("LEGACY"), .NegatePresetClear("false"), .enable("true"), .NewFFLayout("false")) d_ff_12 (
    .clk(CLK), .D(d_ff_5_q), .Q(MemWrite));  // open: Qn, preset, en, reset
  D_Flip_Flop #(.trigger("rising"), .Pre_Clr_Positions("LEGACY"), .NegatePresetClear("false"), .enable("true"), .NewFFLayout("false")) d_ff_13 (
    .clk(CLK), .D(d_ff_7_q), .Q(d_ff_13_q), .Qn(d_ff_13_qn));  // open: preset, en, reset
  RAM #(.addrWidth(10), .dataWidth(32), .bus("separate"), .Select("high")) ram_1 (
    .addr(register_11_q[11:2]), .din(MDin), .data(ram_1_data), .str(MemWrite), .clk(CLK), .ld(1'b1));  // open: sel, clr
  Register #(.width(32), .trigger("rising"), .Select("low")) register_15 (
    .D({register_11_q, Addr1___0}), .Q(register_15_q), .clk(CLK));  // open: en, clr
  Register #(.width(32), .trigger("rising"), .Select("low")) register_16 (
    .D(ram_1_data), .Q(register_16_q), .clk(CLK));  // open: en, clr
  Register #(.width(32), .trigger("rising"), .Select("low")) register_17 (
    .D(M_PC), .Q(WB_PC), .clk(CLK));  // open: en, clr
  Register #(.width(5), .trigger("rising"), .Select("low")) register_18 (
    .D(register_14_q), .Q(W_p4), .clk(CLK));  // open: en, clr
  D_Flip_Flop #(.trigger("rising"), .Pre_Clr_Positions("LEGACY"), .NegatePresetClear("false"), .enable("true"), .NewFFLayout("false")) d_ff_14 (
    .clk(CLK), .D(d_ff_8_q), .Q(MemToReg_p4), .Qn(d_ff_14_qn));  // open: preset, en, reset
  D_Flip_Flop #(.trigger("rising"), .Pre_Clr_Positions("LEGACY"), .NegatePresetClear("false"), .enable("true"), .NewFFLayout("false")) d_ff_15 (
    .clk(CLK), .D(d_ff_9_q), .Q(JAL_p4), .Qn(d_ff_15_qn));  // open: preset, en, reset
  D_Flip_Flop #(.trigger("rising"), .Pre_Clr_Positions("LEGACY"), .NegatePresetClear("false"), .enable("true"), .NewFFLayout("false")) d_ff_16 (
    .clk(CLK), .D(d_ff_10_q), .Q(RegWrite), .Qn(d_ff_16_qn));  // open: preset, en, reset
  D_Flip_Flop #(.trigger("rising"), .Pre_Clr_Positions("LEGACY"), .NegatePresetClear("false"), .enable("true"), .NewFFLayout("false")) d_ff_17 (
    .clk(CLK), .D(d_ff_11_q), .Q(LB_p4), .Qn(d_ff_17_qn));  // open: preset, en, reset
  D_Flip_Flop #(.trigger("rising"), .Pre_Clr_Positions("LEGACY"), .NegatePresetClear("false"), .enable("true"), .NewFFLayout("false")) d_ff_18 (
    .clk(CLK), .D(d_ff_13_q), .Q(Syscall), .Qn(d_ff_18_qn), .en(halt));  // open: preset, reset
  // Probe on R1
  // Probe on JumpAddr[12:8]
  // Probe on MDin
  Register #(.width(16), .trigger("rising"), .Select("low")) register_19 (
    .D(incrementer_1_p3), .en(halt), .Q(\总周期数 ), .clk(CLK));  // open: clr
  Multiplexer #(.select(2), .width(8), .disabled("Z"), .enable("false")) multiplexer_11 (
    .in0(register_16_q[7:0]), .in1(register_16_q[15:8]), .in2(register_16_q[23:16]),
    .in3(register_16_q[31:24]), .out(multiplexer_11_out), .sel(Addr1___0));
  // Incrementer incrementer_1: pin names not known; wires that end beside it: incrementer_1_p1, \总周期数 , incrementer_1_p3, incrementer_1_p4
  Multiplexer #(.select(1), .width(32), .disabled("Z"), .enable("false")) multiplexer_12 (
    .in0(register_16_q), .in1(bit_extender_3_out), .out(incrementer_1_p4), .sel(LB_p4));
  assign bit_extender_3_out = {{24{multiplexer_11_out[7]}}, multiplexer_11_out};  // Bit_Extender bit_extender_3
  Multiplexer #(.select(1), .width(32), .disabled("Z"), .enable("false")) multiplexer_13 (
    .in0(register_15_q), .in1(incrementer_1_p4), .out(multiplexer_13_out), .sel(MemToReg_p4));
  // Probe on multiplexer_13_out
  Adder #(.width(32)) adder_4 (.a(32'h4), .b(WB_PC), .out(adder_4_out));  // open: cin, cout
  Multiplexer #(.select(1), .width(32), .disabled("Z"), .enable("false")) multiplexer_14 (
    .in0(multiplexer_13_out), .in1(adder_4_out), .out(RDin), .sel(JAL_p4));

  // Other names for the same wires on the sheet: JumpAddr (some bits) = {ID_PC[31:28], Func};
  //   shamt[4:0] = JumpAddr[12:8]; MEM_PC[31:0] = M_PC

  // Notes on the sheet:
  //   中断源
  //   中断等待指示
  //   控制停机
  //   IF
  //   数码管输出
  //   指令存储器
  //   指令字
  //   contents of rom_1 (hex, n*v repeats v):
  //   20100000 20110000 20120000 20130000 36100000 36310001 36520002 36730003 ae100000 ae110004 ae120008
  //   ae13000c 2002000a 20110000 20120000 20130000 c
  //   JMP
  //   JR
  //   OP
  //   Func
  //   Syscall
  //   OP
  //   Func
  //   rs
  //   rt
  //   rd
  //   Beq
  //   Bne
  //   MemToReg
  //   MemWrite
  //   AluOP
  //   AluSrcB
  //   RegWrite
  //   JAL
  //   RegDst
  //   LB
  //   BLTZ
  //   硬布线控制器
  //   ID
  //   流水调试日志用
  //   EX
  //   数码管显示电路
  //   为方便自动评测，需要输出流水线各段保存的PC值，注意是PC不是PC+4，另外ID段寄存器写入信息，Mem段内存写入信息也要输出
  //   MEM
  //   监视
  //   WB
endmodule

module \气泡流水线  (
  output RegWrite,
  output MemWrite,
  output [31:0] IF_PC,
  output [31:0] ID_PC,
  output [31:0] EX_PC,
  output [31:0] M_PC,
  output [31:0] WB_PC,
  output [31:0] RDin,
  output [31:0] MDin,
  output [31:0] LedData
);

  wire AluSrcB, AluSrcB_p2, and_1_out, and_2_out, and_3_out, and_5_out, and_6_out, and_7_out, and_8_out,
       and_9_out, and_10_out, and_11_out, Beq, Beq_p2, BLTZ, BLTZ_p2, Bne, Bne_p2, CLK, d_ff_1_q, Equal,
       ex_mem_1_jal_p3, ex_mem_1_lb_p3, ex_mem_1_mem_syscall, ex_mem_1_memtoreg_p3, EX_nop, EX_RegWrite, Go,
       halt, halt1, halt2, id_ex_1_ex_syscall, id_ex_1_jal_p2, id_ex_1_lb_p2, id_ex_1_memtoreg_p2,
       id_ex_1_memwrite_p2, ID_JMP, ID_JR, ID_MemWrite, ID_RegWrite, IR1, IR2, IR3, JAL, JAL_p4, JMP, JR, LB,
       LB_p4, Less, MEM_nop, MEM_RegWrite, MemToReg, MemToReg_p4, multiplexer_15_out, nand_1_out, or_1_out,
       or_2_out, or_3_out, or_4_out, or_5_out, or_6_out, RegDst, RST, SignedExt, Syscall, W1, W2, W3,
       WB_Syscall;
  wire [1:0] Addr1___0;
  wire [3:0] AluOP, AluOP_p2;
  wire [4:0] EX_WriteReg_num, MEM_WriteReg_num, multiplexer_4_out, R1_num, R2_num, shamt_p2, W, W_p4;
  wire [5:0] Func, OP;
  wire [7:0] multiplexer_10_out;
  wire [15:0] incrementer_1_p2, incrementer_2_p2, incrementer_3_p2, incrementer_4_p2, incrementer_5_p2,
       \LoadUse次数 , multiplexer_16_out, multiplexer_17_out, multiplexer_18_out, multiplexer_19_out, \总周期数 ,
       \插入气泡数 , \无条件分支数 , \条件分支成功数 ;
  wire [27:8] ID_JumpAddr;
  wire [31:0] adder_2_out, adder_4_out, AluResult, bit_extender_1_out, bit_extender_2_out,
       bit_extender_3_out, EX_R1, EX_R2, id_ex_1_imm_p2, JumpAddr, mem_wb_1_p13, mips_alu_1_result,
       multiplexer_1_out, multiplexer_2_out, multiplexer_3_out, multiplexer_8_out, multiplexer_9_out,
       multiplexer_11_out, multiplexer_12_out, multiplexer_13_out, PC_plus_4, PCBranch, R1, R2, ram_1_data,
       rom_1_data, shifter_1_out, WB_R2;
  wire [31:2] ex_mem_1_aluresult_p3;

  Button \u_总复位  (.out(RST));
  Button _1 (.out(IR1));
  Button _2 (.out(IR2));
  Button _3 (.out(IR3));
  Button \u_继续运行  (.out(Go));
  LED #(.active("true")) led_1 (.in(W1));
  LED #(.active("true")) led_2 (.in(W2));
  LED #(.active("true")) led_3 (.in(W3));
  Multiplexer #(.select(1), .width(32), .disabled("Z"), .enable("false")) multiplexer_1 (
    .in0(PC_plus_4), .in1(JumpAddr), .out(multiplexer_1_out), .sel(JMP));
  Hex_Digit_Display hex_digit_display_1 (.value(LedData[31:28]));  // open: dp
  Multiplexer #(.select(1), .width(32), .disabled("Z"), .enable("false")) multiplexer_2 (
    .in0(multiplexer_1_out), .in1(EX_R1), .out(multiplexer_2_out), .sel(JR));
  and and_1 (and_1_out, Beq_p2, Equal);
  and and_2 (and_2_out, BLTZ_p2, Less);
  and and_3 (and_3_out, Bne_p2, ~Equal);  // AND_Gate
  Hex_Digit_Display hex_digit_display_2 (.value(LedData[23:20]));  // open: dp
  Hex_Digit_Display hex_digit_display_3 (.value(LedData[27:24]));  // open: dp
  and and_4 (halt, halt1, halt2);
  // Probe on multiplexer_3_out
  Multiplexer #(.select(1), .width(32), .disabled("Z"), .enable("false")) multiplexer_3 (
    .in0(multiplexer_2_out), .in1(PCBranch), .out(multiplexer_3_out), .sel(or_1_out));
  or or_1 (or_1_out, and_1_out, and_2_out, and_3_out);
  Hex_Digit_Display hex_digit_display_4 (.value(LedData[15:12]));  // open: dp
  Hex_Digit_Display hex_digit_display_5 (.value(LedData[19:16]));  // open: dp
  Register #(.width(32), .trigger("rising"), .Select("low")) PC (
    .D(multiplexer_3_out), .en(halt), .Q(IF_PC), .clk(CLK));  // open: clr
  Hex_Digit_Display hex_digit_display_6 (.value(LedData[7:4]));  // open: dp
  Hex_Digit_Display hex_digit_display_7 (.value(LedData[11:8]));  // open: dp
  Clock #(.highDuration(1), .lowDuration(1)) clock_1 (.out(CLK));
  Adder #(.width(32)) adder_1 (.a(IF_PC), .b(32'h4), .out(PC_plus_4));  // open: cin, cout
  Hex_Digit_Display hex_digit_display_8 (.value(LedData[3:0]));  // open: dp
  ROM #(.addrWidth(10), .dataWidth(32), .Select("high")) rom_1 (.addr(IF_PC[11:2]), .data(rom_1_data));
  IF___ID if_id_1 (
    .CLK(CLK), .JMP(JMP), .IF_PC(IF_PC), .IR(rom_1_data), .halt(halt), .JR(JR), .ID_PC(ID_PC),
    .IR_p1({OP, ID_JumpAddr, Func}), .in_3(Beq_p2), .in_7(Equal), .in_11(BLTZ_p2), .in_4(Less), .in_10(Bne_p2));
  // Probe on \总周期数 
  // Probe on \无条件分支数 
  // Probe on \条件分支成功数 
  // Probe on \插入气泡数 
  // Probe on \LoadUse次数 
  // Probe on IF_PC[11:0]
  \单周期硬布线控制器  \u_单周期硬布线控制器_1  (
    .Func(Func), .OP(OP), .ALU_OP(AluOP), .MemToReg(MemToReg), .MemWrite(ID_MemWrite), .ALU_SRC(AluSrcB),
    .RegWrite(ID_RegWrite), .SysCALL(Syscall), .SignedExt(SignedExt), .RegDst(RegDst), .JR(ID_JR),
    .JMP(ID_JMP), .Beq(Beq), .JAL(JAL), .Bne(Bne), .LB(LB), .BLTZ(BLTZ));  // open: eret
  Multiplexer #(.select(1), .width(5), .disabled("Z"), .enable("false")) multiplexer_4 (
    .in0(ID_JumpAddr[22:18]), .in1(ID_JumpAddr[17:13]), .out(multiplexer_4_out), .sel(RegDst));
  // Probe on ID_PC[11:0]
  // Probe on EX_PC[11:0]
  Multiplexer #(.select(1), .width(5), .disabled("Z"), .enable("false")) multiplexer_5 (
    .in0(ID_JumpAddr[27:23]), .in1(5'b00010), .out(R1_num), .sel(Syscall));
  Multiplexer #(.select(1), .width(5), .disabled("Z"), .enable("false")) multiplexer_6 (
    .in0(ID_JumpAddr[22:18]), .in1(5'b00100), .out(R2_num), .sel(Syscall));
  Multiplexer #(.select(1), .width(5), .disabled("Z"), .enable("false")) multiplexer_7 (
    .in0(multiplexer_4_out), .in1({5{1'b1}}), .out(W), .sel(JAL));
  // Probe on M_PC[11:0]
  assign bit_extender_1_out = {{16{1'b0}}, {ID_JumpAddr[17:8], Func}};  // Bit_Extender bit_extender_1
  assign bit_extender_2_out = {{16{ID_JumpAddr[17]}}, {ID_JumpAddr[17:8], Func}};  // Bit_Extender bit_extender_2
  // Probe on WB_PC[11:0]
  MIPS_Regifile mips_regifile_1 (
    .Din(RDin), .Clk(CLK), .R1(R1), .R2(R2), .WE(RegWrite), .W_num(W_p4), .R1_num(R1_num), .R2_num(R2_num));
  Multiplexer #(.select(1), .width(32), .disabled("Z"), .enable("false")) multiplexer_8 (
    .in0(bit_extender_1_out), .in1(bit_extender_2_out), .out(multiplexer_8_out), .sel(SignedExt));
  ID___EX id_ex_1 (
    .MemWrite(ID_MemWrite), .R1(R1), .AluOp(AluOP), .AluSrcB(AluSrcB), .R2(R2), .shamt(ID_JumpAddr[12:8]),
    .Beq(Beq), .imm(multiplexer_8_out), .BLTZ(BLTZ), .Bne(Bne), .ID_PC(ID_PC), .W(W), .MemTo_Reg(MemToReg),
    .CLK(CLK), .JAL(JAL), .ID_RegWrite(ID_RegWrite), .LB(LB), .R2_p2(EX_R2), .Beq_p2(Beq_p2),
    .imm_p2(id_ex_1_imm_p2), .EX_PC(EX_PC), .W_p2(EX_WriteReg_num), .BLTZ_p2(BLTZ_p2),
    .MemToReg_p2(id_ex_1_memtoreg_p2), .JAL_p2(id_ex_1_jal_p2), .EX_RegWrite(EX_RegWrite),
    .LB_p2(id_ex_1_lb_p2), .MemWrite_p2(id_ex_1_memwrite_p2), .AluOp_p2(AluOP_p2), .R1_p2(EX_R1),
    .AluSrcB_p2(AluSrcB_p2), .Bne_p2(Bne_p2), .shamt_p2(shamt_p2), .Equal(Equal), .Less(Less),
    .EX_nop(EX_nop), .MEM_nop(MEM_nop), .ID_JumpAddr({ID_PC[31:28], ID_JumpAddr, Func, 2'b00}),
    .JumpAddr(JumpAddr), .ID_JMP(ID_JMP), .ID_JR(ID_JR), .JMP(JMP), .JR(JR), .ID_Syscall(Syscall),
    .EX_Syscall(id_ex_1_ex_syscall));  // open: ID_R1_Forward, ID_R2_Forward, R1_Forward, R2_Forward, halt1
  Multiplexer #(.select(1), .width(32), .disabled("Z"), .enable("false")) multiplexer_9 (
    .in0(EX_R2), .in1(id_ex_1_imm_p2), .out(multiplexer_9_out), .sel(AluSrcB_p2));
  Shifter #(.width(32), .shift("ll")) shifter_1 (.in(id_ex_1_imm_p2), .\dist (5'b00010), .out(shifter_1_out));
  Adder #(.width(32)) adder_2 (.a(32'h4), .b(EX_PC), .out(adder_2_out));  // open: cin, cout
  MIPS_ALU mips_alu_1 (
    .X(EX_R1), .Y(multiplexer_9_out), .AluOP(AluOP_p2), .Equal(Equal), .Result(mips_alu_1_result),
    .shamt(shamt_p2), .Less(Less));  // open: Result_2
  Adder #(.width(32)) adder_3 (.a(shifter_1_out), .b(adder_2_out), .out(PCBranch));  // open: cin, cout
  EX___MEM ex_mem_1 (
    .MemWrite(id_ex_1_memwrite_p2), .ALUResult(mips_alu_1_result), .CLK(CLK), .MDin(EX_R2), .EX_PC(EX_PC),
    .W(EX_WriteReg_num), .MemTo_Reg(id_ex_1_memtoreg_p2), .JAL(id_ex_1_jal_p2), .EX_RegWrite(EX_RegWrite),
    .LB(id_ex_1_lb_p2), .JAL_p3(ex_mem_1_jal_p3), .MEM_RegWrite(MEM_RegWrite),
    .ALUResult_p3({ex_mem_1_aluresult_p3, Addr1___0}), .MDin_p3(MDin), .LB_p3(ex_mem_1_lb_p3), .MEM_PC(M_PC),
    .W_p3(MEM_WriteReg_num), .MemToReg_p3(ex_mem_1_memtoreg_p3), .MemWrite_p3(MemWrite),
    .EX_Syscall(id_ex_1_ex_syscall), .MEM_Syscall(ex_mem_1_mem_syscall));  // open: halt1
  RAM #(.addrWidth(10), .dataWidth(32), .bus("separate"), .Select("high")) ram_1 (
    .addr(ex_mem_1_aluresult_p3[11:2]), .din(MDin), .data(ram_1_data), .str(MemWrite), .clk(CLK), .ld(1'b1));  // open: sel, clr
  // MEM___WB mem_wb_1: pin names not known; wires that end beside it: {ex_mem_1_aluresult_p3, Addr1___0}, ram_1_data, M_PC, MEM_WriteReg_num, ex_mem_1_memtoreg_p3, ex_mem_1_jal_p3, MEM_RegWrite, ex_mem_1_lb_p3, MDin, ex_mem_1_mem_syscall, CLK, AluResult, mem_wb_1_p13, mem_wb_1_p13, WB_PC, W_p4, MemToReg_p4, JAL_p4, RegWrite, LB_p4, WB_R2, WB_Syscall
  Multiplexer #(.select(2), .width(8), .disabled("Z"), .enable("false")) multiplexer_10 (
    .in0(mem_wb_1_p13[7:0]), .in1(mem_wb_1_p13[15:8]), .in2(mem_wb_1_p13[23:16]), .in3(mem_wb_1_p13[31:24]),
    .out(multiplexer_10_out), .sel(Addr1___0));
  Multiplexer #(.select(1), .width(32), .disabled("Z"), .enable("false")) multiplexer_11 (
    .in0(mem_wb_1_p13), .in1(bit_extender_3_out), .out(multiplexer_11_out), .sel(LB_p4));
  assign bit_extender_3_out = {{24{multiplexer_10_out[7]}}, multiplexer_10_out};  // Bit_Extender bit_extender_3
  \数据相关检测逻辑  \u_数据相关检测逻辑  (
    .R1_num(R1_num), .EX_WriteReg_num(EX_WriteReg_num), .EX_RegWrite(EX_RegWrite), .R2_num(R2_num),
    .MEM_WriteReg_num(MEM_WriteReg_num), .MEM_RegWrite(MEM_RegWrite), .halt(halt2), .EX_nop(EX_nop),
    .MEM_nop(MEM_nop), .OP(OP), .Func(Func), .Syscall(Syscall));
  Multiplexer #(.select(1), .width(32), .disabled("Z"), .enable("false")) multiplexer_12 (
    .in0(AluResult), .in1(multiplexer_11_out), .out(multiplexer_12_out), .sel(MemToReg_p4));
  Adder #(.width(32)) adder_4 (.a(32'h4), .b(WB_PC), .out(adder_4_out));  // open: cin, cout
  Multiplexer #(.select(1), .width(32), .disabled("Z"), .enable("false")) multiplexer_13 (
    .in0(LedData), .in1(WB_R2), .out(multiplexer_13_out), .sel(and_5_out));
  and and_5 (and_5_out, AluResult[0], WB_Syscall);
  Multiplexer #(.select(1), .width(32), .disabled("Z"), .enable("false")) multiplexer_14 (
    .in0(multiplexer_12_out), .in1(adder_4_out), .out(RDin), .sel(JAL_p4));
  Register #(.width(32), .trigger("rising"), .Select("low")) register_1 (
    .D(multiplexer_13_out), .Q(LedData), .clk(CLK));  // open: en, clr
  nand nand_1 (nand_1_out, ~AluResult[0], WB_Syscall);  // NAND_Gate
  Multiplexer #(.select(1), .width(1), .disabled("Z"), .enable("false")) multiplexer_15 (
    .in0(1'b1), .in1(d_ff_1_q), .out(multiplexer_15_out), .sel(nand_1_out));
  D_Flip_Flop #(.trigger("rising"), .Pre_Clr_Positions("ABOVE_BELOW"), .NegatePresetClear("false"), .enable("false"), .NewFFLayout("false")) d_ff_1 (
    .clk(CLK), .D(multiplexer_15_out), .Q(d_ff_1_q));  // open: Qn, preset, reset
  not not_1 (halt1, d_ff_1_q);
  // Probe on R1
  // Probe on ID_JumpAddr[12:8]
  // Probe on MDin
  Register #(.width(16), .trigger("rising"), .Select("low")) register_2 (
    .D(incrementer_1_p2), .en(halt1), .Q(\总周期数 ), .clk(CLK));  // open: clr
  Register #(.width(16), .trigger("rising"), .Select("low")) register_3 (
    .D(multiplexer_16_out), .en(halt1), .Q(\无条件分支数 ), .clk(CLK));  // open: clr
  Register #(.width(16), .trigger("rising"), .Select("low")) register_4 (
    .D(multiplexer_17_out), .en(halt1), .Q(\条件分支成功数 ), .clk(CLK));  // open: clr
  and and_6 (and_6_out, Beq_p2, Equal);
  and and_7 (and_7_out, BLTZ_p2, Less);
  and and_8 (and_8_out, Bne_p2, ~Equal);  // AND_Gate
  // Incrementer incrementer_1: pin names not known; wires that end beside it: \总周期数 , incrementer_1_p2
  Multiplexer #(.select(1), .width(16), .disabled("Z"), .enable("false")) multiplexer_16 (
    .in0(\无条件分支数 ), .in1(incrementer_2_p2), .out(multiplexer_16_out), .sel(or_2_out));
  // Incrementer incrementer_2: pin names not known; wires that end beside it: \无条件分支数 , incrementer_2_p2
  or or_2 (or_2_out, JMP, JR);
  Multiplexer #(.select(1), .width(16), .disabled("Z"), .enable("false")) multiplexer_17 (
    .in0(\条件分支成功数 ), .in1(incrementer_3_p2), .out(multiplexer_17_out), .sel(or_3_out));
  // Incrementer incrementer_3: pin names not known; wires that end beside it: \条件分支成功数 , incrementer_3_p2
  or or_3 (or_3_out, and_6_out, and_7_out, and_8_out);
  Register #(.width(16), .trigger("rising"), .Select("low")) register_5 (
    .D(multiplexer_19_out), .en(halt1), .Q(\插入气泡数 ), .clk(CLK));  // open: clr
  Multiplexer #(.select(1), .width(16), .disabled("Z"), .enable("false")) multiplexer_18 (
    .in0(\插入气泡数 ), .in1(incrementer_4_p2), .out(multiplexer_18_out), .sel(or_4_out));
  // Incrementer incrementer_4: pin names not known; wires that end beside it: \插入气泡数 , incrementer_4_p2
  or or_4 (or_4_out, EX_nop, MEM_nop);
  // Incrementer incrementer_5: pin names not known; wires that end beside it: incrementer_4_p2, incrementer_5_p2
  Multiplexer #(.select(1), .width(16), .disabled("Z"), .enable("false")) multiplexer_19 (
    .in0(multiplexer_18_out), .in1(incrementer_5_p2), .out(multiplexer_19_out), .sel(or_6_out));
  and and_9 (and_9_out, Beq_p2, Equal);
  and and_10 (and_10_out, BLTZ_p2, Less);
  and and_11 (and_11_out, Bne_p2, ~Equal);  // AND_Gate
  or or_5 (or_5_out, JMP, JR);
  or or_6 (or_6_out, and_9_out, and_10_out, and_11_out, or_5_out);

  // Other names for the same wires on the sheet: ID_JumpAddr (some bits) = {ID_PC[31:28], Func};
  //   shamt[4:0] = ID_JumpAddr[12:8]; MEM_PC[31:0] = M_PC

  // Notes on the sheet:
  //   中断源
  //   中断等待指示
  //   控制停机
  //   IF
  //   数码管输出
  //   指令存储器
  //   指令字
  //   contents of rom_1 (hex, n*v repeats v):
  //   20110001 8000c05 20110001 20120002 20130003 8000c09 20110001 20120002 20130003 8000c0d 20110001
  //   20120002 20130003 8000c11 20110001 20120002 20130003 c000cb8 20100001 20110001 118fc0 112020
  //   20020022 c 118882 12200001 8000c15 112020 20020022 c 20110001 118880 112020 20020022 c 12200001
  //   8000c1f 20110001 118fc0 112020 20020022 c 1188c3 112020 20020022 c 118903 112020 20020022 c 118903
  //   112020 20020022 c 118903 112020 20020022 c 118903 112020 20020022 c 118903 112020 20020022 c 118903
  //   112020 20020022 c 118903 112020 20020022 c 20100001 109fc0 139fc3 8021 2012000c 24160003 26100001
  //   3210000f 20080008 20090001 139900 2709825 132020 20020022 c 1094022 1500fff9 22100001 2018000f
  //   2188024 108700 20080008 20090001 139902 2709825 132021 20020022 c 1094022 1500fff9 108702 2c9b022
  //   12c00001 8000c50 4020 1084027 84400 3508ffff 82021 20020022 c 2010ffff 20110000 ae300000 22100001
  //   22310004 ae300000 22100001 22310004 ae300000 22100001 22310004 ae300000 22100001 22310004 ae300000
  //   22100001 22310004 ae300000 22100001 22310004 ae300000 22100001 22310004 ae300000 22100001 22310004
  //   ae300000 22100001 22310004 ae300000 22100001 22310004 ae300000 22100001 22310004 ae300000 22100001
  //   22310004 ae300000 22100001 22310004 ae300000 22100001 22310004 ae300000 22100001 22310004 ae300000
  //   22100001 22310004 22100001 8020 2011003c 8e130000 8e340000 274402a 11000002 ae330000 ae140000
  //   2231fffc 1611fff8 102020 20020022 c 22100004 2011003c 1611fff2 20020032 c 20100000 22100001 102020
  //   20020022 c 22100002 102020 20020022 c 22100003 102020 20020022 c 22100004 102020 20020022 c 22100005
  //   102020 20020022 c 22100006 102020 20020022 c 22100007 102020 20020022 c 22100008 102020 20020022
  //   20020022 c 3e00008
  //   JMP
  //   JR
  //   OP
  //   Func
  //   Syscall
  //   OP
  //   Func
  //   rs
  //   rt
  //   rd
  //   Beq
  //   Bne
  //   MemToReg
  //   MemWrite
  //   AluOP
  //   AluSrcB
  //   RegWrite
  //   JAL
  //   RegDst
  //   LB
  //   BLTZ
  //   硬布线控制器
  //   ID
  //   流水调试日志用
  //   EX
  //   数码管显示电路
  //   为方便自动评测，需要输出流水线各段保存的PC值，注意是PC不是PC+4，另外ID段寄存器写入信息，Mem段内存写入信息也要输出
  //   MEM
  //   WB
  //   Watch
endmodule
module \重定向流水线  (
  output RegWrite,
  output MemWrite,
  output [31:0] IF_PC,
  output [31:0] ID_PC,
  output [31:0] EX_PC,
  output [31:0] M_PC,
  output [31:0] WB_PC,
  output [31:0] RDin,
  output [31:0] MDin,
  output [31:0] LedData
);

  wire AluSrcB, AluSrcB_p2, and_1_out, and_2_out, and_3_out, and_5_out, and_6_out, and_7_out, and_8_out,
       and_9_out, and_10_out, and_11_out, Beq, Beq_p2, BLTZ, BLTZ_p2, Bne, Bne_p2, CLK, d_ff_1_q, Equal,
       ex_mem_1_jal_p3, ex_mem_1_lb_p3, ex_mem_1_mem_syscall, EX_MemToReg, EX_nop, EX_RegWrite, Go, halt,
       halt1, halt2, id_ex_1_ex_syscall, id_ex_1_jal_p2, id_ex_1_lb_p2, id_ex_1_memwrite_p2, ID_JMP, ID_JR,
       ID_MemWrite, ID_RegWrite, IR1, IR2, IR3, JAL, JAL_p4, JMP, JR, LB, LB_p4, Less, MEM_MemToReg, MEM_nop,
       MEM_RegWrite, MemToReg, MemToReg_p4, multiplexer_15_out, nand_1_out, or_1_out, or_2_out, or_3_out,
       or_4_out, or_5_out, or_6_out, RegDst, RST, SignedExt, Syscall, W1, W2, W3, WB_Syscall;
  wire [1:0] Addr1___0, ID_R1_Forward, ID_R2_Forward, mem_wb_1_wb_addr1___0, R1_Forward, R2_Forward;
  wire [3:0] AluOP, AluOP_p2;
  wire [4:0] EX_WriteReg_num, MEM_WriteReg_num, multiplexer_4_out, R1_num, R2_num, shamt_p2, W, W_p4;
  wire [5:0] Func, OP;
  wire [7:0] multiplexer_14_out;
  wire [15:0] incrementer_1_p2, incrementer_2_p2, incrementer_3_p2, incrementer_4_p2, incrementer_5_p2,
       \LoadUse次数 , multiplexer_18_out, multiplexer_19_out, multiplexer_20_out, multiplexer_21_out, \总周期数 ,
       \插入气泡数 , \无条件分支数 , \条件分支成功数 ;
  wire [27:8] ID_JumpAddr;
  wire [31:0] adder_3_out, adder_4_out, AluResult, bit_extender_1_out, bit_extender_2_out,
       bit_extender_3_out, EX_R1, EX_R2, id_ex_1_imm_p2, id_ex_1_r2_p2, JumpAddr, mem_wb_1_memdata_p4,
       mips_alu_1_result, mips_probe_1_p1, multiplexer_1_out, multiplexer_2_out, multiplexer_3_out,
       multiplexer_8_out, multiplexer_9_out, multiplexer_11_out, multiplexer_12_out, multiplexer_16_out,
       PC_plus_4, PCBranch, R1, R2, ram_1_data, shifter_1_out, WB_MemData, WB_R2;
  wire [31:2] MEM_AluResult;

  Button \u_总复位  (.out(RST));
  Button _1 (.out(IR1));
  Button _2 (.out(IR2));
  Button _3 (.out(IR3));
  Button \u_继续运行  (.out(Go));
  LED #(.active("true")) led_1 (.in(W1));
  LED #(.active("true")) led_2 (.in(W2));
  LED #(.active("true")) led_3 (.in(W3));
  Multiplexer #(.select(1), .width(32), .disabled("Z"), .enable("false")) multiplexer_1 (
    .in0(PC_plus_4), .in1(JumpAddr), .out(multiplexer_1_out), .sel(JMP));
  Hex_Digit_Display hex_digit_display_1 (.value(LedData[31:28]));  // open: dp
  Multiplexer #(.select(1), .width(32), .disabled("Z"), .enable("false")) multiplexer_2 (
    .in0(multiplexer_1_out), .in1(EX_R1), .out(multiplexer_2_out), .sel(JR));
  and and_1 (and_1_out, Beq_p2, Equal);
  and and_2 (and_2_out, BLTZ_p2, Less);
  and and_3 (and_3_out, Bne_p2, ~Equal);  // AND_Gate
  Hex_Digit_Display hex_digit_display_2 (.value(LedData[23:20]));  // open: dp
  Hex_Digit_Display hex_digit_display_3 (.value(LedData[27:24]));  // open: dp
  and and_4 (halt, halt1, halt2);
  // Probe on multiplexer_3_out
  Multiplexer #(.select(1), .width(32), .disabled("Z"), .enable("false")) multiplexer_3 (
    .in0(multiplexer_2_out), .in1(PCBranch), .out(multiplexer_3_out), .sel(or_1_out));
  or or_1 (or_1_out, and_1_out, and_2_out, and_3_out);
  Hex_Digit_Display hex_digit_display_4 (.value(LedData[19:16]));  // open: dp
  Hex_Digit_Display hex_digit_display_5 (.value(LedData[15:12]));  // open: dp
  Register #(.width(32), .trigger("rising"), .Select("low")) PC (
    .D(multiplexer_3_out), .en(halt), .Q(IF_PC), .clk(CLK));  // open: clr
  Hex_Digit_Display hex_digit_display_6 (.value(LedData[11:8]));  // open: dp
  Hex_Digit_Display hex_digit_display_7 (.value(LedData[7:4]));  // open: dp
  Clock #(.highDuration(1), .lowDuration(1)) clock_1 (.out(CLK));
  Adder #(.width(32)) adder_1 (.a(IF_PC), .b(32'h4), .out(PC_plus_4));  // open: cin, cout
  Hex_Digit_Display hex_digit_display_8 (.value(LedData[3:0]));  // open: dp
  // Mips_Probe mips_probe_1: pin names not known; wires that end beside it: mips_probe_1_p1
  ROM #(.addrWidth(10), .dataWidth(32), .Select("high")) rom_1 (.addr(IF_PC[11:2]), .data(mips_probe_1_p1));
  IF___ID if_id_1 (
    .CLK(CLK), .JMP(JMP), .IF_PC(IF_PC), .IR(mips_probe_1_p1), .halt(halt), .JR(JR), .ID_PC(ID_PC),
    .IR_p1({OP, ID_JumpAddr, Func}), .in_3(Beq_p2), .in_7(Equal), .in_11(BLTZ_p2), .in_4(Less), .in_10(Bne_p2));
  // Probe on \总周期数 
  // Probe on \无条件分支数 
  // Probe on \条件分支成功数 
  // Probe on \插入气泡数 
  // Probe on \LoadUse次数 
  // Probe on IF_PC[11:0]
  \单周期硬布线控制器  \u_单周期硬布线控制器_1  (
    .Func(Func), .OP(OP), .ALU_OP(AluOP), .MemToReg(MemToReg), .MemWrite(ID_MemWrite), .ALU_SRC(AluSrcB),
    .RegWrite(ID_RegWrite), .SysCALL(Syscall), .SignedExt(SignedExt), .RegDst(RegDst), .JR(ID_JR),
    .JMP(ID_JMP), .Beq(Beq), .JAL(JAL), .Bne(Bne), .LB(LB), .BLTZ(BLTZ));  // open: eret
  Multiplexer #(.select(1), .width(5), .disabled("Z"), .enable("false")) multiplexer_4 (
    .in0(ID_JumpAddr[22:18]), .in1(ID_JumpAddr[17:13]), .out(multiplexer_4_out), .sel(RegDst));
  // Probe on ID_PC[11:0]
  // Probe on EX_PC[11:0]
  Multiplexer #(.select(1), .width(5), .disabled("Z"), .enable("false")) multiplexer_5 (
    .in0(ID_JumpAddr[27:23]), .in1(5'b00010), .out(R1_num), .sel(Syscall));
  Multiplexer #(.select(1), .width(5), .disabled("Z"), .enable("false")) multiplexer_6 (
    .in0(ID_JumpAddr[22:18]), .in1(5'b00100), .out(R2_num), .sel(Syscall));
  Multiplexer #(.select(1), .width(5), .disabled("Z"), .enable("false")) multiplexer_7 (
    .in0(multiplexer_4_out), .in1({5{1'b1}}), .out(W), .sel(JAL));
  // Probe on M_PC[11:0]
  assign bit_extender_1_out = {{16{1'b0}}, {ID_JumpAddr[17:8], Func}};  // Bit_Extender bit_extender_1
  assign bit_extender_2_out = {{16{ID_JumpAddr[17]}}, {ID_JumpAddr[17:8], Func}};  // Bit_Extender bit_extender_2
  // Probe on WB_PC[11:0]
  MIPS_Regifile mips_regifile_1 (
    .Din(RDin), .Clk(CLK), .R1(R1), .R2(R2), .WE(RegWrite), .W_num(W_p4), .R1_num(R1_num), .R2_num(R2_num));
  Multiplexer #(.select(1), .width(32), .disabled("Z"), .enable("false")) multiplexer_8 (
    .in0(bit_extender_1_out), .in1(bit_extender_2_out), .out(multiplexer_8_out), .sel(SignedExt));
  ID___EX id_ex_1 (
    .MemWrite(ID_MemWrite), .R1(R1), .AluOp(AluOP), .AluSrcB(AluSrcB), .R2(R2), .shamt(ID_JumpAddr[12:8]),
    .Beq(Beq), .imm(multiplexer_8_out), .BLTZ(BLTZ), .Bne(Bne), .ID_PC(ID_PC), .W(W), .MemTo_Reg(MemToReg),
    .CLK(CLK), .JAL(JAL), .ID_RegWrite(ID_RegWrite), .LB(LB), .R2_p2(id_ex_1_r2_p2), .Beq_p2(Beq_p2),
    .imm_p2(id_ex_1_imm_p2), .EX_PC(EX_PC), .W_p2(EX_WriteReg_num), .BLTZ_p2(BLTZ_p2),
    .MemToReg_p2(EX_MemToReg), .JAL_p2(id_ex_1_jal_p2), .EX_RegWrite(EX_RegWrite), .LB_p2(id_ex_1_lb_p2),
    .MemWrite_p2(id_ex_1_memwrite_p2), .AluOp_p2(AluOP_p2), .R1_p2(EX_R1), .AluSrcB_p2(AluSrcB_p2),
    .Bne_p2(Bne_p2), .shamt_p2(shamt_p2), .Equal(Equal), .Less(Less), .EX_nop(EX_nop), .MEM_nop(MEM_nop),
    .ID_JumpAddr({ID_PC[31:28], ID_JumpAddr, Func, 2'b00}), .JumpAddr(JumpAddr), .ID_JMP(ID_JMP),
    .ID_JR(ID_JR), .JMP(JMP), .JR(JR), .ID_Syscall(Syscall), .EX_Syscall(id_ex_1_ex_syscall),
    .ID_R1_Forward(ID_R1_Forward), .ID_R2_Forward(ID_R2_Forward), .R1_Forward(R1_Forward),
    .R2_Forward(R2_Forward), .halt1(halt1));
  Multiplexer #(.select(2), .width(32), .disabled("Z"), .enable("false")) multiplexer_9 (
    .in0(EX_R1), .in1({MEM_AluResult, Addr1___0}), .in2(AluResult), .in3(WB_MemData),
    .out(multiplexer_9_out), .sel(R1_Forward));
  Multiplexer #(.select(2), .width(32), .disabled("Z"), .enable("false")) multiplexer_10 (
    .in0(id_ex_1_r2_p2), .in1({MEM_AluResult, Addr1___0}), .in2(AluResult), .in3(WB_MemData), .out(EX_R2),
    .sel(R2_Forward));
  Multiplexer #(.select(1), .width(32), .disabled("Z"), .enable("false")) multiplexer_11 (
    .in0(EX_R2), .in1(id_ex_1_imm_p2), .out(multiplexer_11_out), .sel(AluSrcB_p2));
  Shifter #(.width(32), .shift("ll")) shifter_1 (.in(id_ex_1_imm_p2), .\dist (5'b00010), .out(shifter_1_out));
  Adder #(.width(32)) adder_2 (.a(shifter_1_out), .b(adder_3_out), .out(PCBranch));  // open: cin, cout
  Adder #(.width(32)) adder_3 (.a(32'h4), .b(EX_PC), .out(adder_3_out));  // open: cin, cout
  \重定向逻辑  \u_重定向逻辑_1  (
    .R1_num(R1_num), .OP(OP), .EX_WriteReg_num(EX_WriteReg_num), .EX_RegWrite(EX_RegWrite),
    .EX_MemToReg(EX_MemToReg), .Syscall(Syscall), .R2_num(R2_num), .Func(Func),
    .MEM_WriteReg_num(MEM_WriteReg_num), .MEM_RegWrite(MEM_RegWrite), .MEM_MemToReg(MEM_MemToReg),
    .R1_Forward(ID_R1_Forward), .R2_Forward(ID_R2_Forward), .EX_nop(EX_nop), .MEM_nop(MEM_nop), .halt(halt2));
  MIPS_ALU mips_alu_1 (
    .X(multiplexer_9_out), .Y(multiplexer_11_out), .AluOP(AluOP_p2), .Equal(Equal),
    .Result(mips_alu_1_result), .shamt(shamt_p2), .Less(Less));  // open: Result_2
  EX___MEM ex_mem_1 (
    .MemWrite(id_ex_1_memwrite_p2), .ALUResult(mips_alu_1_result), .CLK(CLK), .MDin(EX_R2), .EX_PC(EX_PC),
    .W(EX_WriteReg_num), .MemTo_Reg(EX_MemToReg), .JAL(id_ex_1_jal_p2), .EX_RegWrite(EX_RegWrite),
    .LB(id_ex_1_lb_p2), .JAL_p3(ex_mem_1_jal_p3), .MEM_RegWrite(MEM_RegWrite),
    .ALUResult_p3({MEM_AluResult, Addr1___0}), .MDin_p3(MDin), .LB_p3(ex_mem_1_lb_p3), .MEM_PC(M_PC),
    .W_p3(MEM_WriteReg_num), .MemToReg_p3(MEM_MemToReg), .MemWrite_p3(MemWrite),
    .EX_Syscall(id_ex_1_ex_syscall), .MEM_Syscall(ex_mem_1_mem_syscall), .halt1(halt1));
  RAM #(.addrWidth(10), .dataWidth(32), .bus("separate"), .Select("high")) ram_1 (
    .addr(MEM_AluResult[11:2]), .din(MDin), .data(ram_1_data), .str(MemWrite), .clk(CLK), .ld(1'b1));  // open: sel, clr
  MEM___WB mem_wb_1 (
    .ALUResult({MEM_AluResult, Addr1___0}), .CLK(CLK), .MEM_PC(M_PC), .W(MEM_WriteReg_num),
    .MemTo_Reg(MEM_MemToReg), .JAL(ex_mem_1_jal_p3), .MEM_RegWrite(MEM_RegWrite), .LB(ex_mem_1_lb_p3),
    .JAL_p4(JAL_p4), .WB_RegWrite(RegWrite), .ALUResult_p4(AluResult), .MemData_p4(mem_wb_1_memdata_p4),
    .LB_p4(LB_p4), .WB_PC(WB_PC), .W_p4(W_p4), .MemToReg_p4(MemToReg_p4), .MemData(ram_1_data),
    .MEM_R2(MDin), .WB_R2(WB_R2), .MEM_Syscall(ex_mem_1_mem_syscall), .WB_Syscall(WB_Syscall), .halt1(halt1),
    .Addr1___0(Addr1___0), .WB_Addr1___0(mem_wb_1_wb_addr1___0));
  and and_5 (and_5_out, AluResult[0], WB_Syscall);
  Register #(.width(32), .trigger("rising"), .Select("low")) register_1 (
    .D(multiplexer_12_out), .Q(LedData), .clk(CLK));  // open: en, clr
  Multiplexer #(.select(1), .width(32), .disabled("Z"), .enable("false")) multiplexer_12 (
    .in0(LedData), .in1(WB_R2), .out(multiplexer_12_out), .sel(and_5_out));
  Multiplexer #(.select(1), .width(32), .disabled("Z"), .enable("false")) multiplexer_13 (
    .in0(mem_wb_1_memdata_p4), .in1(bit_extender_3_out), .out(WB_MemData), .sel(LB_p4));
  Multiplexer #(.select(2), .width(8), .disabled("Z"), .enable("false")) multiplexer_14 (
    .in0(mem_wb_1_memdata_p4[7:0]), .in1(mem_wb_1_memdata_p4[15:8]), .in2(mem_wb_1_memdata_p4[23:16]),
    .in3(mem_wb_1_memdata_p4[31:24]), .out(multiplexer_14_out), .sel(mem_wb_1_wb_addr1___0));
  assign bit_extender_3_out = {{24{multiplexer_14_out[7]}}, multiplexer_14_out};  // Bit_Extender bit_extender_3
  nand nand_1 (nand_1_out, ~AluResult[0], WB_Syscall);  // NAND_Gate
  Multiplexer #(.select(1), .width(1), .disabled("Z"), .enable("false")) multiplexer_15 (
    .in0(1'b1), .in1(d_ff_1_q), .out(multiplexer_15_out), .sel(nand_1_out));
  D_Flip_Flop #(.trigger("rising"), .Pre_Clr_Positions("ABOVE_BELOW"), .NegatePresetClear("false"), .enable("false"), .NewFFLayout("false")) d_ff_1 (
    .clk(CLK), .D(multiplexer_15_out), .Q(d_ff_1_q), .reset(Go));  // open: Qn, preset
  not not_1 (halt1, d_ff_1_q);
  Multiplexer #(.select(1), .width(32), .disabled("Z"), .enable("false")) multiplexer_16 (
    .in0(AluResult), .in1(WB_MemData), .out(multiplexer_16_out), .sel(MemToReg_p4));
  Adder #(.width(32)) adder_4 (.a(32'h4), .b(WB_PC), .out(adder_4_out));  // open: cin, cout
  Multiplexer #(.select(1), .width(32), .disabled("Z"), .enable("false")) multiplexer_17 (
    .in0(multiplexer_16_out), .in1(adder_4_out), .out(RDin), .sel(JAL_p4));
  Register #(.width(16), .trigger("rising"), .Select("low")) register_2 (
    .D(incrementer_1_p2), .en(halt1), .Q(\总周期数 ), .clk(CLK));  // open: clr
  Register #(.width(16), .trigger("rising"), .Select("low")) register_3 (
    .D(multiplexer_18_out), .en(halt1), .Q(\无条件分支数 ), .clk(CLK));  // open: clr
  Register #(.width(16), .trigger("rising"), .Select("low")) register_4 (
    .D(multiplexer_19_out), .en(halt1), .Q(\条件分支成功数 ), .clk(CLK));  // open: clr
  and and_6 (and_6_out, Beq_p2, Equal);
  and and_7 (and_7_out, BLTZ_p2, Less);
  and and_8 (and_8_out, Bne_p2, ~Equal);  // AND_Gate
  Register #(.width(16), .trigger("rising"), .Select("low")) register_5 (
    .D(multiplexer_21_out), .en(halt1), .Q(\插入气泡数 ), .clk(CLK));  // open: clr
  // Incrementer incrementer_1: pin names not known; wires that end beside it: \总周期数 , incrementer_1_p2
  // Incrementer incrementer_2: pin names not known; wires that end beside it: \无条件分支数 , incrementer_2_p2
  or or_2 (or_2_out, JMP, JR);
  // Incrementer incrementer_3: pin names not known; wires that end beside it: \条件分支成功数 , incrementer_3_p2
  or or_3 (or_3_out, and_6_out, and_7_out, and_8_out);
  // Incrementer incrementer_4: pin names not known; wires that end beside it: \插入气泡数 , incrementer_4_p2
  or or_4 (or_4_out, EX_nop, MEM_nop);
  Multiplexer #(.select(1), .width(16), .disabled("Z"), .enable("false")) multiplexer_18 (
    .in0(\无条件分支数 ), .in1(incrementer_2_p2), .out(multiplexer_18_out), .sel(or_2_out));
  Multiplexer #(.select(1), .width(16), .disabled("Z"), .enable("false")) multiplexer_19 (
    .in0(\条件分支成功数 ), .in1(incrementer_3_p2), .out(multiplexer_19_out), .sel(or_3_out));
  Multiplexer #(.select(1), .width(16), .disabled("Z"), .enable("false")) multiplexer_20 (
    .in0(\插入气泡数 ), .in1(incrementer_4_p2), .out(multiplexer_20_out), .sel(or_4_out));
  // Incrementer incrementer_5: pin names not known; wires that end beside it: incrementer_4_p2, incrementer_5_p2
  Multiplexer #(.select(1), .width(16), .disabled("Z"), .enable("false")) multiplexer_21 (
    .in0(multiplexer_20_out), .in1(incrementer_5_p2), .out(multiplexer_21_out), .sel(or_5_out));
  and and_9 (and_9_out, Beq_p2, Equal);
  and and_10 (and_10_out, BLTZ_p2, Less);
  or or_5 (or_5_out, and_9_out, and_10_out, and_11_out, or_6_out);
  and and_11 (and_11_out, Bne_p2, ~Equal);  // AND_Gate
  or or_6 (or_6_out, JMP, JR);

  // Other names for the same wires on the sheet: ID_JumpAddr (some bits) = {ID_PC[31:28], Func};
  //   shamt[4:0] = ID_JumpAddr[12:8]; MEM_AluResult[1:0] = Addr1___0; MEM_PC[31:0] = M_PC

  // Notes on the sheet:
  //   中断源
  //   中断等待指示
  //   控制停机
  //   IF
  //   数码管输出
  //   指令存储器
  //   指令字
  //   contents of rom_1 (hex, n*v repeats v):
  //   20110001 8100005 20110001 20120002 20130003 8100009 20110001 20120002 20130003 810000d 20110001
  //   20120002 20130003 8100011 20110001 20120002 20130003 c1000f7 20100001 20110001 118fc0 112020
  //   20020022 c 118882 12200001 8100015 112020 20020022 c 20110001 118880 112020 20020022 c 12200001
  //   810001f 20110001 118fc0 112020 20020022 c 1188c3 112020 20020022 c 118903 112020 20020022 c 118903
  //   112020 20020022 c 118903 112020 20020022 c 118903 112020 20020022 c 118903 112020 20020022 c 118903
  //   112020 20020022 c 118903 112020 20020022 c 20100001 109fc0 139fc3 8021 2012000c 24160003 26100001
  //   3210000f 20080008 20090001 139900 2709825 132020 20020022 c 1094022 1500fff9 22100001 2018000f
  //   2188024 108700 20080008 20090001 139902 2709825 132021 20020022 c 1094022 1500fff9 108702 2c9b022
  //   12c00001 8100050 4020 1084027 84400 3508ffff 82021 20020022 c 2010ffff 20110000 ae300000 22100001
  //   22310004 ae300000 22100001 22310004 ae300000 22100001 22310004 ae300000 22100001 22310004 ae300000
  //   22100001 22310004 ae300000 22100001 22310004 ae300000 22100001 22310004 ae300000 22100001 22310004
  //   ae300000 22100001 22310004 ae300000 22100001 22310004 ae300000 22100001 22310004 ae300000 22100001
  //   22310004 ae300000 22100001 22310004 ae300000 22100001 22310004 ae300000 22100001 22310004 ae300000
  //   22100001 22310004 22100001 8020 2011003c 8e130000 8e340000 274402a 11000002 ae330000 ae140000
  //   2231fffc 1611fff8 102020 20020022 c 22100004 2011003c 1611fff2 20020032 c 20080001 20090003 20110876
  //   118d00 112020 20020022 c 200b0008 1118807 1318807 112020 20020022 c 216bffff 1560fff9 2002000a c
  //   2008ffff 20117777 112020 20020022 c 200b0010 2288826 112020 20020022 c 216bffff 1560fffa 2002000a c
  //   20090000 200b0010 34118483 20120404 118c00 129400 36318281 22520404 ad310000 2328820 21290004
  //   216bffff 1560fffb 200b0020 20090000 81310000 112020 20020022 c 21290001 216bffff 1560fff9 2002000a c
  //   2011fff1 112020 20020022 c 22310001 620fffb 2002000a c 20100000 22100001 102020 20020022 c 22100002
  //   102020 20020022 c 22100003 102020 20020022 c 22100004 102020 20020022 c 22100005 102020 20020022 c
  //   22100006 102020 20020022 c 22100007 102020 20020022 c 22100008 102020 20020022 20020022 c 3e00008
  //   JMP
  //   JR
  //   OP
  //   Func
  //   Syscall
  //   OP
  //   Func
  //   rs
  //   rt
  //   rd
  //   Beq
  //   Bne
  //   MemToReg
  //   MemWrite
  //   AluOP
  //   AluSrcB
  //   RegWrite
  //   JAL
  //   RegDst
  //   LB
  //   BLTZ
  //   硬布线控制器
  //   ID
  //   流水调试日志用
  //   EX
  //   为方便自动评测，需要输出流水线各段保存的PC值，注意是PC不是PC+4，另外ID段寄存器写入信息，Mem段内存写入信息也要输出
  //   重定向逻辑
  //   MEM
  //   WB
  //   Watch
endmodule

// 中断请求生成
module \中断按键参考电路  (
  input  CLK,
  input  \_1号中断 ,
  input  \同步清零信号 ,
  output \与中断屏蔽位与 ,
  output \_1号中断等待指示灯 
);

  wire and_1_out, d_ff_1_q, or_2_out;

  or or_1 (\_1号中断等待指示灯 , \与中断屏蔽位与 , d_ff_1_q);
  D_Flip_Flop #(.trigger("rising"), .Pre_Clr_Positions("LEGACY"), .NegatePresetClear("false"), .enable("true"), .NewFFLayout("false")) d_ff_1 (
    .clk(\_1号中断 ), .D(1'b1), .Q(d_ff_1_q), .reset(\与中断屏蔽位与 ));  // open: Qn, preset, en
  or or_2 (or_2_out, d_ff_1_q, \与中断屏蔽位与 );
  and and_1 (and_1_out, or_2_out, ~\同步清零信号 );  // AND_Gate
  D_Flip_Flop #(.trigger("rising"), .Pre_Clr_Positions("LEGACY"), .NegatePresetClear("false"), .enable("true"), .NewFFLayout("false")) IR1 (
    .clk(CLK), .D(and_1_out), .Q(\与中断屏蔽位与 ));  // open: Qn, preset, en, reset

  // Notes on the sheet:
  //   中断信号采样参考电路
  //   Reset 
endmodule

module IF___ID (
  input  CLK,
  input  JMP,
  input  in_3,
  input  in_4,
  input  [31:0] IF_PC,
  input  [31:0] IR,
  input  in_7,
  input  halt,
  input  JR,
  input  in_10,
  input  in_11,
  output [31:0] ID_PC,
  output [31:0] IR_p1
);

  wire and_1_out, and_2_out, and_3_out, or_1_out, or_2_out;
  wire [31:0] multiplexer_1_out, multiplexer_2_out;

  and and_1 (and_1_out, in_3, in_7);
  and and_2 (and_2_out, in_11, in_4);
  and and_3 (and_3_out, in_10, ~in_7);  // AND_Gate
  Multiplexer #(.select(1), .width(32), .disabled("Z"), .enable("false")) multiplexer_1 (
    .in0(IF_PC), .in1({32{1'b0}}), .out(multiplexer_1_out), .sel(or_2_out));
  Multiplexer #(.select(1), .width(32), .disabled("Z"), .enable("false")) multiplexer_2 (
    .in0(IR), .in1({32{1'b0}}), .out(multiplexer_2_out), .sel(or_2_out));
  or or_1 (or_1_out, and_1_out, and_2_out, and_3_out);
  or or_2 (or_2_out, JMP, or_1_out, JR);
  Register #(.width(32), .trigger("rising"), .Select("low")) register_1 (
    .D(multiplexer_1_out), .en(halt), .Q(ID_PC), .clk(CLK));  // open: clr
  Register #(.width(32), .trigger("rising"), .Select("low")) register_2 (
    .D(multiplexer_2_out), .en(halt), .Q(IR_p1), .clk(CLK));  // open: clr

  // Other names for the same wires on the sheet: Beq_p2 = in_3; BLTZ_p2 = in_11; Bne_p2 = in_10; Equal = in_7;
  //   Less = in_4

  // Notes on the sheet:
  //   输出
  //   输入
endmodule

module ID___EX (
  input  MemWrite,
  input  [31:0] R1,
  input  [3:0] AluOp,
  input  AluSrcB,
  input  [31:0] R2,
  input  [4:0] shamt,
  input  Beq,
  input  [31:0] imm,
  input  BLTZ,
  input  Bne,
  input  [31:0] ID_PC,
  input  [1:0] ID_R1_Forward,
  input  [1:0] ID_R2_Forward,
  input  [4:0] W,
  input  MemTo_Reg,
  input  Equal,
  input  JAL,
  input  Less,
  input  ID_RegWrite,
  input  CLK,
  input  LB,
  input  EX_nop,
  input  ID_Syscall,
  input  MEM_nop,
  input  ID_JMP,
  input  ID_JR,
  input  halt1,
  input  [31:0] ID_JumpAddr,
  output [31:0] R2_p2,
  output Beq_p2,
  output [31:0] imm_p2,
  output [31:0] R1_p2,
  output [31:0] EX_PC,
  output [1:0] R1_Forward,
  output [4:0] W_p2,
  output [1:0] R2_Forward,
  output MemToReg_p2,
  output JAL_p2,
  output BLTZ_p2,
  output EX_RegWrite,
  output LB_p2,
  output EX_Syscall,
  output MemWrite_p2,
  output [3:0] AluOp_p2,
  output AluSrcB_p2,
  output Bne_p2,
  output [4:0] shamt_p2,
  output JMP,
  output JR,
  output [31:0] JumpAddr
);

  wire and_1_out, and_2_out, and_3_out, multiplexer_3_out, multiplexer_4_out, multiplexer_5_out,
       multiplexer_8_out, multiplexer_9_out, multiplexer_10_out, multiplexer_13_out, multiplexer_14_out,
       multiplexer_15_out, multiplexer_18_out, multiplexer_19_out, multiplexer_20_out, or_1_out;
  wire [1:0] multiplexer_17_out, multiplexer_22_out;
  wire [3:0] multiplexer_7_out;
  wire [4:0] multiplexer_2_out, multiplexer_12_out;
  wire [31:0] multiplexer_1_out, multiplexer_6_out, multiplexer_11_out, multiplexer_16_out,
       multiplexer_21_out;

  and and_1 (and_1_out, Beq_p2, Equal);
  and and_2 (and_2_out, BLTZ_p2, Less);
  and and_3 (and_3_out, Bne_p2, ~Equal);  // AND_Gate
  or or_1 (or_1_out, JMP, and_1_out, and_2_out, MEM_nop, and_3_out, EX_nop, JR);
  Multiplexer #(.select(1), .width(32), .disabled("Z"), .enable("false")) multiplexer_1 (
    .in0(R1), .in1({32{1'b0}}), .out(multiplexer_1_out), .sel(or_1_out));
  Multiplexer #(.select(1), .width(5), .disabled("Z"), .enable("false")) multiplexer_2 (
    .in0(W), .in1({5{1'b0}}), .out(multiplexer_2_out), .sel(or_1_out));
  Multiplexer #(.select(1), .width(1), .disabled("Z"), .enable("false")) multiplexer_3 (
    .in0(MemTo_Reg), .in1(1'b0), .out(multiplexer_3_out), .sel(or_1_out));
  Multiplexer #(.select(1), .width(1), .disabled("Z"), .enable("false")) multiplexer_4 (
    .in0(MemWrite), .in1(1'b0), .out(multiplexer_4_out), .sel(or_1_out));
  Multiplexer #(.select(1), .width(1), .disabled("Z"), .enable("false")) multiplexer_5 (
    .in0(Bne), .in1(1'b0), .out(multiplexer_5_out), .sel(or_1_out));
  Register #(.width(32), .trigger("rising"), .Select("low")) register_1 (
    .D(multiplexer_1_out), .en(halt1), .Q(R1_p2), .clk(CLK));  // open: clr
  Register #(.width(5), .trigger("rising"), .Select("low")) register_2 (
    .D(multiplexer_2_out), .en(halt1), .Q(W_p2), .clk(CLK));  // open: clr
  D_Flip_Flop #(.trigger("rising"), .Pre_Clr_Positions("LEGACY"), .NegatePresetClear("false"), .enable("true"), .NewFFLayout("false")) d_ff_1 (
    .clk(CLK), .D(multiplexer_3_out), .Q(MemToReg_p2), .en(halt1));  // open: Qn, preset, reset
  D_Flip_Flop #(.trigger("rising"), .Pre_Clr_Positions("LEGACY"), .NegatePresetClear("false"), .enable("true"), .NewFFLayout("false")) d_ff_2 (
    .clk(CLK), .D(multiplexer_4_out), .Q(MemWrite_p2), .en(halt1));  // open: Qn, preset, reset
  D_Flip_Flop #(.trigger("rising"), .Pre_Clr_Positions("LEGACY"), .NegatePresetClear("false"), .enable("true"), .NewFFLayout("false")) d_ff_3 (
    .clk(CLK), .D(multiplexer_5_out), .Q(Bne_p2), .en(halt1));  // open: Qn, preset, reset
  Multiplexer #(.select(1), .width(32), .disabled("Z"), .enable("false")) multiplexer_6 (
    .in0(R2), .in1({32{1'b0}}), .out(multiplexer_6_out), .sel(or_1_out));
  Multiplexer #(.select(1), .width(4), .disabled("Z"), .enable("false")) multiplexer_7 (
    .in0(AluOp), .in1(4'b0000), .out(multiplexer_7_out), .sel(or_1_out));
  Register #(.width(32), .trigger("rising"), .Select("low")) register_3 (
    .D(multiplexer_6_out), .en(halt1), .Q(R2_p2), .clk(CLK));  // open: clr
  Register #(.width(4), .trigger("rising"), .Select("low")) register_4 (
    .D(multiplexer_7_out), .en(halt1), .Q(AluOp_p2), .clk(CLK));  // open: clr
  Multiplexer #(.select(1), .width(1), .disabled("Z"), .enable("false")) multiplexer_8 (
    .in0(JAL), .in1(1'b0), .out(multiplexer_8_out), .sel(or_1_out));
  Multiplexer #(.select(1), .width(1), .disabled("Z"), .enable("false")) multiplexer_9 (
    .in0(AluSrcB), .in1(1'b0), .out(multiplexer_9_out), .sel(or_1_out));
  Multiplexer #(.select(1), .width(1), .disabled("Z"), .enable("false")) multiplexer_10 (
    .in0(ID_Syscall), .in1(1'b0), .out(multiplexer_10_out), .sel(or_1_out));
  D_Flip_Flop #(.trigger("rising"), .Pre_Clr_Positions("LEGACY"), .NegatePresetClear("false"), .enable("true"), .NewFFLayout("false")) d_ff_4 (
    .clk(CLK), .D(multiplexer_8_out), .Q(JAL_p2), .en(halt1));  // open: Qn, preset, reset
  D_Flip_Flop #(.trigger("rising"), .Pre_Clr_Positions("LEGACY"), .NegatePresetClear("false"), .enable("true"), .NewFFLayout("false")) d_ff_5 (
    .clk(CLK), .D(multiplexer_9_out), .Q(AluSrcB_p2), .en(halt1));  // open: Qn, preset, reset
  D_Flip_Flop #(.trigger("rising"), .Pre_Clr_Positions("LEGACY"), .NegatePresetClear("false"), .enable("true"), .NewFFLayout("false")) d_ff_6 (
    .clk(CLK), .D(multiplexer_10_out), .Q(EX_Syscall), .en(halt1));  // open: Qn, preset, reset
  Multiplexer #(.select(1), .width(32), .disabled("Z"), .enable("false")) multiplexer_11 (
    .in0(imm), .in1({32{1'b0}}), .out(multiplexer_11_out), .sel(or_1_out));
  Multiplexer #(.select(1), .width(5), .disabled("Z"), .enable("false")) multiplexer_12 (
    .in0(shamt), .in1({5{1'b0}}), .out(multiplexer_12_out), .sel(or_1_out));
  Register #(.width(32), .trigger("rising"), .Select("low")) register_5 (
    .D(multiplexer_11_out), .en(halt1), .Q(imm_p2), .clk(CLK));  // open: clr
  Register #(.width(5), .trigger("rising"), .Select("low")) register_6 (
    .D(multiplexer_12_out), .en(halt1), .Q(shamt_p2), .clk(CLK));  // open: clr
  Multiplexer #(.select(1), .width(1), .disabled("Z"), .enable("false")) multiplexer_13 (
    .in0(ID_RegWrite), .in1(1'b0), .out(multiplexer_13_out), .sel(or_1_out));
  Multiplexer #(.select(1), .width(1), .disabled("Z"), .enable("false")) multiplexer_14 (
    .in0(Beq), .in1(1'b0), .out(multiplexer_14_out), .sel(or_1_out));
  Multiplexer #(.select(1), .width(1), .disabled("Z"), .enable("false")) multiplexer_15 (
    .in0(ID_JMP), .in1(1'b0), .out(multiplexer_15_out), .sel(or_1_out));
  D_Flip_Flop #(.trigger("rising"), .Pre_Clr_Positions("LEGACY"), .NegatePresetClear("false"), .enable("true"), .NewFFLayout("false")) d_ff_7 (
    .clk(CLK), .D(multiplexer_13_out), .Q(EX_RegWrite), .en(halt1));  // open: Qn, preset, reset
  D_Flip_Flop #(.trigger("rising"), .Pre_Clr_Positions("LEGACY"), .NegatePresetClear("false"), .enable("true"), .NewFFLayout("false")) d_ff_8 (
    .clk(CLK), .D(multiplexer_14_out), .Q(Beq_p2), .en(halt1));  // open: Qn, preset, reset
  D_Flip_Flop #(.trigger("rising"), .Pre_Clr_Positions("LEGACY"), .NegatePresetClear("false"), .enable("true"), .NewFFLayout("false")) d_ff_9 (
    .clk(CLK), .D(multiplexer_15_out), .Q(JMP), .en(halt1));  // open: Qn, preset, reset
  Multiplexer #(.select(1), .width(32), .disabled("Z"), .enable("false")) multiplexer_16 (
    .in0(ID_PC), .in1({32{1'b0}}), .out(multiplexer_16_out), .sel(or_1_out));
  Register #(.width(32), .trigger("rising"), .Select("low")) register_7 (
    .D(multiplexer_16_out), .en(halt1), .Q(EX_PC), .clk(CLK));  // open: clr
  Multiplexer #(.select(1), .width(2), .disabled("Z"), .enable("false")) multiplexer_17 (
    .in0(ID_R1_Forward), .in1(2'b00), .out(multiplexer_17_out), .sel(or_1_out));
  Register #(.width(2), .trigger("rising"), .Select("low")) register_8 (
    .D(multiplexer_17_out), .en(halt1), .Q(R1_Forward), .clk(CLK));  // open: clr
  Multiplexer #(.select(1), .width(1), .disabled("Z"), .enable("false")) multiplexer_18 (
    .in0(LB), .in1(1'b0), .out(multiplexer_18_out), .sel(or_1_out));
  Multiplexer #(.select(1), .width(1), .disabled("Z"), .enable("false")) multiplexer_19 (
    .in0(BLTZ), .in1(1'b0), .out(multiplexer_19_out), .sel(or_1_out));
  Multiplexer #(.select(1), .width(1), .disabled("Z"), .enable("false")) multiplexer_20 (
    .in0(ID_JR), .in1(1'b0), .out(multiplexer_20_out), .sel(or_1_out));
  Multiplexer #(.select(1), .width(32), .disabled("Z"), .enable("false")) multiplexer_21 (
    .in0(ID_JumpAddr), .in1({32{1'b0}}), .out(multiplexer_21_out), .sel(or_1_out));
  D_Flip_Flop #(.trigger("rising"), .Pre_Clr_Positions("LEGACY"), .NegatePresetClear("false"), .enable("true"), .NewFFLayout("false")) d_ff_10 (
    .clk(CLK), .D(multiplexer_18_out), .Q(LB_p2), .en(halt1));  // open: Qn, preset, reset
  D_Flip_Flop #(.trigger("rising"), .Pre_Clr_Positions("LEGACY"), .NegatePresetClear("false"), .enable("true"), .NewFFLayout("false")) d_ff_11 (
    .clk(CLK), .D(multiplexer_19_out), .Q(BLTZ_p2), .en(halt1));  // open: Qn, preset, reset
  D_Flip_Flop #(.trigger("rising"), .Pre_Clr_Positions("LEGACY"), .NegatePresetClear("false"), .enable("true"), .NewFFLayout("false")) d_ff_12 (
    .clk(CLK), .D(multiplexer_20_out), .Q(JR), .en(halt1));  // open: Qn, preset, reset
  Register #(.width(32), .trigger("rising"), .Select("low")) register_9 (
    .D(multiplexer_21_out), .en(halt1), .Q(JumpAddr), .clk(CLK));  // open: clr
  Multiplexer #(.select(1), .width(2), .disabled("Z"), .enable("false")) multiplexer_22 (
    .in0(ID_R2_Forward), .in1(2'b00), .out(multiplexer_22_out), .sel(or_1_out));
  Register #(.width(2), .trigger("rising"), .Select("low")) register_10 (
    .D(multiplexer_22_out), .en(halt1), .Q(R2_Forward), .clk(CLK));  // open: clr

  // Notes on the sheet:
  //   输入
  //   输出
endmodule

module EX___MEM (
  input  MemWrite,
  input  [31:0] ALUResult,
  input  CLK,
  input  EX_Syscall,
  input  [31:0] MDin,
  input  [31:0] EX_PC,
  input  [4:0] W,
  input  MemTo_Reg,
  input  JAL,
  input  EX_RegWrite,
  input  LB,
  input  halt1,
  output JAL_p3,
  output MEM_RegWrite,
  output [31:0] ALUResult_p3,
  output MEM_Syscall,
  output [31:0] MDin_p3,
  output LB_p3,
  output [31:0] MEM_PC,
  output [4:0] W_p3,
  output MemToReg_p3,
  output MemWrite_p3
);

  Register #(.width(32), .trigger("rising"), .Select("low")) register_1 (
    .D(ALUResult), .en(halt1), .Q(ALUResult_p3), .clk(CLK));  // open: clr
  D_Flip_Flop #(.trigger("rising"), .Pre_Clr_Positions("ABOVE_BELOW"), .NegatePresetClear("false"), .enable("true"), .NewFFLayout("false")) d_ff_1 (
    .clk(CLK), .D(MemTo_Reg), .Q(MemToReg_p3), .en(halt1));  // open: Qn, preset, reset
  D_Flip_Flop #(.trigger("rising"), .Pre_Clr_Positions("ABOVE_BELOW"), .NegatePresetClear("false"), .enable("true"), .NewFFLayout("false")) d_ff_2 (
    .clk(CLK), .D(LB), .Q(LB_p3), .en(halt1));  // open: Qn, preset, reset
  Register #(.width(32), .trigger("rising"), .Select("low")) register_2 (
    .D(MDin), .en(halt1), .Q(MDin_p3), .clk(CLK));  // open: clr
  D_Flip_Flop #(.trigger("rising"), .Pre_Clr_Positions("ABOVE_BELOW"), .NegatePresetClear("false"), .enable("true"), .NewFFLayout("false")) d_ff_3 (
    .clk(CLK), .D(JAL), .Q(JAL_p3), .en(halt1));  // open: Qn, preset, reset
  D_Flip_Flop #(.trigger("rising"), .Pre_Clr_Positions("ABOVE_BELOW"), .NegatePresetClear("false"), .enable("true"), .NewFFLayout("false")) d_ff_4 (
    .clk(CLK), .D(MemWrite), .Q(MemWrite_p3), .en(halt1));  // open: Qn, preset, reset
  Register #(.width(32), .trigger("rising"), .Select("low")) register_3 (
    .D(EX_PC), .en(halt1), .Q(MEM_PC), .clk(CLK));  // open: clr
  D_Flip_Flop #(.trigger("rising"), .Pre_Clr_Positions("ABOVE_BELOW"), .NegatePresetClear("false"), .enable("true"), .NewFFLayout("false")) d_ff_5 (
    .clk(CLK), .D(EX_RegWrite), .Q(MEM_RegWrite), .en(halt1));  // open: Qn, preset, reset
  D_Flip_Flop #(.trigger("rising"), .Pre_Clr_Positions("ABOVE_BELOW"), .NegatePresetClear("false"), .enable("true"), .NewFFLayout("false")) d_ff_6 (
    .clk(CLK), .D(EX_Syscall), .Q(MEM_Syscall), .en(halt1));  // open: Qn, preset, reset
  Register #(.width(5), .trigger("rising"), .Select("low")) register_4 (
    .D(W), .en(halt1), .Q(W_p3), .clk(CLK));  // open: clr

  // Notes on the sheet:
  //   输入
  //   输出
endmodule

module MEM___WB (
  input  CLK,
  input  [31:0] ALUResult,
  input  [31:0] MEM_R2,
  input  [31:0] MemData,
  input  MEM_Syscall,
  input  [31:0] MEM_PC,
  input  [4:0] W,
  input  MemTo_Reg,
  input  JAL,
  input  MEM_RegWrite,
  input  LB,
  input  halt1,
  input  [1:0] Addr1___0,
  output JAL_p4,
  output [31:0] WB_R2,
  output WB_Syscall,
  output WB_RegWrite,
  output [31:0] MemData_p4,
  output [31:0] ALUResult_p4,
  output [31:0] WB_PC,
  output [4:0] W_p4,
  output LB_p4,
  output MemToReg_p4,
  output [1:0] WB_Addr1___0
);

  Register #(.width(32), .trigger("rising"), .Select("low")) register_1 (
    .D(ALUResult), .en(halt1), .Q(ALUResult_p4), .clk(CLK));  // open: clr
  D_Flip_Flop #(.trigger("rising"), .Pre_Clr_Positions("ABOVE_BELOW"), .NegatePresetClear("false"), .enable("true"), .NewFFLayout("false")) d_ff_1 (
    .clk(CLK), .D(MemTo_Reg), .Q(MemToReg_p4), .en(halt1));  // open: Qn, preset, reset
  D_Flip_Flop #(.trigger("rising"), .Pre_Clr_Positions("LEGACY"), .NegatePresetClear("false"), .enable("true"), .NewFFLayout("false")) d_ff_2 (
    .clk(CLK), .D(LB), .Q(LB_p4), .en(halt1));  // open: Qn, preset, reset
  Register #(.width(32), .trigger("rising"), .Select("low")) register_2 (
    .D(MemData), .en(halt1), .Q(MemData_p4), .clk(CLK));  // open: clr
  D_Flip_Flop #(.trigger("rising"), .Pre_Clr_Positions("ABOVE_BELOW"), .NegatePresetClear("false"), .enable("true"), .NewFFLayout("false")) d_ff_3 (
    .clk(CLK), .D(JAL), .Q(JAL_p4), .en(halt1));  // open: Qn, preset, reset
  D_Flip_Flop #(.trigger("rising"), .Pre_Clr_Positions("ABOVE_BELOW"), .NegatePresetClear("false"), .enable("true"), .NewFFLayout("false")) d_ff_4 (
    .clk(CLK), .D(MEM_Syscall), .Q(WB_Syscall), .en(halt1));  // open: Qn, preset, reset
  Register #(.width(32), .trigger("rising"), .Select("low")) register_3 (
    .D(MEM_PC), .en(halt1), .Q(WB_PC), .clk(CLK));  // open: clr
  D_Flip_Flop #(.trigger("rising"), .Pre_Clr_Positions("ABOVE_BELOW"), .NegatePresetClear("false"), .enable("true"), .NewFFLayout("false")) d_ff_5 (
    .clk(CLK), .D(MEM_RegWrite), .Q(WB_RegWrite), .en(halt1));  // open: Qn, preset, reset
  Register #(.width(5), .trigger("rising"), .Select("low")) register_4 (
    .D(W), .en(halt1), .Q(W_p4), .clk(CLK));  // open: clr
  Register #(.width(32), .trigger("rising"), .Select("low")) register_5 (
    .D(MEM_R2), .en(halt1), .Q(WB_R2), .clk(CLK));  // open: clr
  Register #(.width(2), .trigger("rising"), .Select("low")) register_6 (
    .D(Addr1___0), .en(halt1), .Q(WB_Addr1___0), .clk(CLK));  // open: clr

  // Notes on the sheet:
  //   输入
  //   输出
endmodule

// 源寄存器使用情况
module \源寄存器使用情况  (
  input  [5:0] OP,
  input  [5:0] Func,
  output R1_Used,
  output R2_Used
);

  wire and_1_out, and_2_out, and_3_out, and_4_out, and_5_out, and_6_out, and_7_out, and_8_out, and_9_out,
       and_10_out, and_11_out, and_12_out, and_13_out, and_14_out, and_15_out, and_16_out, and_17_out,
       and_18_out, and_19_out, and_20_out, and_21_out, and_22_out, and_23_out, and_24_out, and_25_out,
       and_26_out, and_27_out, and_28_out, and_29_out, and_30_out, and_31_out, and_32_out, and_33_out,
       and_34_out, and_35_out, and_36_out, and_37_out, and_38_out, and_39_out, and_40_out, and_41_out,
       not_1_out, not_2_out, not_3_out, not_4_out, not_5_out, not_6_out, not_7_out, not_8_out, not_9_out,
       not_10_out, not_11_out, not_12_out, not_13_out, not_14_out, not_15_out, not_16_out, not_17_out,
       not_18_out, not_19_out, not_20_out, not_21_out, not_22_out, not_23_out, not_24_out, not_25_out,
       not_26_out, not_27_out, not_28_out, not_29_out, not_30_out, not_31_out, not_32_out, not_33_out,
       not_34_out, not_35_out, not_36_out, not_37_out, not_38_out, not_39_out, not_40_out, not_41_out,
       not_42_out, not_43_out, not_44_out, not_45_out, not_46_out, not_47_out, not_48_out, not_49_out,
       not_50_out, not_51_out, not_52_out, not_53_out, not_54_out, not_55_out, not_56_out, not_57_out,
       not_58_out, not_59_out, not_60_out, not_61_out, not_62_out, not_63_out, not_64_out, not_65_out,
       not_66_out, not_67_out, not_68_out, not_69_out, not_70_out, not_71_out, not_72_out, not_73_out,
       not_74_out, not_75_out, not_76_out, not_77_out, not_78_out, not_79_out, not_80_out, not_81_out,
       not_82_out, not_83_out, not_84_out, not_85_out, not_86_out, not_87_out, not_88_out, not_89_out,
       not_90_out, not_91_out, not_92_out, not_93_out, not_94_out, not_95_out, not_96_out, not_97_out,
       not_98_out, not_99_out, not_100_out, not_101_out, not_102_out, not_103_out, not_104_out, not_105_out,
       not_106_out, not_107_out, not_108_out, not_109_out, not_110_out, not_111_out, not_112_out,
       not_113_out, not_114_out, not_115_out, not_116_out, not_117_out, not_118_out, not_119_out,
       not_120_out, not_121_out, not_122_out, not_123_out, not_124_out, not_125_out, not_126_out,
       not_127_out, not_128_out, not_129_out, not_130_out, not_131_out, not_132_out, not_133_out,
       not_134_out, not_135_out, not_136_out, not_137_out, not_138_out, not_139_out, not_140_out,
       not_141_out, not_142_out, not_143_out, not_144_out, not_145_out, not_146_out, not_147_out,
       not_148_out, not_149_out, not_150_out, not_151_out, not_152_out, not_153_out, not_154_out,
       not_155_out, not_156_out, not_157_out, not_158_out, not_159_out, not_160_out, not_161_out,
       not_162_out, not_163_out, not_164_out, not_165_out, not_166_out, not_167_out, not_168_out,
       not_169_out, not_170_out, not_171_out, not_172_out, not_173_out, not_174_out, not_175_out,
       not_176_out, not_177_out, not_178_out, not_179_out, not_180_out, not_181_out, not_182_out,
       not_183_out, not_184_out, not_185_out, not_186_out, not_187_out, not_188_out, not_189_out,
       not_190_out, not_191_out, not_192_out, not_193_out, not_194_out, not_195_out, not_196_out,
       not_197_out, not_198_out, not_199_out, not_200_out, not_201_out, not_202_out, not_203_out,
       not_204_out, not_205_out, not_206_out, not_207_out, not_208_out, not_209_out, not_210_out,
       not_211_out, not_212_out, not_213_out, not_214_out, not_215_out, not_216_out, not_217_out,
       not_218_out, not_219_out, not_220_out, not_221_out, not_222_out, not_223_out, not_224_out,
       not_225_out, not_226_out, not_227_out, not_228_out, not_229_out, not_230_out, not_231_out,
       not_232_out, not_233_out, not_234_out, not_235_out, not_236_out, not_237_out, not_238_out,
       not_239_out, not_240_out, not_241_out, not_242_out, not_243_out, not_244_out, not_245_out,
       not_246_out, not_247_out, not_248_out, not_249_out, not_250_out, not_251_out, not_252_out,
       not_253_out, not_254_out, not_255_out, not_256_out, not_257_out, not_258_out, not_259_out,
       not_260_out, not_261_out, not_262_out, not_263_out, not_264_out, not_265_out, not_266_out,
       not_267_out, not_268_out, not_269_out, not_270_out, not_271_out, not_272_out, not_273_out,
       not_274_out, not_275_out, not_276_out, not_277_out, not_278_out, not_279_out, not_280_out,
       not_281_out, not_282_out, not_283_out, not_284_out, not_285_out, not_286_out, not_287_out,
       not_288_out, not_289_out, not_290_out, not_291_out, not_292_out, not_293_out, not_294_out,
       not_295_out, not_296_out, not_297_out, not_298_out, not_299_out, not_300_out, not_301_out,
       not_302_out, not_303_out, not_304_out, not_305_out, not_306_out, not_307_out, not_308_out,
       not_309_out, not_310_out, not_311_out, not_312_out, not_313_out, not_314_out, not_315_out,
       not_316_out, not_317_out, not_318_out;

  not not_1 (not_1_out, OP[5]);
  not not_2 (not_2_out, OP[4]);
  not not_3 (not_3_out, OP[3]);
  not not_4 (not_4_out, OP[2]);
  not not_5 (not_5_out, OP[1]);
  not not_6 (not_6_out, OP[0]);
  not not_7 (not_7_out, Func[5]);
  not not_8 (not_8_out, Func[4]);
  not not_9 (not_9_out, Func[3]);
  not not_10 (not_10_out, Func[2]);
  not not_11 (not_11_out, Func[1]);
  not not_12 (not_12_out, Func[0]);
  not not_13 (not_13_out, OP[5]);
  not not_14 (not_14_out, OP[4]);
  not not_15 (not_15_out, OP[3]);
  not not_16 (not_16_out, OP[2]);
  not not_17 (not_17_out, OP[1]);
  not not_18 (not_18_out, OP[0]);
  not not_19 (not_19_out, Func[5]);
  not not_20 (not_20_out, Func[4]);
  not not_21 (not_21_out, Func[3]);
  not not_22 (not_22_out, Func[2]);
  not not_23 (not_23_out, OP[5]);
  not not_24 (not_24_out, OP[4]);
  not not_25 (not_25_out, OP[3]);
  not not_26 (not_26_out, OP[2]);
  not not_27 (not_27_out, OP[1]);
  not not_28 (not_28_out, OP[0]);
  not not_29 (not_29_out, Func[5]);
  not not_30 (not_30_out, Func[4]);
  not not_31 (not_31_out, Func[3]);
  not not_32 (not_32_out, Func[2]);
  not not_33 (not_33_out, Func[0]);
  not not_34 (not_34_out, OP[5]);
  not not_35 (not_35_out, OP[4]);
  not not_36 (not_36_out, OP[3]);
  not not_37 (not_37_out, OP[2]);
  not not_38 (not_38_out, OP[1]);
  not not_39 (not_39_out, OP[0]);
  not not_40 (not_40_out, Func[4]);
  not not_41 (not_41_out, Func[3]);
  not not_42 (not_42_out, Func[2]);
  not not_43 (not_43_out, Func[1]);
  not not_44 (not_44_out, Func[0]);
  not not_45 (not_45_out, OP[5]);
  not not_46 (not_46_out, OP[4]);
  not not_47 (not_47_out, OP[3]);
  not not_48 (not_48_out, OP[2]);
  not not_49 (not_49_out, OP[1]);
  not not_50 (not_50_out, OP[0]);
  not not_51 (not_51_out, Func[4]);
  not not_52 (not_52_out, Func[3]);
  not not_53 (not_53_out, Func[2]);
  not not_54 (not_54_out, Func[1]);
  not not_55 (not_55_out, OP[5]);
  not not_56 (not_56_out, OP[4]);
  not not_57 (not_57_out, OP[3]);
  not not_58 (not_58_out, OP[2]);
  not not_59 (not_59_out, OP[1]);
  not not_60 (not_60_out, OP[0]);
  not not_61 (not_61_out, Func[4]);
  not not_62 (not_62_out, Func[3]);
  not not_63 (not_63_out, Func[2]);
  not not_64 (not_64_out, Func[0]);
  not not_65 (not_65_out, OP[5]);
  not not_66 (not_66_out, OP[4]);
  not not_67 (not_67_out, OP[3]);
  not not_68 (not_68_out, OP[2]);
  not not_69 (not_69_out, OP[1]);
  not not_70 (not_70_out, OP[0]);
  not not_71 (not_71_out, Func[4]);
  not not_72 (not_72_out, Func[3]);
  not not_73 (not_73_out, Func[1]);
  not not_74 (not_74_out, Func[0]);
  not not_75 (not_75_out, OP[5]);
  not not_76 (not_76_out, OP[4]);
  not not_77 (not_77_out, OP[3]);
  not not_78 (not_78_out, OP[2]);
  not not_79 (not_79_out, OP[1]);
  not not_80 (not_80_out, OP[0]);
  not not_81 (not_81_out, Func[4]);
  not not_82 (not_82_out, Func[3]);
  not not_83 (not_83_out, Func[1]);
  not not_84 (not_84_out, OP[5]);
  not not_85 (not_85_out, OP[4]);
  not not_86 (not_86_out, OP[3]);
  not not_87 (not_87_out, OP[2]);
  not not_88 (not_88_out, OP[1]);
  not not_89 (not_89_out, OP[0]);
  not not_90 (not_90_out, Func[4]);
  not not_91 (not_91_out, Func[3]);
  not not_92 (not_92_out, OP[5]);
  not not_93 (not_93_out, OP[4]);
  not not_94 (not_94_out, OP[3]);
  not not_95 (not_95_out, OP[2]);
  not not_96 (not_96_out, OP[1]);
  not not_97 (not_97_out, OP[0]);
  not not_98 (not_98_out, Func[4]);
  not not_99 (not_99_out, Func[2]);
  not not_100 (not_100_out, Func[0]);
  not not_101 (not_101_out, OP[5]);
  not not_102 (not_102_out, OP[4]);
  not not_103 (not_103_out, OP[3]);
  not not_104 (not_104_out, OP[2]);
  not not_105 (not_105_out, OP[1]);
  not not_106 (not_106_out, OP[0]);
  not not_107 (not_107_out, Func[4]);
  not not_108 (not_108_out, Func[2]);
  not not_109 (not_109_out, OP[5]);
  not not_110 (not_110_out, OP[4]);
  not not_111 (not_111_out, OP[3]);
  not not_112 (not_112_out, OP[2]);
  not not_113 (not_113_out, OP[1]);
  not not_114 (not_114_out, OP[0]);
  not not_115 (not_115_out, Func[5]);
  not not_116 (not_116_out, Func[4]);
  not not_117 (not_117_out, Func[2]);
  not not_118 (not_118_out, Func[1]);
  not not_119 (not_119_out, Func[0]);
  not not_120 (not_120_out, OP[5]);
  not not_121 (not_121_out, OP[4]);
  not not_122 (not_122_out, OP[3]);
  not not_123 (not_123_out, OP[2]);
  not not_124 (not_124_out, OP[1]);
  not not_125 (not_125_out, OP[0]);
  not not_126 (not_126_out, Func[5]);
  not not_127 (not_127_out, Func[4]);
  not not_128 (not_128_out, Func[3]);
  not not_129 (not_129_out, OP[5]);
  not not_130 (not_130_out, OP[4]);
  not not_131 (not_131_out, OP[3]);
  not not_132 (not_132_out, OP[2]);
  not not_133 (not_133_out, OP[1]);
  not not_134 (not_134_out, OP[0]);
  not not_135 (not_135_out, Func[4]);
  not not_136 (not_136_out, Func[3]);
  not not_137 (not_137_out, Func[0]);
  not not_138 (not_138_out, OP[5]);
  not not_139 (not_139_out, OP[4]);
  not not_140 (not_140_out, OP[3]);
  not not_141 (not_141_out, OP[2]);
  not not_142 (not_142_out, OP[1]);
  not not_143 (not_143_out, OP[0]);
  not not_144 (not_144_out, Func[5]);
  not not_145 (not_145_out, Func[4]);
  not not_146 (not_146_out, Func[3]);
  not not_147 (not_147_out, Func[2]);
  not not_148 (not_148_out, Func[1]);
  not not_149 (not_149_out, Func[0]);
  not not_150 (not_150_out, OP[5]);
  not not_151 (not_151_out, OP[4]);
  not not_152 (not_152_out, OP[3]);
  not not_153 (not_153_out, OP[2]);
  not not_154 (not_154_out, OP[1]);
  not not_155 (not_155_out, OP[0]);
  not not_156 (not_156_out, Func[5]);
  not not_157 (not_157_out, Func[4]);
  not not_158 (not_158_out, Func[3]);
  not not_159 (not_159_out, Func[2]);
  not not_160 (not_160_out, OP[5]);
  not not_161 (not_161_out, OP[4]);
  not not_162 (not_162_out, OP[3]);
  not not_163 (not_163_out, OP[2]);
  not not_164 (not_164_out, OP[1]);
  not not_165 (not_165_out, OP[0]);
  not not_166 (not_166_out, Func[5]);
  not not_167 (not_167_out, Func[4]);
  not not_168 (not_168_out, Func[3]);
  not not_169 (not_169_out, Func[2]);
  not not_170 (not_170_out, Func[0]);
  not not_171 (not_171_out, OP[5]);
  not not_172 (not_172_out, OP[4]);
  not not_173 (not_173_out, OP[3]);
  not not_174 (not_174_out, OP[2]);
  not not_175 (not_175_out, OP[1]);
  not not_176 (not_176_out, OP[0]);
  not not_177 (not_177_out, Func[4]);
  not not_178 (not_178_out, Func[3]);
  not not_179 (not_179_out, Func[2]);
  not not_180 (not_180_out, Func[1]);
  not not_181 (not_181_out, Func[0]);
  not not_182 (not_182_out, OP[5]);
  not not_183 (not_183_out, OP[4]);
  not not_184 (not_184_out, OP[3]);
  not not_185 (not_185_out, OP[2]);
  not not_186 (not_186_out, OP[1]);
  not not_187 (not_187_out, OP[0]);
  not not_188 (not_188_out, Func[4]);
  not not_189 (not_189_out, Func[3]);
  not not_190 (not_190_out, Func[2]);
  not not_191 (not_191_out, Func[1]);
  not not_192 (not_192_out, OP[5]);
  not not_193 (not_193_out, OP[4]);
  not not_194 (not_194_out, OP[3]);
  not not_195 (not_195_out, OP[2]);
  not not_196 (not_196_out, OP[1]);
  not not_197 (not_197_out, OP[0]);
  not not_198 (not_198_out, Func[4]);
  not not_199 (not_199_out, Func[3]);
  not not_200 (not_200_out, Func[2]);
  not not_201 (not_201_out, Func[0]);
  not not_202 (not_202_out, OP[5]);
  not not_203 (not_203_out, OP[4]);
  not not_204 (not_204_out, OP[3]);
  not not_205 (not_205_out, OP[2]);
  not not_206 (not_206_out, OP[1]);
  not not_207 (not_207_out, OP[0]);
  not not_208 (not_208_out, Func[4]);
  not not_209 (not_209_out, Func[3]);
  not not_210 (not_210_out, Func[1]);
  not not_211 (not_211_out, Func[0]);
  not not_212 (not_212_out, OP[5]);
  not not_213 (not_213_out, OP[4]);
  not not_214 (not_214_out, OP[3]);
  not not_215 (not_215_out, OP[2]);
  not not_216 (not_216_out, OP[1]);
  not not_217 (not_217_out, OP[0]);
  not not_218 (not_218_out, Func[4]);
  not not_219 (not_219_out, Func[3]);
  not not_220 (not_220_out, Func[1]);
  not not_221 (not_221_out, OP[5]);
  not not_222 (not_222_out, OP[4]);
  not not_223 (not_223_out, OP[3]);
  not not_224 (not_224_out, OP[2]);
  not not_225 (not_225_out, OP[1]);
  not not_226 (not_226_out, OP[0]);
  not not_227 (not_227_out, Func[4]);
  not not_228 (not_228_out, Func[3]);
  not not_229 (not_229_out, OP[5]);
  not not_230 (not_230_out, OP[4]);
  not not_231 (not_231_out, OP[3]);
  not not_232 (not_232_out, OP[2]);
  not not_233 (not_233_out, OP[1]);
  not not_234 (not_234_out, OP[0]);
  not not_235 (not_235_out, Func[4]);
  not not_236 (not_236_out, Func[2]);
  not not_237 (not_237_out, Func[0]);
  not not_238 (not_238_out, OP[5]);
  not not_239 (not_239_out, OP[4]);
  not not_240 (not_240_out, OP[3]);
  not not_241 (not_241_out, OP[2]);
  not not_242 (not_242_out, OP[1]);
  not not_243 (not_243_out, OP[0]);
  not not_244 (not_244_out, Func[4]);
  not not_245 (not_245_out, Func[2]);
  not not_246 (not_246_out, OP[5]);
  not not_247 (not_247_out, OP[4]);
  not not_248 (not_248_out, OP[3]);
  not not_249 (not_249_out, OP[2]);
  not not_250 (not_250_out, OP[1]);
  not not_251 (not_251_out, OP[0]);
  not not_252 (not_252_out, Func[5]);
  not not_253 (not_253_out, Func[4]);
  not not_254 (not_254_out, Func[3]);
  not not_255 (not_255_out, OP[5]);
  not not_256 (not_256_out, OP[4]);
  not not_257 (not_257_out, OP[3]);
  not not_258 (not_258_out, OP[2]);
  not not_259 (not_259_out, OP[1]);
  not not_260 (not_260_out, OP[0]);
  not not_261 (not_261_out, Func[4]);
  not not_262 (not_262_out, Func[3]);
  not not_263 (not_263_out, Func[0]);
  not not_264 (not_264_out, OP[5]);
  not not_265 (not_265_out, OP[4]);
  not not_266 (not_266_out, OP[3]);
  not not_267 (not_267_out, OP[1]);
  not not_268 (not_268_out, OP[0]);
  not not_269 (not_269_out, OP[5]);
  not not_270 (not_270_out, OP[4]);
  not not_271 (not_271_out, OP[3]);
  not not_272 (not_272_out, OP[1]);
  not not_273 (not_273_out, OP[5]);
  not not_274 (not_274_out, OP[4]);
  not not_275 (not_275_out, OP[2]);
  not not_276 (not_276_out, OP[1]);
  not not_277 (not_277_out, OP[0]);
  not not_278 (not_278_out, OP[5]);
  not not_279 (not_279_out, OP[4]);
  not not_280 (not_280_out, OP[1]);
  not not_281 (not_281_out, OP[0]);
  not not_282 (not_282_out, OP[5]);
  not not_283 (not_283_out, OP[4]);
  not not_284 (not_284_out, OP[2]);
  not not_285 (not_285_out, OP[1]);
  not not_286 (not_286_out, OP[5]);
  not not_287 (not_287_out, OP[4]);
  not not_288 (not_288_out, OP[2]);
  not not_289 (not_289_out, OP[0]);
  not not_290 (not_290_out, OP[5]);
  not not_291 (not_291_out, OP[4]);
  not not_292 (not_292_out, OP[1]);
  not not_293 (not_293_out, OP[4]);
  not not_294 (not_294_out, OP[3]);
  not not_295 (not_295_out, OP[2]);
  not not_296 (not_296_out, OP[4]);
  not not_297 (not_297_out, OP[2]);
  not not_298 (not_298_out, OP[4]);
  not not_299 (not_299_out, OP[3]);
  not not_300 (not_300_out, OP[2]);
  not not_301 (not_301_out, OP[1]);
  not not_302 (not_302_out, OP[0]);
  not not_303 (not_303_out, OP[5]);
  not not_304 (not_304_out, OP[4]);
  not not_305 (not_305_out, OP[3]);
  not not_306 (not_306_out, OP[2]);
  not not_307 (not_307_out, OP[1]);
  not not_308 (not_308_out, OP[5]);
  not not_309 (not_309_out, OP[4]);
  not not_310 (not_310_out, OP[3]);
  not not_311 (not_311_out, OP[1]);
  not not_312 (not_312_out, OP[0]);
  not not_313 (not_313_out, OP[5]);
  not not_314 (not_314_out, OP[4]);
  not not_315 (not_315_out, OP[3]);
  not not_316 (not_316_out, OP[1]);
  not not_317 (not_317_out, OP[4]);
  not not_318 (not_318_out, OP[2]);
  and and_1 (and_1_out, not_1_out, not_2_out, not_3_out, not_4_out, not_5_out, not_6_out, not_7_out, not_8_out, not_9_out, not_10_out, not_11_out, not_12_out);
  and and_2 (and_2_out, not_13_out, not_14_out, not_15_out, not_16_out, not_17_out, not_18_out, not_19_out, not_20_out, not_21_out, not_22_out, Func[1], Func[0]);
  and and_3 (and_3_out, not_23_out, not_24_out, not_25_out, not_26_out, not_27_out, not_28_out, not_29_out, not_30_out, not_31_out, not_32_out, Func[1], not_33_out);
  and and_4 (and_4_out, not_34_out, not_35_out, not_36_out, not_37_out, not_38_out, not_39_out, Func[5], not_40_out, not_41_out, not_42_out, not_43_out, not_44_out);
  and and_5 (and_5_out, not_45_out, not_46_out, not_47_out, not_48_out, not_49_out, not_50_out, Func[5], not_51_out, not_52_out, not_53_out, not_54_out, Func[0]);
  and and_6 (and_6_out, not_55_out, not_56_out, not_57_out, not_58_out, not_59_out, not_60_out, Func[5], not_61_out, not_62_out, not_63_out, Func[1], not_64_out);
  and and_7 (and_7_out, not_65_out, not_66_out, not_67_out, not_68_out, not_69_out, not_70_out, Func[5], not_71_out, not_72_out, Func[2], not_73_out, not_74_out);
  and and_8 (and_8_out, not_75_out, not_76_out, not_77_out, not_78_out, not_79_out, not_80_out, Func[5], not_81_out, not_82_out, Func[2], not_83_out, Func[0]);
  and and_9 (and_9_out, not_84_out, not_85_out, not_86_out, not_87_out, not_88_out, not_89_out, Func[5], not_90_out, not_91_out, Func[2], Func[1], Func[0]);
  and and_10 (and_10_out, not_92_out, not_93_out, not_94_out, not_95_out, not_96_out, not_97_out, Func[5], not_98_out, Func[3], not_99_out, Func[1], not_100_out);
  and and_11 (and_11_out, not_101_out, not_102_out, not_103_out, not_104_out, not_105_out, not_106_out, Func[5], not_107_out, Func[3], not_108_out, Func[1], Func[0]);
  and and_12 (and_12_out, not_109_out, not_110_out, not_111_out, not_112_out, not_113_out, not_114_out, not_115_out, not_116_out, Func[3], not_117_out, not_118_out, not_119_out);
  and and_13 (and_13_out, not_264_out, not_265_out, not_266_out, OP[2], not_267_out, not_268_out);
  and and_14 (and_14_out, not_269_out, not_270_out, not_271_out, OP[2], not_272_out, OP[0]);
  and and_15 (and_15_out, not_273_out, not_274_out, OP[3], not_275_out, not_276_out, not_277_out);
  and and_16 (and_16_out, not_278_out, not_279_out, OP[3], OP[2], not_280_out, not_281_out);
  and and_17 (and_17_out, not_282_out, not_283_out, OP[3], not_284_out, not_285_out, OP[0]);
  and and_18 (and_18_out, not_286_out, not_287_out, OP[3], not_288_out, OP[1], not_289_out);
  and and_19 (and_19_out, not_290_out, not_291_out, OP[3], OP[2], not_292_out, OP[0]);
  and and_20 (and_20_out, OP[5], not_293_out, not_294_out, not_295_out, OP[1], OP[0]);
  and and_21 (and_21_out, OP[5], not_296_out, OP[3], not_297_out, OP[1], OP[0]);
  and and_22 (and_22_out, not_120_out, not_121_out, not_122_out, not_123_out, not_124_out, not_125_out, not_126_out, not_127_out, not_128_out, Func[2], Func[1], Func[0]);
  and and_23 (and_23_out, not_129_out, not_130_out, not_131_out, not_132_out, not_133_out, not_134_out, Func[5], not_135_out, not_136_out, Func[2], Func[1], not_137_out);
  and and_24 (and_24_out, OP[5], not_298_out, not_299_out, not_300_out, not_301_out, not_302_out);
  and and_25 (and_25_out, not_303_out, not_304_out, not_305_out, not_306_out, not_307_out, OP[0]);
  and and_26 (and_26_out, not_138_out, not_139_out, not_140_out, not_141_out, not_142_out, not_143_out, not_144_out, not_145_out, not_146_out, not_147_out, not_148_out, not_149_out);
  and and_27 (and_27_out, not_150_out, not_151_out, not_152_out, not_153_out, not_154_out, not_155_out, not_156_out, not_157_out, not_158_out, not_159_out, Func[1], Func[0]);
  and and_28 (and_28_out, not_160_out, not_161_out, not_162_out, not_163_out, not_164_out, not_165_out, not_166_out, not_167_out, not_168_out, not_169_out, Func[1], not_170_out);
  and and_29 (and_29_out, not_171_out, not_172_out, not_173_out, not_174_out, not_175_out, not_176_out, Func[5], not_177_out, not_178_out, not_179_out, not_180_out, not_181_out);
  and and_30 (and_30_out, not_182_out, not_183_out, not_184_out, not_185_out, not_186_out, not_187_out, Func[5], not_188_out, not_189_out, not_190_out, not_191_out, Func[0]);
  and and_31 (and_31_out, not_192_out, not_193_out, not_194_out, not_195_out, not_196_out, not_197_out, Func[5], not_198_out, not_199_out, not_200_out, Func[1], not_201_out);
  and and_32 (and_32_out, not_202_out, not_203_out, not_204_out, not_205_out, not_206_out, not_207_out, Func[5], not_208_out, not_209_out, Func[2], not_210_out, not_211_out);
  and and_33 (and_33_out, not_212_out, not_213_out, not_214_out, not_215_out, not_216_out, not_217_out, Func[5], not_218_out, not_219_out, Func[2], not_220_out, Func[0]);
  and and_34 (and_34_out, not_221_out, not_222_out, not_223_out, not_224_out, not_225_out, not_226_out, Func[5], not_227_out, not_228_out, Func[2], Func[1], Func[0]);
  and and_35 (and_35_out, not_229_out, not_230_out, not_231_out, not_232_out, not_233_out, not_234_out, Func[5], not_235_out, Func[3], not_236_out, Func[1], not_237_out);
  and and_36 (and_36_out, not_238_out, not_239_out, not_240_out, not_241_out, not_242_out, not_243_out, Func[5], not_244_out, Func[3], not_245_out, Func[1], Func[0]);
  and and_37 (and_37_out, not_308_out, not_309_out, not_310_out, OP[2], not_311_out, not_312_out);
  and and_38 (and_38_out, not_313_out, not_314_out, not_315_out, OP[2], not_316_out, OP[0]);
  and and_39 (and_39_out, OP[5], not_317_out, OP[3], not_318_out, OP[1], OP[0]);
  and and_40 (and_40_out, not_246_out, not_247_out, not_248_out, not_249_out, not_250_out, not_251_out, not_252_out, not_253_out, not_254_out, Func[2], Func[1], Func[0]);
  and and_41 (and_41_out, not_255_out, not_256_out, not_257_out, not_258_out, not_259_out, not_260_out, Func[5], not_261_out, not_262_out, Func[2], Func[1], not_263_out);
  or or_1 (R2_Used, and_26_out, and_27_out, and_28_out, and_29_out, and_30_out, and_31_out, and_32_out, and_33_out, and_34_out, and_35_out, and_36_out, and_37_out, and_38_out, and_39_out, and_40_out, and_41_out);
  or or_2 (R1_Used, and_1_out, and_2_out, and_3_out, and_4_out, and_5_out, and_6_out, and_7_out, and_8_out, and_9_out, and_10_out, and_11_out, and_12_out, and_13_out, and_14_out, and_15_out, and_16_out, and_17_out, and_18_out, and_19_out, and_20_out, and_21_out, and_22_out, and_23_out, and_24_out, and_25_out);
endmodule

module \数据相关检测逻辑  (
  input  [4:0] R1_num,
  input  [5:0] OP,
  input  [4:0] EX_WriteReg_num,
  input  EX_RegWrite,
  input  Syscall,
  input  [4:0] R2_num,
  input  [5:0] Func,
  input  [4:0] MEM_WriteReg_num,
  input  MEM_RegWrite,
  output halt,
  output EX_nop,
  output MEM_nop
);

  wire and_1_out, and_2_out, and_3_out, and_4_out, and_5_out, and_6_out, comparator_1_eq, comparator_2_eq,
       comparator_3_eq, comparator_4_eq, comparator_5_eq, comparator_6_eq, comparator_7_eq, comparator_8_eq,
       or_1_out, or_2_out, or_3_out, or_4_out, or_5_out, or_6_out, or_7_out, R1_Used, R2_Used;

  \源寄存器使用情况  \u_源寄存器使用情况_1  (.R1_Used(R1_Used), .R2_Used(R2_Used), .OP(OP), .Func(Func));
  Comparator #(.width(5), .mode("twosComplement")) comparator_1 (
    .a(5'b00010), .b(EX_WriteReg_num), .eq(comparator_1_eq));  // open: gt, lt
  Comparator #(.width(5), .mode("twosComplement")) comparator_2 (
    .a(5'b00100), .b(EX_WriteReg_num), .eq(comparator_2_eq));  // open: gt, lt
  Comparator #(.width(5), .mode("twosComplement")) comparator_3 (
    .a(5'b00100), .b(MEM_WriteReg_num), .eq(comparator_3_eq), .lt(comparator_3_eq));  // open: gt
  Comparator #(.width(5), .mode("twosComplement")) comparator_4 (
    .a(5'b00010), .b(MEM_WriteReg_num), .eq(comparator_4_eq));  // open: gt, lt
  or or_1 (or_1_out, comparator_1_eq, comparator_2_eq);
  or or_2 (or_2_out, comparator_3_eq, comparator_4_eq);
  and and_1 (and_1_out, or_1_out, Syscall);
  and and_2 (and_2_out, or_2_out, Syscall);
  Comparator #(.width(5), .mode("twosComplement")) comparator_5 (
    .a(EX_WriteReg_num), .b(R1_num), .eq(comparator_5_eq));  // open: gt, lt
  Comparator #(.width(5), .mode("twosComplement")) comparator_6 (
    .a(EX_WriteReg_num), .b(R2_num), .eq(comparator_6_eq));  // open: gt, lt
  Comparator #(.width(5), .mode("twosComplement")) comparator_7 (
    .a(R2_num), .b(MEM_WriteReg_num), .eq(comparator_7_eq));  // open: gt, lt
  Comparator #(.width(5), .mode("twosComplement")) comparator_8 (
    .a(R1_num), .b(MEM_WriteReg_num), .eq(comparator_8_eq));  // open: gt, lt
  or or_3 (or_3_out, EX_WriteReg_num[0], EX_WriteReg_num[1], EX_WriteReg_num[2], EX_WriteReg_num[3], EX_WriteReg_num[4]);
  and and_3 (and_3_out, comparator_5_eq, R1_Used);
  or or_4 (or_4_out, and_3_out, and_1_out, and_4_out);
  and and_4 (and_4_out, R2_Used, comparator_6_eq);
  and and_5 (and_5_out, comparator_7_eq, R2_Used);
  or or_5 (or_5_out, and_5_out, and_2_out, and_6_out);
  and and_6 (and_6_out, R1_Used, comparator_8_eq);
  or or_6 (or_6_out, MEM_WriteReg_num[0], MEM_WriteReg_num[1], MEM_WriteReg_num[2], MEM_WriteReg_num[3], MEM_WriteReg_num[4]);
  and and_7 (EX_nop, EX_RegWrite, or_3_out, or_4_out);
  and and_8 (MEM_nop, or_5_out, or_6_out, MEM_RegWrite);
  not not_1 (halt, or_7_out);
  or or_7 (or_7_out, EX_nop, MEM_nop);
endmodule

module \重定向逻辑  (
  input  [4:0] R1_num,
  input  [5:0] OP,
  input  [4:0] EX_WriteReg_num,
  input  EX_RegWrite,
  input  EX_MemToReg,
  input  Syscall,
  input  [4:0] R2_num,
  input  [5:0] Func,
  input  [4:0] MEM_WriteReg_num,
  input  MEM_RegWrite,
  input  MEM_MemToReg,
  output [1:0] R1_Forward,
  output EX_nop,
  output halt,
  output [1:0] R2_Forward,
  output MEM_nop
);

  wire and_1_out, and_2_out, and_3_out, and_4_out, and_5_out, and_6_out, and_7_out, and_8_out, and_9_out,
       and_10_out, and_11_out, and_12_out, and_13_out, and_14_out, and_15_out, and_16_out, and_17_out,
       and_18_out, and_19_out, and_20_out, and_21_out, comparator_1_eq, comparator_2_eq, comparator_3_eq,
       comparator_4_eq, comparator_5_eq, comparator_6_eq, comparator_7_eq, comparator_8_eq, comparator_9_eq,
       comparator_10_eq, comparator_11_eq, comparator_12_eq, comparator_13_eq, comparator_14_eq,
       comparator_15_eq, comparator_16_eq, or_1_out, or_2_out, or_3_out, or_4_out, or_5_out, or_6_out,
       or_7_out, or_8_out, or_9_out, or_10_out, or_11_out, or_12_out, or_13_out, or_14_out, or_15_out,
       R1_Used, R2_Used;
  wire [1:0] multiplexer_2_out, multiplexer_3_out, multiplexer_5_out, multiplexer_6_out;

  \源寄存器使用情况  \u_源寄存器使用情况_1  (.R1_Used(R1_Used), .R2_Used(R2_Used), .OP(OP), .Func(Func));
  Comparator #(.width(5), .mode("twosComplement")) comparator_1 (
    .a(5'b00010), .b(EX_WriteReg_num), .eq(comparator_1_eq));  // open: gt, lt
  Comparator #(.width(5), .mode("twosComplement")) comparator_2 (
    .a(EX_WriteReg_num), .b(R1_num), .eq(comparator_2_eq));  // open: gt, lt
  and and_1 (and_1_out, comparator_2_eq, R1_Used);
  and and_2 (and_2_out, comparator_1_eq, Syscall);
  Comparator #(.width(5), .mode("twosComplement")) comparator_3 (
    .a(MEM_WriteReg_num), .b(R1_num), .eq(comparator_3_eq));  // open: gt, lt
  Comparator #(.width(5), .mode("twosComplement")) comparator_4 (
    .a(5'b00010), .b(MEM_WriteReg_num), .eq(comparator_4_eq));  // open: gt, lt
  Comparator #(.width(5), .mode("twosComplement")) comparator_5 (
    .a(MEM_WriteReg_num), .b(R1_num), .eq(comparator_5_eq));  // open: gt, lt
  Comparator #(.width(5), .mode("twosComplement")) comparator_6 (
    .a(5'b00010), .b(MEM_WriteReg_num), .eq(comparator_6_eq));  // open: gt, lt
  or or_1 (or_1_out, and_1_out, and_2_out);
  and and_3 (and_3_out, comparator_3_eq, R1_Used);
  and and_4 (and_4_out, comparator_4_eq, Syscall);
  and and_5 (and_5_out, comparator_5_eq, R1_Used);
  and and_6 (and_6_out, comparator_6_eq, Syscall);
  or or_2 (or_2_out, EX_WriteReg_num[0], EX_WriteReg_num[1], EX_WriteReg_num[2], EX_WriteReg_num[3], EX_WriteReg_num[4]);
  or or_3 (or_3_out, MEM_WriteReg_num[0], MEM_WriteReg_num[1], MEM_WriteReg_num[2], MEM_WriteReg_num[3], MEM_WriteReg_num[4]);
  or or_4 (or_4_out, and_3_out, and_4_out);
  or or_5 (or_5_out, MEM_WriteReg_num[0], MEM_WriteReg_num[1], MEM_WriteReg_num[2], MEM_WriteReg_num[3], MEM_WriteReg_num[4]);
  or or_6 (or_6_out, and_5_out, and_6_out);
  and and_7 (and_7_out, EX_RegWrite, or_2_out, or_1_out, ~EX_MemToReg);  // AND_Gate
  and and_8 (and_8_out, MEM_RegWrite, or_3_out, or_4_out, ~MEM_MemToReg);  // AND_Gate
  and and_9 (and_9_out, MEM_RegWrite, or_5_out, or_6_out, MEM_MemToReg);
  Multiplexer #(.select(1), .width(2), .disabled("Z"), .enable("false")) multiplexer_1 (
    .in0(multiplexer_2_out), .in1(2'b01), .out(R1_Forward), .sel(and_7_out));
  Multiplexer #(.select(1), .width(2), .disabled("Z"), .enable("false")) multiplexer_2 (
    .in0(multiplexer_3_out), .in1(2'b10), .out(multiplexer_2_out), .sel(and_8_out));
  Multiplexer #(.select(1), .width(2), .disabled("Z"), .enable("false")) multiplexer_3 (
    .in0(2'b00), .in1(2'b11), .out(multiplexer_3_out), .sel(and_9_out));
  Comparator #(.width(5), .mode("twosComplement")) comparator_7 (
    .a(EX_WriteReg_num), .b(R2_num), .eq(comparator_7_eq));  // open: gt, lt
  Comparator #(.width(5), .mode("twosComplement")) comparator_8 (
    .a(5'b00100), .b(EX_WriteReg_num), .eq(comparator_8_eq));  // open: gt, lt
  and and_10 (and_10_out, comparator_7_eq, R2_Used);
  and and_11 (and_11_out, comparator_8_eq, Syscall);
  Comparator #(.width(5), .mode("twosComplement")) comparator_9 (
    .a(MEM_WriteReg_num), .b(R2_num), .eq(comparator_9_eq));  // open: gt, lt
  and and_12 (and_12_out, comparator_9_eq, R2_Used);
  Comparator #(.width(5), .mode("twosComplement")) comparator_10 (
    .a(5'b00100), .b(MEM_WriteReg_num), .eq(comparator_10_eq));  // open: gt, lt
  and and_13 (and_13_out, comparator_10_eq, Syscall);
  Comparator #(.width(5), .mode("twosComplement")) comparator_11 (
    .a(MEM_WriteReg_num), .b(R2_num), .eq(comparator_11_eq));  // open: gt, lt
  and and_14 (and_14_out, comparator_11_eq, R2_Used);
  Comparator #(.width(5), .mode("twosComplement")) comparator_12 (
    .a(5'b00100), .b(MEM_WriteReg_num), .eq(comparator_12_eq));  // open: gt, lt
  and and_15 (and_15_out, comparator_12_eq, Syscall);
  or or_7 (or_7_out, and_10_out, and_11_out);
  or or_8 (or_8_out, EX_WriteReg_num[0], EX_WriteReg_num[1], EX_WriteReg_num[2], EX_WriteReg_num[3], EX_WriteReg_num[4]);
  or or_9 (or_9_out, MEM_WriteReg_num[0], MEM_WriteReg_num[1], MEM_WriteReg_num[2], MEM_WriteReg_num[3], MEM_WriteReg_num[4]);
  or or_10 (or_10_out, and_12_out, and_13_out);
  or or_11 (or_11_out, MEM_WriteReg_num[0], MEM_WriteReg_num[1], MEM_WriteReg_num[2], MEM_WriteReg_num[3], MEM_WriteReg_num[4]);
  or or_12 (or_12_out, and_14_out, and_15_out);
  and and_16 (and_16_out, EX_RegWrite, or_8_out, or_7_out, ~EX_MemToReg);  // AND_Gate
  and and_17 (and_17_out, MEM_RegWrite, or_9_out, or_10_out, ~MEM_MemToReg);  // AND_Gate
  and and_18 (and_18_out, MEM_RegWrite, or_11_out, or_12_out, MEM_MemToReg);
  Multiplexer #(.select(1), .width(2), .disabled("Z"), .enable("false")) multiplexer_4 (
    .in0(multiplexer_5_out), .in1(2'b01), .out(R2_Forward), .sel(and_16_out));
  Multiplexer #(.select(1), .width(2), .disabled("Z"), .enable("false")) multiplexer_5 (
    .in0(multiplexer_6_out), .in1(2'b10), .out(multiplexer_5_out), .sel(and_17_out));
  Multiplexer #(.select(1), .width(2), .disabled("Z"), .enable("false")) multiplexer_6 (
    .in0(2'b00), .in1(2'b11), .out(multiplexer_6_out), .sel(and_18_out));
  Comparator #(.width(5), .mode("twosComplement")) comparator_13 (
    .a(5'b00010), .b(EX_WriteReg_num), .eq(comparator_13_eq));  // open: gt, lt
  Comparator #(.width(5), .mode("twosComplement")) comparator_14 (
    .a(5'b00100), .b(EX_WriteReg_num), .eq(comparator_14_eq));  // open: gt, lt
  or or_13 (or_13_out, comparator_13_eq, comparator_14_eq);
  and and_19 (and_19_out, or_13_out, Syscall);
  Comparator #(.width(5), .mode("twosComplement")) comparator_15 (
    .a(EX_WriteReg_num), .b(R1_num), .eq(comparator_15_eq));  // open: gt, lt
  and and_20 (and_20_out, comparator_15_eq, R1_Used);
  and and_21 (and_21_out, R2_Used, comparator_16_eq);
  Comparator #(.width(5), .mode("twosComplement")) comparator_16 (
    .a(EX_WriteReg_num), .b(R2_num), .eq(comparator_16_eq));  // open: gt, lt
  or or_14 (or_14_out, EX_WriteReg_num[0], EX_WriteReg_num[1], EX_WriteReg_num[2], EX_WriteReg_num[3], EX_WriteReg_num[4]);
  or or_15 (or_15_out, and_20_out, and_19_out, and_21_out);
  and and_22 (EX_nop, EX_RegWrite, or_14_out, or_15_out, EX_MemToReg);
  not not_1 (halt, EX_nop);

  assign MEM_nop = 1'b0;
endmodule

// 中断电路
module \单级中断总电路  (
  input  IR1,
  input  CLK,
  input  eret,
  input  IR2,
  input  [31:0] PC,
  input  [31:0] next_PC,
  input  IR3,
  output W1,
  output \中断信号 ,
  output W2,
  output [31:0] \断点 ,
  output [1:0] \中断号 ,
  output W3
);

  wire and_1_out, and_2_out, and_3_out, decoder_1_out1, decoder_1_out2, decoder_1_out3, IE_q, IE_qn,
       multiplexer_1_out, not_1_out, priority_encoder_1_en_out, \中断1 , \中断2 , \中断3 ;
  wire [1:0] register_1_q;

  Register #(.width(2), .trigger("rising"), .Select("low")) register_1 (
    .D(\中断号 ), .en(\中断信号 ), .Q(register_1_q), .clk(CLK));  // open: clr
  Decoder #(.select(2), .tristate("false"), .disabled("Z"), .enable("false")) decoder_1 (
    .out1(decoder_1_out1), .out2(decoder_1_out2), .out3(decoder_1_out3), .sel(register_1_q));  // open: out0
  and and_1 (and_1_out, decoder_1_out1, eret);
  and and_2 (and_2_out, decoder_1_out2, eret);
  and and_3 (and_3_out, decoder_1_out3, eret);
  \中断按键参考电路  \u_中断按键参考电路_1  (.\与中断屏蔽位与 (\中断1 ), .\同步清零信号 (and_1_out), .\_1号中断等待指示灯 (W1), .CLK(CLK), .\_1号中断 (IR1));
  \中断按键参考电路  \u_中断按键参考电路_2  (.\与中断屏蔽位与 (\中断2 ), .\同步清零信号 (and_2_out), .\_1号中断等待指示灯 (W2), .CLK(CLK), .\_1号中断 (IR2));
  \中断按键参考电路  \u_中断按键参考电路_3  (.\与中断屏蔽位与 (\中断3 ), .\同步清零信号 (and_3_out), .\_1号中断等待指示灯 (W3), .CLK(CLK), .\_1号中断 (IR3));
  Multiplexer #(.select(1), .width(1), .disabled("Z"), .enable("false")) multiplexer_1 (
    .in0(IE_q), .in1(1'b1), .out(multiplexer_1_out), .sel(\中断信号 ));
  and and_4 (\中断信号 , IE_qn, not_1_out);
  D_Flip_Flop #(.trigger("rising"), .Pre_Clr_Positions("ABOVE_BELOW"), .NegatePresetClear("false"), .enable("false"), .NewFFLayout("false")) IE (
    .clk(CLK), .D(multiplexer_1_out), .Q(IE_q), .Qn(IE_qn), .reset(eret));  // open: preset
  not not_1 (not_1_out, priority_encoder_1_en_out);
  Priority_Encoder #(.select(2), .disabled("Z")) priority_encoder_1 (
    .in1(\中断1 ), .in2(\中断2 ), .in3(\中断3 ), .out(\中断号 ), .en_out(priority_encoder_1_en_out));  // open: in0, gs, en_in
  Register #(.width(32), .trigger("rising"), .Select("low")) EPC (
    .D(next_PC), .en(\中断信号 ), .Q(\断点 ), .clk(CLK));  // open: clr
endmodule

module \单周期MIPS_单级中断  (
  input  IR1,
  input  IR2,
  input  IR3,
  output RegWrite,
  output MemWrite,
  output [31:0] PC,
  output [31:0] IR,
  output [31:0] RDin,
  output [31:0] MDin,
  output [31:0] LedData
);

  wire AluSrcB, and_1_out, and_2_out, and_3_out, and_4_out, Beq, BLTZ, Bne, CLK, comparator_1_eq,
       comparator_2_eq, Equal, eret, Go, halt, IR1_t, IR2_t, IR3_t, IRA, IRB, IRC, JAL, JMP, JR, LB, Less,
       MemToReg, or_1_out, RegDst, SignedExt, Syscall, W1, W2, W3, \中断信号 ;
  wire [1:0] Addr1___0, \中断号 ;
  wire [3:0] AluOP;
  wire [4:0] multiplexer_7_out, multiplexer_8_out, multiplexer_9_out, multiplexer_10_out;
  wire [7:0] multiplexer_14_out, ram_1_data, ram_1_data_2, ram_1_data_3, ram_1_data_4;
  wire [15:0] incrementer_1_p2, \总周期数 ;
  wire [27:0] PC_plus_4;
  wire [31:0] bit_extender_1_out, bit_extender_2_out, bit_extender_3_out, multiplexer_1_out,
       multiplexer_2_out, multiplexer_4_out, multiplexer_5_out, multiplexer_6_out, multiplexer_11_out,
       multiplexer_12_out, multiplexer_13_out, multiplexer_15_out, multiplexer_16_out, next_PC, PCBranch, R1,
       shifter_1_out, \断点 ;
  wire [31:2] mips_alu_1_result;
  wire [31:28] JumpAddr;

  Clock #(.highDuration(1), .lowDuration(1)) clock_1 (.out(CLK));
  Button _1 (.out(IRA));
  Button _2 (.out(IRB));
  Button _3 (.out(IRC));
  Button \u_继续运行  (.out(Go));
  LED #(.active("true")) led_1 (.in(W1));
  LED #(.active("true")) led_2 (.in(W2));
  LED #(.active("true")) led_3 (.in(W3));
  Hex_Digit_Display hex_digit_display_1 (.value(LedData[31:28]));  // open: dp
  Multiplexer #(.select(1), .width(32), .disabled("Z"), .enable("false")) multiplexer_1 (
    .in0({JumpAddr, PC_plus_4}), .in1({JumpAddr, IR[25:0], 2'b00}), .out(multiplexer_1_out), .sel(JMP));
  Hex_Digit_Display hex_digit_display_2 (.value(LedData[27:24]));  // open: dp
  Hex_Digit_Display hex_digit_display_3 (.value(LedData[23:20]));  // open: dp
  Comparator #(.width(32), .mode("twosComplement")) comparator_1 (
    .a(R1), .b(32'h22), .eq(comparator_1_eq));  // open: gt, lt
  nand nand_1 (halt, ~comparator_1_eq, Syscall);  // NAND_Gate
  Multiplexer #(.select(1), .width(32), .disabled("Z"), .enable("false")) multiplexer_2 (
    .in0(multiplexer_1_out), .in1(R1), .out(multiplexer_2_out), .sel(JR));
  and and_1 (and_1_out, Beq, Equal);
  or or_1 (or_1_out, and_1_out, and_2_out, and_3_out);
  and and_2 (and_2_out, BLTZ, Less);
  and and_3 (and_3_out, Bne, ~Equal);  // AND_Gate
  Hex_Digit_Display hex_digit_display_4 (.value(LedData[15:12]));  // open: dp
  Hex_Digit_Display hex_digit_display_5 (.value(LedData[19:16]));  // open: dp
  // Probe on halt
  Multiplexer #(.select(1), .width(32), .disabled("Z"), .enable("false")) multiplexer_3 (
    .in0(multiplexer_2_out), .in1(PCBranch), .out(next_PC), .sel(or_1_out));
  Hex_Digit_Display hex_digit_display_6 (.value(LedData[11:8]));  // open: dp
  Hex_Digit_Display hex_digit_display_7 (.value(LedData[7:4]));  // open: dp
  // Probe on \总周期数 
  Multiplexer #(.select(2), .width(32), .disabled("Z"), .enable("false")) multiplexer_4 (
    .in1(32'h30ac), .in2(32'h3150), .in3(32'h31f4), .out(multiplexer_4_out), .sel(\中断号 ));  // open: in0
  Hex_Digit_Display hex_digit_display_8 (.value(LedData[3:0]));  // open: dp
  Multiplexer #(.select(1), .width(32), .disabled("Z"), .enable("false")) multiplexer_5 (
    .in0(next_PC), .in1(multiplexer_4_out), .out(multiplexer_5_out), .sel(\中断信号 ));
  Multiplexer #(.select(1), .width(32), .disabled("Z"), .enable("false")) multiplexer_6 (
    .in0(multiplexer_5_out), .in1(\断点 ), .out(multiplexer_6_out), .sel(eret));
  or or_2 (IR1_t, IR1, IRA);
  Register #(.width(32), .trigger("rising"), .Select("low")) u_PC (
    .D(multiplexer_6_out), .en(halt), .Q(PC), .clk(CLK));  // open: clr
  or or_3 (IR2_t, IR2, IRB);
  \单周期硬布线控制器  \u_单周期硬布线控制器_1  (
    .Func(IR[5:0]), .OP(IR[31:26]), .ALU_OP(AluOP), .MemToReg(MemToReg), .MemWrite(MemWrite),
    .ALU_SRC(AluSrcB), .RegWrite(RegWrite), .SysCALL(Syscall), .SignedExt(SignedExt), .RegDst(RegDst),
    .JR(JR), .JMP(JMP), .Beq(Beq), .JAL(JAL), .Bne(Bne), .LB(LB), .BLTZ(BLTZ), .eret(eret));
  Adder #(.width(32)) adder_1 (.a(PC), .b(32'h4), .out({JumpAddr, PC_plus_4}));  // open: cin, cout
  // Probe on IR
  ROM #(.addrWidth(10), .dataWidth(32), .Select("high")) rom_1 (.addr(PC[11:2]), .data(IR));
  or or_4 (IR3_t, IR3, IRC);
  Multiplexer #(.select(1), .width(5), .disabled("Z"), .enable("false")) multiplexer_7 (
    .in0(IR[20:16]), .in1(IR[15:11]), .out(multiplexer_7_out), .sel(RegDst));
  Multiplexer #(.select(1), .width(5), .disabled("Z"), .enable("false")) multiplexer_8 (
    .in0(multiplexer_7_out), .in1({5{1'b1}}), .out(multiplexer_8_out), .sel(JAL));
  Comparator #(.width(32), .mode("twosComplement")) comparator_2 (
    .a(R1), .b(32'h22), .eq(comparator_2_eq));  // open: gt, lt
  Multiplexer #(.select(1), .width(5), .disabled("Z"), .enable("false")) multiplexer_9 (
    .in0(IR[25:21]), .in1(5'b00010), .out(multiplexer_9_out), .sel(Syscall));
  Multiplexer #(.select(1), .width(5), .disabled("Z"), .enable("false")) multiplexer_10 (
    .in0(IR[20:16]), .in1(5'b00100), .out(multiplexer_10_out), .sel(Syscall));
  assign bit_extender_1_out = {{16{1'b0}}, IR[15:0]};  // Bit_Extender bit_extender_1
  assign bit_extender_2_out = {{16{IR[15]}}, IR[15:0]};  // Bit_Extender bit_extender_2
  Multiplexer #(.select(1), .width(32), .disabled("Z"), .enable("false")) multiplexer_11 (
    .in0(LedData), .in1(MDin), .out(multiplexer_11_out), .sel(and_4_out));
  and and_4 (and_4_out, comparator_2_eq, Syscall);
  Multiplexer #(.select(1), .width(32), .disabled("Z"), .enable("false")) multiplexer_12 (
    .in0(bit_extender_1_out), .in1(bit_extender_2_out), .out(multiplexer_12_out), .sel(SignedExt));
  // Probe on multiplexer_12_out
  Register #(.width(32), .trigger("rising"), .Select("low")) register_1 (
    .D(multiplexer_11_out), .Q(LedData), .clk(CLK));  // open: en, clr
  MIPS_Regifile mips_regifile_1 (
    .Din(RDin), .Clk(CLK), .R1(R1), .R2(MDin), .WE(RegWrite), .W_num(multiplexer_8_out),
    .R1_num(multiplexer_9_out), .R2_num(multiplexer_10_out));
  Multiplexer #(.select(1), .width(32), .disabled("Z"), .enable("false")) multiplexer_13 (
    .in0(MDin), .in1(multiplexer_12_out), .out(multiplexer_13_out), .sel(AluSrcB));
  Shifter #(.width(32), .shift("ll")) shifter_1 (.in(multiplexer_12_out), .\dist (5'b00010), .out(shifter_1_out));
  MIPS_ALU mips_alu_1 (
    .X(R1), .Y(multiplexer_13_out), .AluOP(AluOP), .Equal(Equal), .Result({mips_alu_1_result, Addr1___0}),
    .shamt(IR[10:6]), .Less(Less));  // open: Result_2
  Adder #(.width(32)) adder_2 (.a(shifter_1_out), .b({JumpAddr, PC_plus_4}), .out(PCBranch));  // open: cin, cout
  Register #(.width(16), .trigger("rising"), .Select("low")) register_2 (
    .D(incrementer_1_p2), .en(halt), .Q(\总周期数 ), .clk(CLK));  // open: clr
  // Incrementer incrementer_1: pin names not known; wires that end beside it: \总周期数 , incrementer_1_p2, PC
  RAM #(.addrWidth(10), .dataWidth(32), .bus("separate"), .Select("high")) ram_1 (
    .addr(mips_alu_1_result[11:2]), .din(MDin),
    .data({ram_1_data_4, ram_1_data_3, ram_1_data_2, ram_1_data}), .str(MemWrite), .clk(CLK), .ld(1'b1));  // open: sel, clr
  Multiplexer #(.select(2), .width(8), .disabled("Z"), .enable("false")) multiplexer_14 (
    .in0(ram_1_data), .in1(ram_1_data_2), .in2(ram_1_data_3), .in3(ram_1_data_4), .out(multiplexer_14_out),
    .sel(Addr1___0));
  assign bit_extender_3_out = {{24{multiplexer_14_out[7]}}, multiplexer_14_out};  // Bit_Extender bit_extender_3
  Multiplexer #(.select(1), .width(32), .disabled("Z"), .enable("false")) multiplexer_15 (
    .in0({mips_alu_1_result, Addr1___0}), .in1(multiplexer_16_out), .out(multiplexer_15_out), .sel(MemToReg));
  Multiplexer #(.select(1), .width(32), .disabled("Z"), .enable("false")) multiplexer_16 (
    .in0({ram_1_data_4, ram_1_data_3, ram_1_data_2, ram_1_data}), .in1(bit_extender_3_out),
    .out(multiplexer_16_out), .sel(LB));
  \单级中断总电路  \u_单级中断总电路_1  (
    .IR1(IR1_t), .CLK(CLK), .IR2(IR2_t), .PC(PC), .IR3(IR3_t), .W1(W1), .\中断信号 (\中断信号 ), .\断点 (\断点 ),
    .W2(W2), .\中断号 (\中断号 ), .W3(W3), .eret(eret), .next_PC(next_PC));
  Multiplexer #(.select(1), .width(32), .disabled("Z"), .enable("false")) multiplexer_17 (
    .in0(multiplexer_15_out), .in1({JumpAddr, PC_plus_4}), .out(RDin), .sel(JAL));

  // Other names for the same wires on the sheet: OP[5:0] = IR[31:26]; Func[5:0] = IR[5:0]; JumpAddr[27:2] = IR[25:0];
  //   shamt[4:0] = IR[10:6]; PC_plus_4[31:28] = JumpAddr

  // Notes on the sheet:
  //   中断源
  //   中断等待指示
  //   总复位信号应将除ROM以外所有存储组件全部清零
  //   控制停机
  //   数码管输出
  //   数码管输出应该用寄存器锁存，否则显示数据只能一闪而过
  //   JMP
  //   JR
  //   OP
  //   Func
  //   Syscall
  //   Beq
  //   Bne
  //   MemToReg
  //   MemWrite
  //   AluOP
  //   AluSrcB
  //   RegWrite
  //   JAL
  //   RegDst
  //   LB
  //   BLTZ
  //   硬布线控制器
  //   指令存储器
  //   指令字
  //   contents of rom_1 (hex, n*v repeats v):
  //   201d07d0 20100001 109fc0 139fc3 8021 2012000c 24160008 26100001 3210000f 20080008 20090001 139900
  //   2709825 132020 20020022 c 1094022 1500fff9 22100001 2018000f 2188024 108700 20080008 20090001 139902
  //   2709825 132021 20020022 c 1094022 1500fff9 108702 2c9b022 12c00001 8000c07 4020 1084027 84400
  //   3508ffff 82021 20020022 c 8100001 afa20000 23bd0004 afa40000 23bd0004 afb00000 23bd0004 afb30000
  //   23bd0004 afb40000 23bd0004 afb50000 23bd0004 afb60000 23bd0004 20160001 20140003 20150001 168020
  //   108100 2149825 132020 20020022 c 1600fffa 295a022 1680fff7 23bdfffc 8fb60000 23bdfffc 8fb50000
  //   23bdfffc 8fb40000 23bdfffc 8fb30000 23bdfffc 8fb00000 23bdfffc 8fa40000 23bdfffc 8fa20000 42000018
  //   afa20000 23bd0004 afa40000 23bd0004 afb00000 23bd0004 afb30000 23bd0004 afb40000 23bd0004 afb50000
  //   23bd0004 afb60000 23bd0004 20160002 20140003 20150001 168020 108100 2149825 132020 20020022 c
  //   1600fffa 295a022 1680fff7 23bdfffc 8fb60000 23bdfffc 8fb50000 23bdfffc 8fb40000 23bdfffc 8fb30000
  //   23bdfffc 8fb00000 23bdfffc 8fa40000 23bdfffc 8fa20000 42000018 afa20000 23bd0004 afa40000 23bd0004
  //   afb00000 23bd0004 afb30000 23bd0004 afb40000 23bd0004 afb50000 23bd0004 afb60000 23bd0004 20160003
  //   20140003 20150001 168020 108100 2149825 132020 20020022 c 1600fffa 295a022 1680fff7 23bdfffc
  //   8fb60000 23bdfffc 8fb50000 23bdfffc 8fb40000 23bdfffc 8fb30000 23bdfffc 8fb00000 23bdfffc 8fa40000
  //   23bdfffc 8fa20000 42000018
  //   数据通路
  //   OP
  //   Func
  //   rs
  //   rt
  //   rd
  //   为方便自动评测，需要输出PC，IR，寄存器堆写如数据RDin
  //   RAM写使能MemWrite、RAM写入数据MDin等信号
  //   数码管显示电路
  //   监视
endmodule

// 中断电路
module \多级嵌套中断总电路  (
  input  IR1,
  input  CLK,
  input  eret,
  input  mfc0,
  input  IR2,
  input  [31:0] PC,
  input  [31:0] next_PC,
  input  mtc0,
  input  IR3,
  output W1,
  output \中断信号 ,
  output W2,
  output [31:0] \断点 ,
  output [1:0] \中断号 ,
  output W3
);

  wire and_1_out, and_2_out, and_3_out, and_4_out, and_5_out, and_6_out, comparator_1_eq, comparator_2_eq,
       comparator_3_eq, d_ff_1_q, d_ff_2_q, d_ff_3_q, d_ff_4_q, d_ff_5_q, d_ff_6_q, d_ff_7_q, d_ff_8_q,
       d_ff_9_q, decoder_1_out1, decoder_1_out2, decoder_1_out3, IE_q, IE_qn, multiplexer_1_out,
       multiplexer_2_out, multiplexer_3_out, multiplexer_4_out, multiplexer_5_out, multiplexer_6_out,
       multiplexer_7_out, multiplexer_8_out, multiplexer_9_out, multiplexer_10_out, multiplexer_11_out,
       multiplexer_12_out, multiplexer_13_out, multiplexer_14_out, not_1_out, or_1_out, or_2_out, or_3_out,
       or_4_out, or_5_out, or_6_out, priority_encoder_1_en_out, \中断1 , \中断2 , \中断3 , \中断屏蔽1 , \中断屏蔽2 ,
       \中断屏蔽3 ;
  wire [1:0] multiplexer_15_out, multiplexer_17_out, multiplexer_19_out, \中断号1 , \中断号2_q , \中断号3_q ;
  wire [31:0] EPC2_q, EPC3_q, multiplexer_16_out, multiplexer_18_out, multiplexer_20_out;

  Decoder #(.select(2), .tristate("false"), .disabled("Z"), .enable("false")) decoder_1 (
    .out1(decoder_1_out1), .out2(decoder_1_out2), .out3(decoder_1_out3), .sel(\中断号1 ));  // open: out0
  and and_1 (and_1_out, decoder_1_out1, eret);
  and and_2 (and_2_out, decoder_1_out2, eret);
  and and_3 (and_3_out, decoder_1_out3, eret);
  \中断按键参考电路  \u_中断按键参考电路_1  (.\与中断屏蔽位与 (\中断1 ), .\同步清零信号 (and_1_out), .\_1号中断等待指示灯 (W1), .CLK(CLK), .\_1号中断 (IR1));
  \中断按键参考电路  \u_中断按键参考电路_2  (.\与中断屏蔽位与 (\中断2 ), .\同步清零信号 (and_2_out), .\_1号中断等待指示灯 (W2), .CLK(CLK), .\_1号中断 (IR2));
  \中断按键参考电路  \u_中断按键参考电路_3  (.\与中断屏蔽位与 (\中断3 ), .\同步清零信号 (and_3_out), .\_1号中断等待指示灯 (W3), .CLK(CLK), .\_1号中断 (IR3));
  Multiplexer #(.select(1), .width(1), .disabled("Z"), .enable("false")) multiplexer_1 (
    .in0(IE_q), .in1(1'b1), .out(multiplexer_1_out), .sel(or_1_out));
  or or_1 (or_1_out, \中断信号 , mtc0);
  Multiplexer #(.select(1), .width(1), .disabled("Z"), .enable("false")) multiplexer_2 (
    .in0(multiplexer_1_out), .in1(1'b0), .out(multiplexer_2_out), .sel(mfc0));
  D_Flip_Flop #(.trigger("rising"), .Pre_Clr_Positions("ABOVE_BELOW"), .NegatePresetClear("false"), .enable("false"), .NewFFLayout("false")) IE (
    .clk(CLK), .D(multiplexer_2_out), .Q(IE_q), .Qn(IE_qn), .reset(eret));  // open: preset
  and and_4 (and_4_out, \中断1 , \中断屏蔽1 );
  and and_5 (and_5_out, \中断2 , \中断屏蔽2 );
  and and_6 (and_6_out, \中断3 , \中断屏蔽3 );
  and and_7 (\中断信号 , IE_qn, not_1_out);
  not not_1 (not_1_out, priority_encoder_1_en_out);
  Priority_Encoder #(.select(2), .disabled("Z")) priority_encoder_1 (
    .in1(and_4_out), .in2(and_5_out), .in3(and_6_out), .out(\中断号 ), .en_out(priority_encoder_1_en_out));  // open: in0, gs, en_in
  Pull_Resistor #(.pull(0)) pull_resistor_1 (.node(\中断号 ));
  Comparator #(.width(2), .mode("unsigned")) comparator_1 (.a(\中断号 ), .b(2'b01), .eq(comparator_1_eq));  // open: gt, lt
  Comparator #(.width(2), .mode("unsigned")) comparator_2 (.a(\中断号 ), .b(2'b10), .eq(comparator_2_eq));  // open: gt, lt
  Comparator #(.width(2), .mode("unsigned")) comparator_3 (.a(\中断号 ), .b(2'b11), .eq(comparator_3_eq));  // open: gt, lt
  or or_2 (or_2_out, comparator_1_eq, comparator_2_eq, comparator_3_eq);
  or or_3 (or_3_out, comparator_2_eq, comparator_3_eq);
  Multiplexer #(.select(1), .width(1), .disabled("Z"), .enable("false")) multiplexer_3 (
    .in0(d_ff_1_q), .in1(1'b1), .out(multiplexer_3_out), .sel(or_2_out));
  Multiplexer #(.select(1), .width(1), .disabled("Z"), .enable("false")) multiplexer_4 (
    .in0(d_ff_2_q), .in1(1'b1), .out(multiplexer_4_out), .sel(or_3_out));
  Multiplexer #(.select(1), .width(1), .disabled("Z"), .enable("false")) multiplexer_5 (
    .in0(d_ff_3_q), .in1(1'b1), .out(multiplexer_5_out), .sel(comparator_3_eq));
  Multiplexer #(.select(1), .width(1), .disabled("Z"), .enable("false")) multiplexer_6 (
    .in0(multiplexer_3_out), .in1(d_ff_4_q), .out(multiplexer_6_out), .sel(eret));
  Multiplexer #(.select(1), .width(1), .disabled("Z"), .enable("false")) multiplexer_7 (
    .in0(multiplexer_4_out), .in1(d_ff_5_q), .out(multiplexer_7_out), .sel(eret));
  Multiplexer #(.select(1), .width(1), .disabled("Z"), .enable("false")) multiplexer_8 (
    .in0(multiplexer_5_out), .in1(d_ff_6_q), .out(multiplexer_8_out), .sel(eret));
  or or_4 (or_4_out, eret, \中断信号 );
  D_Flip_Flop #(.trigger("rising"), .Pre_Clr_Positions("ABOVE_BELOW"), .NegatePresetClear("false"), .enable("true"), .NewFFLayout("false")) d_ff_1 (
    .clk(CLK), .D(multiplexer_6_out), .Q(d_ff_1_q), .Qn(\中断屏蔽1 ), .en(or_4_out));  // open: preset, reset
  D_Flip_Flop #(.trigger("rising"), .Pre_Clr_Positions("ABOVE_BELOW"), .NegatePresetClear("false"), .enable("true"), .NewFFLayout("false")) d_ff_2 (
    .clk(CLK), .D(multiplexer_7_out), .Q(d_ff_2_q), .Qn(\中断屏蔽2 ), .en(or_4_out));  // open: preset, reset
  D_Flip_Flop #(.trigger("rising"), .Pre_Clr_Positions("ABOVE_BELOW"), .NegatePresetClear("false"), .enable("true"), .NewFFLayout("false")) d_ff_3 (
    .clk(CLK), .D(multiplexer_8_out), .Q(d_ff_3_q), .Qn(\中断屏蔽3 ), .en(or_4_out));  // open: preset, reset
  Multiplexer #(.select(1), .width(1), .disabled("Z"), .enable("false")) multiplexer_9 (
    .in0(d_ff_1_q), .in1(d_ff_7_q), .out(multiplexer_9_out), .sel(eret));
  Multiplexer #(.select(1), .width(1), .disabled("Z"), .enable("false")) multiplexer_10 (
    .in0(d_ff_2_q), .in1(d_ff_8_q), .out(multiplexer_10_out), .sel(eret));
  Multiplexer #(.select(1), .width(1), .disabled("Z"), .enable("false")) multiplexer_11 (
    .in0(d_ff_3_q), .in1(d_ff_9_q), .out(multiplexer_11_out), .sel(eret));
  D_Flip_Flop #(.trigger("rising"), .Pre_Clr_Positions("ABOVE_BELOW"), .NegatePresetClear("false"), .enable("true"), .NewFFLayout("false")) d_ff_4 (
    .clk(CLK), .D(multiplexer_9_out), .Q(d_ff_4_q), .en(or_4_out));  // open: Qn, preset, reset
  D_Flip_Flop #(.trigger("rising"), .Pre_Clr_Positions("ABOVE_BELOW"), .NegatePresetClear("false"), .enable("true"), .NewFFLayout("false")) d_ff_5 (
    .clk(CLK), .D(multiplexer_10_out), .Q(d_ff_5_q), .en(or_4_out));  // open: Qn, preset, reset
  D_Flip_Flop #(.trigger("rising"), .Pre_Clr_Positions("ABOVE_BELOW"), .NegatePresetClear("false"), .enable("true"), .NewFFLayout("false")) d_ff_6 (
    .clk(CLK), .D(multiplexer_11_out), .Q(d_ff_6_q), .en(or_4_out));  // open: Qn, preset, reset
  Multiplexer #(.select(1), .width(1), .disabled("Z"), .enable("false")) multiplexer_12 (
    .in0(d_ff_4_q), .in1(1'b0), .out(multiplexer_12_out), .sel(eret));
  Multiplexer #(.select(1), .width(1), .disabled("Z"), .enable("false")) multiplexer_13 (
    .in0(d_ff_5_q), .in1(1'b0), .out(multiplexer_13_out), .sel(eret));
  Multiplexer #(.select(1), .width(1), .disabled("Z"), .enable("false")) multiplexer_14 (
    .in0(d_ff_6_q), .in1(1'b0), .out(multiplexer_14_out), .sel(eret));
  D_Flip_Flop #(.trigger("rising"), .Pre_Clr_Positions("ABOVE_BELOW"), .NegatePresetClear("false"), .enable("true"), .NewFFLayout("false")) d_ff_7 (
    .clk(CLK), .D(multiplexer_12_out), .Q(d_ff_7_q), .en(or_4_out));  // open: Qn, preset, reset
  D_Flip_Flop #(.trigger("rising"), .Pre_Clr_Positions("ABOVE_BELOW"), .NegatePresetClear("false"), .enable("true"), .NewFFLayout("false")) d_ff_8 (
    .clk(CLK), .D(multiplexer_13_out), .Q(d_ff_8_q), .en(or_4_out));  // open: Qn, preset, reset
  D_Flip_Flop #(.trigger("rising"), .Pre_Clr_Positions("ABOVE_BELOW"), .NegatePresetClear("false"), .enable("true"), .NewFFLayout("false")) d_ff_9 (
    .clk(CLK), .D(multiplexer_14_out), .Q(d_ff_9_q), .en(or_4_out));  // open: Qn, preset, reset
  or or_5 (or_5_out, \中断信号 , eret);
  or or_6 (or_6_out, \中断信号 , eret);
  Multiplexer #(.select(1), .width(2), .disabled("Z"), .enable("false")) multiplexer_15 (
    .in0(\中断号 ), .in1(\中断号2_q ), .out(multiplexer_15_out), .sel(eret));
  Register #(.width(2), .trigger("rising"), .Select("low")) \u_中断号1  (
    .D(multiplexer_15_out), .en(or_5_out), .Q(\中断号1 ), .clk(CLK));  // open: clr
  Multiplexer #(.select(1), .width(32), .disabled("Z"), .enable("false")) multiplexer_16 (
    .in0(next_PC), .in1(EPC2_q), .out(multiplexer_16_out), .sel(eret));
  Register #(.width(32), .trigger("rising"), .Select("low")) EPC1 (
    .D(multiplexer_16_out), .en(or_6_out), .Q(\断点 ), .clk(CLK));  // open: clr
  Multiplexer #(.select(1), .width(2), .disabled("Z"), .enable("false")) multiplexer_17 (
    .in0(\中断号1 ), .in1(\中断号3_q ), .out(multiplexer_17_out), .sel(eret));
  Register #(.width(2), .trigger("rising"), .Select("low")) \u_中断号2  (
    .D(multiplexer_17_out), .en(or_5_out), .Q(\中断号2_q ), .clk(CLK));  // open: clr
  Multiplexer #(.select(1), .width(32), .disabled("Z"), .enable("false")) multiplexer_18 (
    .in0(\断点 ), .in1(EPC3_q), .out(multiplexer_18_out), .sel(eret));
  Register #(.width(32), .trigger("rising"), .Select("low")) EPC2 (
    .D(multiplexer_18_out), .en(or_6_out), .Q(EPC2_q), .clk(CLK));  // open: clr
  Multiplexer #(.select(1), .width(2), .disabled("Z"), .enable("false")) multiplexer_19 (
    .in0(\中断号2_q ), .in1(2'b00), .out(multiplexer_19_out), .sel(eret));
  Register #(.width(2), .trigger("rising"), .Select("low")) \u_中断号3  (
    .D(multiplexer_19_out), .en(or_5_out), .Q(\中断号3_q ), .clk(CLK));  // open: clr
  Register #(.width(32), .trigger("rising"), .Select("low")) EPC3 (
    .D(multiplexer_20_out), .en(or_6_out), .Q(EPC3_q), .clk(CLK));  // open: clr
  Multiplexer #(.select(1), .width(32), .disabled("Z"), .enable("false")) multiplexer_20 (
    .in0(EPC2_q), .in1({32{1'b0}}), .out(multiplexer_20_out), .sel(eret));

  // Notes on the sheet:
  //   中断请求生成电路
  //   优先级仲裁
  //   屏蔽字
  //   硬件堆栈
  //   中断号
  //   EPC
endmodule
module \单周期MIPS_多级中断  (
  input  IR1,
  input  IR2,
  input  IR3,
  output RegWrite,
  output MemWrite,
  output [31:0] PC,
  output [31:0] IR,
  output [31:0] RDin,
  output [31:0] MDin,
  output [31:0] LedData
);

  wire AluSrcB, and_1_out, and_2_out, and_3_out, and_4_out, and_5_out, and_6_out, Beq, BLTZ, Bne, CLK,
       comparator_1_eq, comparator_2_eq, comparator_3_eq, comparator_4_eq, comparator_5_eq, comparator_6_eq,
       comparator_7_eq, Equal, eret, Go, halt, IR1_t, IR2_t, IR3_t, IRA, IRB, IRC, JAL, JMP, JR, LB, Less,
       MemToReg, mfc0, mips_probe_1_p1, mtc0, not_1_out, not_2_out, not_3_out, not_4_out, not_5_out,
       or_1_out, or_2_out, or_3_out, RegDst, SignedExt, Syscall, W1, W2, W3, \中断信号 ;
  wire [1:0] Addr1___0, \中断号 ;
  wire [3:0] AluOP;
  wire [4:0] multiplexer_7_out, multiplexer_8_out, multiplexer_9_out, multiplexer_10_out;
  wire [7:0] multiplexer_14_out, ram_1_data, ram_1_data_2, ram_1_data_3, ram_1_data_4;
  wire [15:0] incrementer_1_p2, \总周期数 ;
  wire [27:0] PC_plus_4;
  wire [31:0] bit_extender_1_out, bit_extender_2_out, bit_extender_3_out, multiplexer_1_out,
       multiplexer_2_out, multiplexer_4_out, multiplexer_5_out, multiplexer_6_out, multiplexer_11_out,
       multiplexer_12_out, multiplexer_13_out, multiplexer_15_out, multiplexer_16_out, next_PC, PCBranch, R1,
       shifter_1_out, \断点 ;
  wire [31:2] mips_alu_1_result;
  wire [31:28] JumpAddr;

  Clock #(.highDuration(1), .lowDuration(1)) clock_1 (.out(CLK));
  Button _1 ();  // open: out
  Button _2 ();  // open: out
  Button _3 ();  // open: out
  Button \u_继续运行  (.out(Go));
  LED #(.active("true")) led_1 (.in(W1));
  LED #(.active("true")) led_2 (.in(W2));
  LED #(.active("true")) led_3 (.in(W3));
  Hex_Digit_Display hex_digit_display_1 (.value(LedData[31:28]));  // open: dp
  Multiplexer #(.select(1), .width(32), .disabled("Z"), .enable("false")) multiplexer_1 (
    .in0({JumpAddr, PC_plus_4}), .in1({JumpAddr, IR[25:0], 2'b00}), .out(multiplexer_1_out), .sel(JMP));
  Hex_Digit_Display hex_digit_display_2 (.value(LedData[27:24]));  // open: dp
  Hex_Digit_Display hex_digit_display_3 (.value(LedData[23:20]));  // open: dp
  Comparator #(.width(32), .mode("twosComplement")) comparator_1 (
    .a(R1), .b(32'h22), .eq(comparator_1_eq));  // open: gt, lt
  nand nand_1 (halt, ~comparator_1_eq, Syscall);  // NAND_Gate
  Multiplexer #(.select(1), .width(32), .disabled("Z"), .enable("false")) multiplexer_2 (
    .in0(multiplexer_1_out), .in1(R1), .out(multiplexer_2_out), .sel(JR));
  and and_1 (and_1_out, Beq, Equal);
  and and_2 (and_2_out, BLTZ, Less);
  or or_1 (or_1_out, and_1_out, and_2_out, and_3_out);
  and and_3 (and_3_out, Bne, ~Equal);  // AND_Gate
  Hex_Digit_Display hex_digit_display_4 (.value(LedData[15:12]));  // open: dp
  Hex_Digit_Display hex_digit_display_5 (.value(LedData[19:16]));  // open: dp
  // Probe on halt
  Multiplexer #(.select(1), .width(32), .disabled("Z"), .enable("false")) multiplexer_3 (
    .in0(multiplexer_2_out), .in1(PCBranch), .out(next_PC), .sel(or_1_out));
  Comparator #(.width(16), .mode("twosComplement")) comparator_2 (
    .a(16'h258), .b(\总周期数 ), .eq(comparator_2_eq));  // open: gt, lt
  Comparator #(.width(16), .mode("twosComplement")) comparator_3 (
    .a(\总周期数 ), .b(16'h1), .eq(comparator_3_eq));  // open: gt, lt
  Comparator #(.width(16), .mode("twosComplement")) comparator_4 (
    .a(\总周期数 ), .b(16'h4), .eq(comparator_4_eq));  // open: gt, lt
  Comparator #(.width(16), .mode("twosComplement")) comparator_5 (
    .a(\总周期数 ), .b(16'h7), .eq(comparator_5_eq));  // open: gt, lt
  or or_2 (or_2_out, comparator_5_eq, comparator_6_eq);
  Comparator #(.width(16), .mode("twosComplement")) comparator_6 (
    .a(\总周期数 ), .b(16'h241), .eq(comparator_6_eq));  // open: gt, lt
  Hex_Digit_Display hex_digit_display_6 (.value(LedData[11:8]));  // open: dp
  Hex_Digit_Display hex_digit_display_7 (.value(LedData[7:4]));  // open: dp
  // Probe on \总周期数 
  Multiplexer #(.select(2), .width(32), .disabled("Z"), .enable("false")) multiplexer_4 (
    .in1(32'h30ac), .in2(32'h3158), .in3(32'h3204), .out(multiplexer_4_out), .sel(\中断号 ));  // open: in0
  or or_3 (or_3_out, comparator_2_eq, comparator_3_eq);
  Pull_Resistor #(.pull(0)) pull_resistor_1 (.node(IRA));
  assign IRA = or_3_out ? ~CLK : 1'bz;  // Controlled_Inverter controlled_inverter_1
  Pull_Resistor #(.pull(0)) pull_resistor_2 (.node(IRB));
  assign IRB = comparator_4_eq ? ~CLK : 1'bz;  // Controlled_Inverter controlled_inverter_2
  Pull_Resistor #(.pull(0)) pull_resistor_3 (.node(IRC));
  assign IRC = or_2_out ? ~CLK : 1'bz;  // Controlled_Inverter controlled_inverter_3
  Hex_Digit_Display hex_digit_display_8 (.value(LedData[3:0]));  // open: dp
  Multiplexer #(.select(1), .width(32), .disabled("Z"), .enable("false")) multiplexer_5 (
    .in0(next_PC), .in1(multiplexer_4_out), .out(multiplexer_5_out), .sel(\中断信号 ));
  Multiplexer #(.select(1), .width(32), .disabled("Z"), .enable("false")) multiplexer_6 (
    .in0(multiplexer_5_out), .in1(\断点 ), .out(multiplexer_6_out), .sel(eret));
  or or_4 (IR1_t, IR1, IRA);
  Register #(.width(32), .trigger("rising"), .Select("low")) u_PC (
    .D(multiplexer_6_out), .en(halt), .Q(PC), .clk(CLK));  // open: clr
  or or_5 (IR2_t, IR2, IRB);
  \单周期硬布线控制器  \u_单周期硬布线控制器_1  (
    .Func(IR[5:0]), .OP(IR[31:26]), .ALU_OP(AluOP), .MemToReg(MemToReg), .MemWrite(MemWrite),
    .ALU_SRC(AluSrcB), .RegWrite(RegWrite), .SysCALL(Syscall), .SignedExt(SignedExt), .RegDst(RegDst),
    .JR(JR), .JMP(JMP), .Beq(Beq), .JAL(JAL), .Bne(Bne), .LB(LB), .BLTZ(BLTZ), .eret(eret));
  Adder #(.width(32)) adder_1 (.a(PC), .b(32'h4), .out({JumpAddr, PC_plus_4}));  // open: cin, cout
  // Mips_Probe mips_probe_1: pin names not known; wires that end beside it: mips_probe_1_p1, mips_probe_1_p1, IR
  ROM #(.addrWidth(10), .dataWidth(32), .Select("high")) rom_1 (.addr(PC[11:2]), .data(IR));
  or or_6 (IR3_t, IR3, IRC);
  Multiplexer #(.select(1), .width(5), .disabled("Z"), .enable("false")) multiplexer_7 (
    .in0(IR[20:16]), .in1(IR[15:11]), .out(multiplexer_7_out), .sel(RegDst));
  Multiplexer #(.select(1), .width(5), .disabled("Z"), .enable("false")) multiplexer_8 (
    .in0(multiplexer_7_out), .in1({5{1'b1}}), .out(multiplexer_8_out), .sel(JAL));
  Comparator #(.width(32), .mode("twosComplement")) comparator_7 (
    .a(R1), .b(32'h22), .eq(comparator_7_eq));  // open: gt, lt
  Multiplexer #(.select(1), .width(5), .disabled("Z"), .enable("false")) multiplexer_9 (
    .in0(IR[25:21]), .in1(5'b00010), .out(multiplexer_9_out), .sel(Syscall));
  Multiplexer #(.select(1), .width(5), .disabled("Z"), .enable("false")) multiplexer_10 (
    .in0(IR[20:16]), .in1(5'b00100), .out(multiplexer_10_out), .sel(Syscall));
  assign bit_extender_1_out = {{16{1'b0}}, IR[15:0]};  // Bit_Extender bit_extender_1
  assign bit_extender_2_out = {{16{IR[15]}}, IR[15:0]};  // Bit_Extender bit_extender_2
  Multiplexer #(.select(1), .width(32), .disabled("Z"), .enable("false")) multiplexer_11 (
    .in0(LedData), .in1(MDin), .out(multiplexer_11_out), .sel(and_4_out));
  and and_4 (and_4_out, comparator_7_eq, Syscall);
  Multiplexer #(.select(1), .width(32), .disabled("Z"), .enable("false")) multiplexer_12 (
    .in0(bit_extender_1_out), .in1(bit_extender_2_out), .out(multiplexer_12_out), .sel(SignedExt));
  // Probe on multiplexer_12_out
  Register #(.width(32), .trigger("rising"), .Select("low")) register_1 (
    .D(multiplexer_11_out), .Q(LedData), .clk(CLK));  // open: en, clr
  MIPS_Regifile mips_regifile_1 (
    .Din(RDin), .Clk(CLK), .R1(R1), .R2(MDin), .WE(RegWrite), .W_num(multiplexer_8_out),
    .R1_num(multiplexer_9_out), .R2_num(multiplexer_10_out));
  Multiplexer #(.select(1), .width(32), .disabled("Z"), .enable("false")) multiplexer_13 (
    .in0(MDin), .in1(multiplexer_12_out), .out(multiplexer_13_out), .sel(AluSrcB));
  Shifter #(.width(32), .shift("ll")) shifter_1 (.in(multiplexer_12_out), .\dist (5'b00010), .out(shifter_1_out));
  MIPS_ALU mips_alu_1 (
    .X(R1), .Y(multiplexer_13_out), .AluOP(AluOP), .Equal(Equal), .Result({mips_alu_1_result, Addr1___0}),
    .shamt(IR[10:6]), .Less(Less));  // open: Result_2
  Adder #(.width(32)) adder_2 (.a(shifter_1_out), .b({JumpAddr, PC_plus_4}), .out(PCBranch));  // open: cin, cout
  Register #(.width(16), .trigger("rising"), .Select("low")) register_2 (
    .D(incrementer_1_p2), .en(halt), .Q(\总周期数 ), .clk(CLK));  // open: clr
  // Incrementer incrementer_1: pin names not known; wires that end beside it: \总周期数 , incrementer_1_p2
  RAM #(.addrWidth(10), .dataWidth(32), .bus("separate"), .Select("high")) ram_1 (
    .addr(mips_alu_1_result[11:2]), .din(MDin),
    .data({ram_1_data_4, ram_1_data_3, ram_1_data_2, ram_1_data}), .str(MemWrite), .clk(CLK), .ld(1'b1));  // open: sel, clr
  Multiplexer #(.select(2), .width(8), .disabled("Z"), .enable("false")) multiplexer_14 (
    .in0(ram_1_data), .in1(ram_1_data_2), .in2(ram_1_data_3), .in3(ram_1_data_4), .out(multiplexer_14_out),
    .sel(Addr1___0));
  assign bit_extender_3_out = {{24{multiplexer_14_out[7]}}, multiplexer_14_out};  // Bit_Extender bit_extender_3
  Multiplexer #(.select(1), .width(32), .disabled("Z"), .enable("false")) multiplexer_15 (
    .in0({mips_alu_1_result, Addr1___0}), .in1(multiplexer_16_out), .out(multiplexer_15_out), .sel(MemToReg));
  Multiplexer #(.select(1), .width(32), .disabled("Z"), .enable("false")) multiplexer_16 (
    .in0({ram_1_data_4, ram_1_data_3, ram_1_data_2, ram_1_data}), .in1(bit_extender_3_out),
    .out(multiplexer_16_out), .sel(LB));
  \多级嵌套中断总电路  \u_多级嵌套中断总电路_1  (
    .IR1(IR1_t), .CLK(CLK), .eret(eret), .mfc0(mfc0), .IR2(IR2_t), .PC(PC), .next_PC(next_PC), .mtc0(mtc0),
    .IR3(IR3_t), .W1(W1), .\中断信号 (\中断信号 ), .W2(W2), .\断点 (\断点 ), .\中断号 (\中断号 ), .W3(W3));
  Multiplexer #(.select(1), .width(32), .disabled("Z"), .enable("false")) multiplexer_17 (
    .in0(multiplexer_15_out), .in1({JumpAddr, PC_plus_4}), .out(RDin), .sel(JAL));
  not not_1 (not_1_out, IR[26]);
  not not_2 (not_2_out, IR[27]);
  not not_3 (not_3_out, IR[28]);
  not not_4 (not_4_out, IR[29]);
  not not_5 (not_5_out, IR[31]);
  and and_5 (and_5_out, not_1_out, not_2_out, not_3_out, not_4_out, IR[30], not_5_out);
  and and_6 (and_6_out, and_5_out, ~IR[25]);  // AND_Gate
  and and_7 (mtc0, and_6_out, IR[23]);
  and and_8 (mfc0, and_6_out, ~IR[23]);  // AND_Gate

  // Other names for the same wires on the sheet: OP[5:0] = IR[31:26]; Func[5:0] = IR[5:0]; JumpAddr[27:2] = IR[25:0];
  //   shamt[4:0] = IR[10:6]; rs[4:0] = IR[25:21]; PC_plus_4[31:28] = JumpAddr

  // Notes on the sheet:
  //   中断源
  //   中断等待指示
  //   总复位信号应将除ROM以外所有存储组件全部清零
  //   控制停机
  //   数码管输出
  //   数码管输出应该用寄存器锁存，否则显示数据只能一闪而过
  //   JMP
  //   JR
  //   OP
  //   Func
  //   Syscall
  //   Beq
  //   Bne
  //   MemToReg
  //   MemWrite
  //   AluOP
  //   AluSrcB
  //   RegWrite
  //   JAL
  //   RegDst
  //   LB
  //   BLTZ
  //   硬布线控制器
  //   指令存储器
  //   指令字
  //   contents of rom_1 (hex, n*v repeats v):
  //   201d07d0 20100001 109fc0 139fc3 8021 2012000c 24160008 26100001 3210000f 20080008 20090001 139900
  //   2709825 132020 20020022 c 1094022 1500fff9 22100001 2018000f 2188024 108700 20080008 20090001 139902
  //   2709825 132021 20020022 c 1094022 1500fff9 108702 2c9b022 12c00001 8100007 4020 1084027 84400
  //   3508ffff 82021 20020022 c 8100001 afa20000 23bd0004 afa40000 23bd0004 afb00000 23bd0004 afb30000
  //   23bd0004 afb40000 23bd0004 afb50000 23bd0004 afb60000 23bd0004 40000000 20160001 20140003 20150001
  //   168020 108100 2149825 132020 20020022 c 1600fffa 295a022 1680fff7 40800000 23bdfffc 8fb60000
  //   23bdfffc 8fb50000 23bdfffc 8fb40000 23bdfffc 8fb30000 23bdfffc 8fb00000 23bdfffc 8fa40000 23bdfffc
  //   8fa20000 42000018 afa20000 23bd0004 afa40000 23bd0004 afb00000 23bd0004 afb30000 23bd0004 afb40000
  //   23bd0004 afb50000 23bd0004 afb60000 23bd0004 40000000 20160002 20140003 20150001 168020 108100
  //   2149825 132020 20020022 c 1600fffa 295a022 1680fff7 40800000 23bdfffc 8fb60000 23bdfffc 8fb50000
  //   23bdfffc 8fb40000 23bdfffc 8fb30000 23bdfffc 8fb00000 23bdfffc 8fa40000 23bdfffc 8fa20000 42000018
  //   afa20000 23bd0004 afa40000 23bd0004 afb00000 23bd0004 afb30000 23bd0004 afb40000 23bd0004 afb50000
  //   23bd0004 afb60000 23bd0004 40000000 20160003 20140003 20150001 168020 108100 2149825 132020 20020022
  //   c 1600fffa 295a022 1680fff7 40800000 23bdfffc 8fb60000 23bdfffc 8fb50000 23bdfffc 8fb40000 23bdfffc
  //   8fb30000 23bdfffc 8fb00000 23bdfffc 8fa40000 23bdfffc 8fa20000 42000018
  //   OP
  //   Func
  //   rs
  //   rt
  //   rd
  //   数据通路
  //   为方便自动评测，需要输出PC，IR，寄存器堆写如数据RDin
  //   RAM写使能MemWrite、RAM写入数据MDin等信号
  //   数码管显示电路
  //   监视
  //   中断指令控制器
endmodule
